// Logisim project FirstLogisimExperiment.circ as structural Verilog: 3 circuits, main circuit LEDCounterCircuit
module LEDCounterCircuit (
  input  In1,
  input  In2,
  input  In3,
  input  In4,
  input  In5,
  output Out1,
  output Out2,
  output Out3,
  output Out4,
  output Out5
);

  or or_1 (Out1, In1, In2, In3, In4, In5);
  or or_2 (Out2, In2, In3, In4, In5);
  or or_3 (Out3, In3, In4, In5);
  or or_4 (Out4, In4, In5);

  assign Out5 = In5;
endmodule

module LEDCounterTest (
);

  wire button_1_out, button_2_out, button_3_out, button_4_out, button_5_out, ledcountercircuit_1_out1,
       ledcountercircuit_1_out2, ledcountercircuit_1_out3, ledcountercircuit_1_out4, ledcountercircuit_1_out5;
  wire [2:0] fiveinputencoder_1_out1;

  Button button_1 (.out(button_1_out));
  Button button_2 (.out(button_2_out));
  Button button_3 (.out(button_3_out));
  Button button_4 (.out(button_4_out));
  Button button_5 (.out(button_5_out));
  LEDCounterCircuit ledcountercircuit_1 (
    .Out1(ledcountercircuit_1_out1), .Out2(ledcountercircuit_1_out2), .Out3(ledcountercircuit_1_out3),
    .Out4(ledcountercircuit_1_out4), .Out5(ledcountercircuit_1_out5), .In1(button_1_out), .In2(button_2_out),
    .In3(button_3_out), .In4(button_4_out), .In5(button_5_out));
  LED led_1 (.in(ledcountercircuit_1_out1));
  LED led_2 (.in(ledcountercircuit_1_out2));
  LED led_3 (.in(ledcountercircuit_1_out3));
  LED led_4 (.in(ledcountercircuit_1_out4));
  LED led_5 (.in(ledcountercircuit_1_out5));
  FiveInputEncoder fiveinputencoder_1 (
    .Out3(fiveinputencoder_1_out1[2]), .Out1(fiveinputencoder_1_out1[0]), .Out2(fiveinputencoder_1_out1[1]),
    .In3(button_3_out), .In4(button_4_out), .In5(button_5_out), .In1(button_1_out), .In2(button_2_out));
  // Probe on fiveinputencoder_1_out1
  Hex_Digit_Display hex_digit_display_1 (.value({1'b0, fiveinputencoder_1_out1}));  // open: dp
endmodule

module FiveInputEncoder (
  input  In1,
  input  In2,
  input  In3,
  input  In4,
  input  In5,
  output Out1,
  output Out2,
  output Out3
);

  wire and_1_out, and_2_out, and_3_out, and_4_out, not_1_out, not_2_out, not_3_out;

  not not_1 (not_1_out, In2);
  not not_2 (not_2_out, In4);
  not not_3 (not_3_out, In5);
  and and_1 (and_1_out, In3, not_2_out);
  and and_2 (and_2_out, In1, not_1_out, not_2_out);
  and and_3 (and_3_out, In3, not_2_out, not_3_out);
  and and_4 (and_4_out, In2, not_2_out, not_3_out);
  or or_1 (Out3, In5, In4);
  or or_2 (Out1, In5, and_1_out, and_2_out);
  or or_3 (Out2, and_3_out, and_4_out);
endmodule
