// Logisim project LogisimFromZero.circ as structural Verilog: 2 circuits, main circuit FromZero
module FromZero (
  input  [3:0] x,
  input  [3:0] y,
  input  s,
  output [3:0] z
);

  wire [3:0] and_1_out, or_1_out;

  // Probe on x
  assign and_1_out = x & y;  // AND_Gate and_1, 4 bits wide
  assign or_1_out = x | y;  // OR_Gate or_1, 4 bits wide
  Multiplexer #(.enable("false"), .width(4)) multiplexer_1 (.in0(and_1_out), .in1(or_1_out), .out(z), .sel(s));
endmodule

module TestingCircuit (
);

  wire undriven_3;
  wire [3:0] fromzero_1_z, undriven, undriven_2;

  FromZero fromzero_1 (.z(fromzero_1_z), .x(undriven), .y(undriven_2), .s(undriven_3));
endmodule
