// Logisim project Danger.circ as structural Verilog: 1 circuit, main circuit Danger
module Danger (
  input  in_1,
  output out_2
);

  wire buffer_1_out, not_1_out;

  buf buffer_1 (buffer_1_out, in_1);
  not not_1 (not_1_out, in_1);
  and and_1 (out_2, buffer_1_out, not_1_out);
endmodule
