// Logisim project FirstLogisimExperiment.circ as structural Verilog: 5 circuits, main circuit LEDCounterCircuit
module LEDCounterCircuit (
  input  In1,
  input  In2,
  input  In3,
  input  In4,
  input  In5,
  output Out1,
  output Out2,
  output Out3,
  output Out4,
  output Out5
);

  or or_1 (Out1, In1, In2, In3, In4, In5);
  or or_2 (Out2, In2, In3, In4, In5);
  or or_3 (Out3, In3, In4, In5);
  or or_4 (Out4, In4, In5);

  assign Out5 = In5;
endmodule

module LEDCounterTest (
);

  wire button_1_out, button_2_out, button_3_out, button_4_out, button_5_out, digitaltubedriver_1_seq1,
       digitaltubedriver_1_seq2, digitaltubedriver_1_seq3, digitaltubedriver_1_seq4,
       digitaltubedriver_1_seq5, digitaltubedriver_1_seq6, digitaltubedriver_1_seq7,
       ledcountercircuit_1_out1, ledcountercircuit_1_out2, ledcountercircuit_1_out3,
       ledcountercircuit_1_out4, ledcountercircuit_1_out5;
  wire [2:0] fiveinputencoder_1_out1;

  Button button_1 (.out(button_1_out));
  Button button_2 (.out(button_2_out));
  Button button_3 (.out(button_3_out));
  Button button_4 (.out(button_4_out));
  Button button_5 (.out(button_5_out));
  LEDCounterCircuit ledcountercircuit_1 (
    .Out1(ledcountercircuit_1_out1), .Out2(ledcountercircuit_1_out2), .Out3(ledcountercircuit_1_out3),
    .Out4(ledcountercircuit_1_out4), .Out5(ledcountercircuit_1_out5), .In1(button_1_out), .In2(button_2_out),
    .In3(button_3_out), .In4(button_4_out), .In5(button_5_out));
  LED led_1 (.in(ledcountercircuit_1_out1));
  LED led_2 (.in(ledcountercircuit_1_out2));
  LED led_3 (.in(ledcountercircuit_1_out3));
  LED led_4 (.in(ledcountercircuit_1_out4));
  LED led_5 (.in(ledcountercircuit_1_out5));
  FiveInputEncoder fiveinputencoder_1 (
    .Out3(fiveinputencoder_1_out1[2]), .Out1(fiveinputencoder_1_out1[0]), .Out2(fiveinputencoder_1_out1[1]),
    .In3(button_3_out), .In4(button_4_out), .In5(button_5_out), .In1(button_1_out), .In2(button_2_out));
  // Probe on fiveinputencoder_1_out1
  DigitalTubeDriver digitaltubedriver_1 (
    .Seq3(digitaltubedriver_1_seq3), .Seq4(digitaltubedriver_1_seq4), .Seq5(digitaltubedriver_1_seq5),
    .Seq6(digitaltubedriver_1_seq6), .Seq7(digitaltubedriver_1_seq7), .Seq1(digitaltubedriver_1_seq1),
    .Seq2(digitaltubedriver_1_seq2), .X1(fiveinputencoder_1_out1[1]), .X0(fiveinputencoder_1_out1[0]),
    .X3(1'b0), .X2(fiveinputencoder_1_out1[2]));
  Hex_Digit_Display hex_digit_display_1 (.value({1'b0, fiveinputencoder_1_out1}));  // open: dp
  _7_Segment_Display u_7_segment_display_1 (
    .g(digitaltubedriver_1_seq1), .f(digitaltubedriver_1_seq2), .a(digitaltubedriver_1_seq3),
    .b(digitaltubedriver_1_seq4), .e(digitaltubedriver_1_seq5), .d(digitaltubedriver_1_seq6),
    .c(digitaltubedriver_1_seq7), .dp(1'b1));
endmodule

module FiveInputEncoder (
  input  In1,
  input  In2,
  input  In3,
  input  In4,
  input  In5,
  output Out1,
  output Out2,
  output Out3
);

  wire and_1_out, and_2_out, and_3_out, and_4_out, not_1_out, not_2_out, not_3_out;

  not not_1 (not_1_out, In2);
  not not_2 (not_2_out, In4);
  not not_3 (not_3_out, In5);
  and and_1 (and_1_out, In3, not_2_out);
  and and_2 (and_2_out, In1, not_1_out, not_2_out);
  and and_3 (and_3_out, In3, not_2_out, not_3_out);
  and and_4 (and_4_out, In2, not_2_out, not_3_out);
  or or_1 (Out3, In5, In4);
  or or_2 (Out1, In5, and_1_out, and_2_out);
  or or_3 (Out2, and_3_out, and_4_out);
endmodule

module DigitalTubeDriver (
  input  X3,
  input  X2,
  input  X1,
  input  X0,
  output Seq1,
  output Seq2,
  output Seq3,
  output Seq4,
  output Seq5,
  output Seq6,
  output Seq7
);

  wire and_1_out, and_2_out, and_3_out, and_4_out, and_5_out, and_6_out, and_7_out, and_8_out, and_9_out,
       and_10_out, and_11_out, and_12_out, and_13_out, and_14_out, and_15_out, and_16_out, and_17_out,
       and_18_out, and_19_out, and_20_out, and_21_out, and_22_out, and_23_out, and_24_out, and_25_out,
       and_26_out, and_27_out, and_28_out, and_29_out, and_30_out, and_31_out, and_32_out, and_33_out,
       and_34_out, and_35_out, not_1_out, not_2_out, not_3_out, not_4_out;

  not not_1 (not_1_out, X3);
  not not_2 (not_2_out, X2);
  not not_3 (not_3_out, X1);
  not not_4 (not_4_out, X0);
  and and_1 (and_1_out, not_2_out, X1);
  and and_2 (and_2_out, X1, not_4_out);
  and and_3 (and_3_out, not_1_out, X2, not_3_out);
  and and_4 (and_4_out, X3, not_2_out);
  and and_5 (and_5_out, X3, X0);
  and and_6 (and_6_out, not_3_out, not_4_out);
  and and_7 (and_7_out, not_1_out, X2, not_3_out);
  and and_8 (and_8_out, X2, not_4_out);
  and and_9 (and_9_out, X3, not_2_out);
  and and_10 (and_10_out, X3, X1);
  and and_11 (and_11_out, not_2_out, not_4_out);
  and and_12 (and_12_out, not_1_out, X1);
  and and_13 (and_13_out, not_1_out, X2, X0);
  and and_14 (and_14_out, X2, X1);
  and and_15 (and_15_out, X3, not_2_out, not_3_out);
  and and_16 (and_16_out, X3, not_4_out);
  and and_17 (and_17_out, not_1_out, not_2_out);
  and and_18 (and_18_out, not_1_out, not_3_out, not_4_out);
  and and_19 (and_19_out, not_2_out, not_4_out);
  and and_20 (and_20_out, not_1_out, X1, X0);
  and and_21 (and_21_out, X3, not_3_out, X0);
  and and_22 (and_22_out, not_2_out, not_4_out);
  and and_23 (and_23_out, X1, not_4_out);
  and and_24 (and_24_out, X3, X1);
  and and_25 (and_25_out, X3, X2);
  and and_26 (and_26_out, not_1_out, not_2_out, not_4_out);
  and and_27 (and_27_out, not_2_out, X1, X0);
  and and_28 (and_28_out, X2, not_3_out, X0);
  and and_29 (and_29_out, X2, X1, not_4_out);
  and and_30 (and_30_out, X3, not_3_out);
  and and_31 (and_31_out, not_1_out, not_3_out);
  and and_32 (and_32_out, not_1_out, X0);
  and and_33 (and_33_out, not_3_out, X0);
  and and_34 (and_34_out, not_1_out, X2);
  and and_35 (and_35_out, X3, not_2_out);
  or or_1 (Seq1, and_1_out, and_2_out, and_3_out, and_4_out, and_5_out);
  or or_2 (Seq2, and_6_out, and_7_out, and_8_out, and_9_out, and_10_out);
  or or_3 (Seq3, and_11_out, and_12_out, and_13_out, and_14_out, and_15_out, and_16_out);
  or or_4 (Seq4, and_17_out, and_18_out, and_19_out, and_20_out, and_21_out);
  or or_5 (Seq5, and_22_out, and_23_out, and_24_out, and_25_out);
  or or_6 (Seq6, and_26_out, and_27_out, and_28_out, and_29_out, and_30_out);
  or or_7 (Seq7, and_31_out, and_32_out, and_33_out, and_34_out, and_35_out);
endmodule

module DigitalTubeAutoTesting (
);

  wire clock_1_out, digitaltubedriver_1_seq1, digitaltubedriver_1_seq2, digitaltubedriver_1_seq3,
       digitaltubedriver_1_seq4, digitaltubedriver_1_seq5, digitaltubedriver_1_seq6, digitaltubedriver_1_seq7;
  wire [3:0] counter_1_q;

  Counter #(.max('hf), .width(4)) counter_1 (
    .Q(counter_1_q), .clk(clock_1_out));  // open: load, D, count, carry, up, clr
  Clock clock_1 (.out(clock_1_out));
  DigitalTubeDriver digitaltubedriver_1 (
    .Seq3(digitaltubedriver_1_seq3), .Seq4(digitaltubedriver_1_seq4), .Seq5(digitaltubedriver_1_seq5),
    .Seq6(digitaltubedriver_1_seq6), .Seq7(digitaltubedriver_1_seq7), .Seq1(digitaltubedriver_1_seq1),
    .Seq2(digitaltubedriver_1_seq2), .X1(counter_1_q[1]), .X0(counter_1_q[0]), .X3(counter_1_q[3]),
    .X2(counter_1_q[2]));
  _7_Segment_Display u_7_segment_display_1 (
    .g(digitaltubedriver_1_seq1), .f(digitaltubedriver_1_seq2), .a(digitaltubedriver_1_seq3),
    .b(digitaltubedriver_1_seq4), .e(digitaltubedriver_1_seq5), .d(digitaltubedriver_1_seq6),
    .c(digitaltubedriver_1_seq7));  // open: dp
endmodule
