// Logisim project LogisimFromZero.circ as structural Verilog: 2 circuits, main circuit FromZero
module FromZero (
  input  x,
  input  y,
  output z
);

  and and_1 (z, x, y);
endmodule

module TestingCircuit (
);

  wire fromzero_1_p1, fromzero_1_p2, fromzero_1_p3, fromzero_1_p4;

  // FromZero fromzero_1: pin names not known; wires that end beside it: fromzero_1_p1, fromzero_1_p2, fromzero_1_p3, fromzero_1_p4
endmodule
