// Logisim project OscillationCircuit.circ as structural Verilog: 1 circuit, main circuit OscillationCircuit
module OscillationCircuit (
  input  in_1,
  output out_2
);

  nand nand_1 (out_2, in_1, out_2);
endmodule
