// Logisim project CombinatorialLogic.circ as structural Verilog: 19 circuits, main circuit MultiplexerBin
module DigitalTubeDriver (
  input  X3,
  input  X2,
  input  X1,
  input  X0,
  output Seq1,
  output Seq2,
  output Seq3,
  output Seq4,
  output Seq5,
  output Seq6,
  output Seq7
);

  wire and_1_out, and_2_out, and_3_out, and_4_out, and_5_out, and_6_out, and_7_out, and_8_out, and_9_out,
       and_10_out, and_11_out, and_12_out, and_13_out, and_14_out, and_15_out, and_16_out, and_17_out,
       and_18_out, and_19_out, and_20_out, and_21_out, and_22_out, and_23_out, and_24_out, and_25_out,
       and_26_out, and_27_out, and_28_out, and_29_out, and_30_out, and_31_out, and_32_out, and_33_out,
       and_34_out, and_35_out, not_1_out, not_2_out, not_3_out, not_4_out;

  not not_1 (not_1_out, X3);
  not not_2 (not_2_out, X2);
  not not_3 (not_3_out, X1);
  not not_4 (not_4_out, X0);
  and and_1 (and_1_out, not_2_out, X1);
  and and_2 (and_2_out, X1, not_4_out);
  and and_3 (and_3_out, not_1_out, X2, not_3_out);
  and and_4 (and_4_out, X3, not_2_out);
  and and_5 (and_5_out, X3, X0);
  and and_6 (and_6_out, not_3_out, not_4_out);
  and and_7 (and_7_out, not_1_out, X2, not_3_out);
  and and_8 (and_8_out, X2, not_4_out);
  and and_9 (and_9_out, X3, not_2_out);
  and and_10 (and_10_out, X3, X1);
  and and_11 (and_11_out, not_2_out, not_4_out);
  and and_12 (and_12_out, not_1_out, X1);
  and and_13 (and_13_out, not_1_out, X2, X0);
  and and_14 (and_14_out, X2, X1);
  and and_15 (and_15_out, X3, not_2_out, not_3_out);
  and and_16 (and_16_out, X3, not_4_out);
  and and_17 (and_17_out, not_1_out, not_2_out);
  and and_18 (and_18_out, not_1_out, not_3_out, not_4_out);
  and and_19 (and_19_out, not_2_out, not_4_out);
  and and_20 (and_20_out, not_1_out, X1, X0);
  and and_21 (and_21_out, X3, not_3_out, X0);
  and and_22 (and_22_out, not_2_out, not_4_out);
  and and_23 (and_23_out, X1, not_4_out);
  and and_24 (and_24_out, X3, X1);
  and and_25 (and_25_out, X3, X2);
  and and_26 (and_26_out, not_1_out, not_2_out, not_4_out);
  and and_27 (and_27_out, not_2_out, X1, X0);
  and and_28 (and_28_out, X2, not_3_out, X0);
  and and_29 (and_29_out, X2, X1, not_4_out);
  and and_30 (and_30_out, X3, not_3_out);
  and and_31 (and_31_out, not_1_out, not_3_out);
  and and_32 (and_32_out, not_1_out, X0);
  and and_33 (and_33_out, not_3_out, X0);
  and and_34 (and_34_out, not_1_out, X2);
  and and_35 (and_35_out, X3, not_2_out);
  or or_1 (Seq1, and_1_out, and_2_out, and_3_out, and_4_out, and_5_out);
  or or_2 (Seq2, and_6_out, and_7_out, and_8_out, and_9_out, and_10_out);
  or or_3 (Seq3, and_11_out, and_12_out, and_13_out, and_14_out, and_15_out, and_16_out);
  or or_4 (Seq4, and_17_out, and_18_out, and_19_out, and_20_out, and_21_out);
  or or_5 (Seq5, and_22_out, and_23_out, and_24_out, and_25_out);
  or or_6 (Seq6, and_26_out, and_27_out, and_28_out, and_29_out, and_30_out);
  or or_7 (Seq7, and_31_out, and_32_out, and_33_out, and_34_out, and_35_out);
endmodule

// MUX
module MultiplexerBin (
  input  X0,
  input  Sel,
  input  X1,
  output out_4
);

  wire and_1_out, and_2_out;

  and and_1 (and_1_out, ~Sel, X0);  // AND_Gate
  and and_2 (and_2_out, Sel, X1);
  or or_1 (out_4, and_1_out, and_2_out);

  // Other names for the same wires on the sheet: Out = out_4

  // Notes on the sheet:
  //   输入引脚区
  //   电路功能：Out=(Sel==0)?X0:X1;
  //   请勿增删改引脚，请在下方利用上方输入输出引脚的隧道标签信号构建电路，ctrl+d复制选择组件
  //   输出引脚区
endmodule

// MUX
module MultiplexerHex (
  input  [15:0] X,
  input  Sel,
  input  [15:0] Y,
  output [15:0] Out
);

  // Probe on X
  // Probe on Y
  MultiplexerBin M1 (.out_4(Out[0]), .Sel(Sel), .X0(X[0]), .X1(Y[0]));
  MultiplexerBin M2 (.out_4(Out[1]), .Sel(Sel), .X0(X[1]), .X1(Y[1]));
  // Probe on Out
  MultiplexerBin M3 (.out_4(Out[2]), .Sel(Sel), .X0(X[2]), .X1(Y[2]));
  MultiplexerBin M4 (.out_4(Out[3]), .Sel(Sel), .X0(X[3]), .X1(Y[3]));
  MultiplexerBin M5 (.out_4(Out[4]), .Sel(Sel), .X0(X[4]), .X1(Y[4]));
  MultiplexerBin M6 (.out_4(Out[5]), .Sel(Sel), .X0(X[5]), .X1(Y[5]));
  MultiplexerBin M7 (.out_4(Out[6]), .Sel(Sel), .X0(X[6]), .X1(Y[6]));
  MultiplexerBin M8 (.out_4(Out[7]), .Sel(Sel), .X0(X[7]), .X1(Y[7]));
  MultiplexerBin M9 (.out_4(Out[8]), .Sel(Sel), .X0(X[8]), .X1(Y[8]));
  MultiplexerBin M10 (.out_4(Out[9]), .Sel(Sel), .X0(X[9]), .X1(Y[9]));
  MultiplexerBin M11 (.out_4(Out[10]), .Sel(Sel), .X0(X[10]), .X1(Y[10]));
  MultiplexerBin M12 (.out_4(Out[11]), .Sel(Sel), .X0(X[11]), .X1(Y[11]));
  MultiplexerBin M13 (.out_4(Out[12]), .Sel(Sel), .X0(X[12]), .X1(Y[12]));
  MultiplexerBin M14 (.out_4(Out[13]), .Sel(Sel), .X0(X[13]), .X1(Y[13]));
  MultiplexerBin M16 (.out_4(Out[15]), .Sel(Sel), .X0(X[15]), .X1(Y[15]));
  MultiplexerBin M15 (.out_4(Out[14]), .Sel(Sel), .X0(X[14]), .X1(Y[14]));

  // Notes on the sheet:
  //   输入引脚区
  //   电路功能：Out=(Sel==0)?X:Y;
  //   请勿增删改引脚，请在下方利用上方输入输出引脚的隧道标签信号构建电路，ctrl+d复制选择组件
  //   输出引脚区
endmodule

module MultiplexerAutoTesting (
);

  wire and_1_out, CLK, comparator_1_eq, d_ff_1_q, HALT, Halt_t, NEQ, SEL;
  wire [9:0] counter_2_q;
  wire [10:0] counter_1_q;
  wire [15:0] multiplexer_1_out, multiplexer_2_out, multiplexer_2_out_2, multiplexerhex_1_out;
  wire [31:0] XY;

  Clock clock_1 (.out(CLK));
  Counter #(.max('h7ff), .ongoal("stay"), .width(11)) counter_1 (
    .Q(counter_1_q), .carry(Halt_t), .clk(CLK));  // open: load, D, count, up, clr
  LED led_1 (.in(Halt_t));
  Counter #(.max('h3ff), .width(10)) counter_2 (
    .count(NEQ), .Q(counter_2_q), .clk(CLK), .clr(Halt_t));  // open: load, D, carry, up
  ROM #(.addrWidth(11), .dataWidth(32)) rom_1 (.addr(counter_1_q), .data(XY));
  and and_1 (and_1_out, ~Halt_t, NEQ);  // AND_Gate
  Random #(.width(1)) random_1 ();  // open: clk, next, out, clr
  RAM #(.addrWidth(10), .dataWidth(32)) ram_1 (
    .addr(counter_2_q), .we(and_1_out), .clk(CLK), .din(XY));  // open: oe, dout
  _7_Segment_Display u_7_segment_display_1 (
    .g(multiplexer_2_out[15]), .f(multiplexer_2_out[14]), .a(multiplexer_2_out[13]),
    .b(multiplexer_2_out[12]), .e(multiplexer_2_out_2[15]), .d(multiplexer_2_out_2[14]),
    .c(multiplexer_2_out_2[13]), .dp(multiplexer_2_out_2[12]));
  MultiplexerHex multiplexerhex_1 (.Out(multiplexerhex_1_out), .Y(XY[31:16]), .X(XY[15:0]), .Sel(SEL));
  _7_Segment_Display u_7_segment_display_2 (
    .g(multiplexer_2_out[11]), .f(multiplexer_2_out[10]), .a(multiplexer_2_out[9]), .b(multiplexer_2_out[8]),
    .e(multiplexer_2_out_2[11]), .d(multiplexer_2_out_2[10]), .c(multiplexer_2_out_2[9]),
    .dp(multiplexer_2_out_2[8]));
  _7_Segment_Display u_7_segment_display_3 (
    .g(multiplexer_2_out[7]), .f(multiplexer_2_out[6]), .a(multiplexer_2_out[5]), .b(multiplexer_2_out[4]),
    .e(multiplexer_2_out_2[7]), .d(multiplexer_2_out_2[6]), .c(multiplexer_2_out_2[5]),
    .dp(multiplexer_2_out_2[4]));
  D_Flip_Flop d_ff_1 (.clk(CLK), .D(NEQ), .Q(d_ff_1_q));  // open: Qn, preset, reset
  Multiplexer #(.enable("false"), .width(16)) multiplexer_1 (
    .in0(XY[15:0]), .in1(XY[31:16]), .out(multiplexer_1_out), .sel(SEL));
  _7_Segment_Display u_7_segment_display_4 (
    .g(multiplexer_2_out[3]), .f(multiplexer_2_out[2]), .a(multiplexer_2_out[1]), .b(multiplexer_2_out[0]),
    .e(multiplexer_2_out_2[3]), .d(multiplexer_2_out_2[2]), .c(multiplexer_2_out_2[1]),
    .dp(multiplexer_2_out_2[0]));
  Comparator #(.width(16)) comparator_1 (
    .a(multiplexer_1_out), .b(multiplexerhex_1_out), .eq(comparator_1_eq));  // open: gt, lt
  Multiplexer #(.width(32)) multiplexer_2 (
    .in0(32'h8a66ffee), .in1(32'h8a8cef44), .out({multiplexer_2_out_2, multiplexer_2_out}), .sel(d_ff_1_q),
    .en(HALT));
  not not_1 (NEQ, comparator_1_eq);

  // Notes on the sheet:
  //   存储器保存未通过的测试用例
  //   contents of rom_1 (hex, n*v repeats v):
  //   86483f4f 9045b205 fbe9fce5 96280ca8 4899b8c9 4c5a79cc 9b012dbc 9235746a 36687b52 a0441758 f9766af
  //   2bcbc87f ff802acd a0e1645a 5b31cadc 818b2a4a e7335d24 4a5de35 d8a2e906 b9efe7fe 854a3681 3493ad40
  //   480351d2 7627f5e5 bcd68997 3486e006 6cf5520c 413ebb9c 2341bbd8 ea311a86 764210e1 3a307555 faecadbd
  //   18d8f974 20825224 74a6915 d9fde702 ede46977 c6691c8b 9a512ff5 9b7e46e8 6b69326a 7c6a83f0 c33a5362
  //   12a87872 ce72f69d 4edcd791 96da7e5e 2a536aaa f261e612 65567451 1bbd82be e8a40cdb 9db965c1 fee7af6
  //   9571726a bdb68ed5 cae9ead6 bf2aaa6a 79e20ca1 56b3652d d51549ef 1c89dfb 30f5bf34 e9c8517c a980ba5f
  //   8034af9c 8717bc7 d6c1ae9c ae5bcd6f 7064be23 593ca115 f8440ef 2ab79999 49f1178a b72382a c76bca99
  //   15fd59cc fda9c730 840c5a7 6c96a3c1 2e7c0ac 418a8816 8f6def03 2e6a96d5 4ef63fd0 85d39b23 e66733c5
  //   d52340c5 f858303 631c161 c41cfacc 32fe3544 d52c5f84 86439a3e cb793388 49d270b b07748 476ea5cd
  //   2a16cb3f ef7a5417 fed9d034 8ada2b04 1df3364a f6cf75e7 85a09f64 a18a41fe f274d57 fd1375c0 51a48868
  //   89f94237 a648bea6 be3724ea 9a909083 a31d4d3 a8e9534d 610d38f1 740305eb fb4fead9 7fbd4875 d0cdcbe5
  //   cac49b0d 3b72d771 7145fc9b 4669a09c 178df5c7 d98ece2a 647230d1 c8656aec ed4ef2ad 2f300538 3c791dfb
  //   33395bf3 2cdedc46 a325bbaf a6499e14 17b53250 1730d64d e12f63ca d43aa968 2cad0e68 259bbcf1 d22a3128
  //   ba3e67d9 39374aa3 3178b817 31e14b0a b7ad161c 810797ad fd4fc294 2786e297 4fd0fef9 60f79cb7 d5fd6574
  //   e8006d1a f3b0c88f b2915bb5 35b0e737 8994423f 8229558f be73999e c9562f10 732ade5b db3c7a7d 42ac8ab0
  //   e6f29c25 1a3a08a2 c48dc6f3 dfab02aa 9cb010d3 35941d6f bb5aa2df e02a6911 78c571e8 8cb9bc81 bfceffc1
  //   ca81b16d b61fd9e8 bef01b3a 7a6bddef c001978b 8ca3c049 a7423adf 6a48e5d3 e5925fba 321154b8 86b742db
  //   664e5528 ab855b0e 160b4e54 406c3efd 38188041 cd926fa1 c4736eef 57e381b7 490a2743 933de4ce 9143fa51
  //   ecbfea5e 5526df67 b866b375 f4416175 c4464f6e 2fa2d03b 39819a3b bd5361cb f4634cc4 6ea904df b0935c9
  //   c008d876 9997b5e2 22ad9148 cbef5d09 31bd898c d11ec30 a5b4cb81 4b60016d ee0d1b5a 765e5936 644cd8e7
  //   6e9d329 9cb2859e b87d4ce4 d88acf69 9b24e975 fea734cb 40d07fcc 9b30aacf c233aecd 6a49214a b367964
  //   843555f0 6cfe5131 eb831ab5 65ce1a45 a63c07fb 89ccf667 966871b 4408a6f 141c35b1 28e8f435 9259d640
  //   6a13cb84 a86f56a6 2a314ca9 f6f2e8db 816c2f0a 892dbe85 f912ae52 ddc8abd8 7bc6f0aa 30b7ca4a db173885
  //   2bfb2794 409c3474 f63ca186 fc46439a 72e54325 567aa91a 3543cb9f f7d06d2d 7f5f7b90 42130e32 6332d90f
  //   9f08285e de2ecf12 efcdde76 edfc60a1 f86b1213 ffaf1c59 43e95e04 3cb990b8 e0844932 ee7c35c8 6c24c9f
  //   6dc39489 a2b40ae9 3dd0e8b8 f2cd7bec 89f60d5e cc6cd2e7 208738b3 d3ec89b7 2e17dfd2 2e3a3fa1 f5190eb8
  //   d02bfe2d b5fb9518 76e9fa8f b1b49c7b bc9d0e21 94bc9035 5a72e46e 716bb3a3 b1e14149 ce925742 4bbac57c
  //   24b9510b f223c7f cf0730ac 3a1ec1c0 880c9c03 2393f001 adf35475 85a6d141 b6bc998d 724369b2 3271f171
  //   bb107c4a ebbbd3a2 d5d88b58 9919468b 27611bae 7797346b d614e4dd a6130fff b573dcff 18bf5589 ab3df28f
  //   7046889f d2fbcad6 6bcf834f 5844ff61 6c993f0f 91b61910 979b403 d762eb29 a35fff0a 610cf50c 52f2b322
  //   b20214e1 fa6d0e9c 582f19ee 582dc09a e834a8e8 afbcff66 1ca468e0 60eae40f 6999933f 579753de 41abc54d
  //   668f3418 757655cd 10c388e d327525 6cf25180 25f0029c e10c9151 a3f9451e 97c05687 96b19a1a a2ed9a9b
  //   bb7fb0ee ccc37a1f 25f20d5b 10fd5eaf 59914f93 9d5ca730 23b02453 44e13ee7 62d5c38c 46a647d6 21e881d
  //   49cbd0f0 87876f1d 4c30849e 279e3137 a62b500c 83792c90 38fa37ce 824979c4 7345e250 e8d74a70 613dd49c
  //   d2f613cb 934cf1e5 4f940bce 49dd8272 75b82374 8dc4da49 8a33ec7d 13adac32 9c54bd4e 32b2298c 6fb1e957
  //   a591436c 1fb6088d 32d1b593 25780c76 444ef7aa 24574545 7234c559 1fec7d7d 63aa1a6 eec2f6b1 4eee8e2a
  //   fd755ce 8f422290 d4a17170 fb1444e8 aae978d2 73a0f74a d87a0dc3 34250347 f1f0b035 7871bfac 162d3dd1
  //   2602c112 cbc94c28 dd88f9c1 d851c7e5 78f9a165 44e1879e 5f783109 5f0364ab fce6d3f1 8426f091 674ce1b7
  //   b3550178 eb644a3d d37a143b db924ff1 3b7ce680 6bf280e0 7748af5f 6f519314 46f5011e 336d9cc9 42b2a27f
  //   943f14ee db2d9211 57af1c78 dfa1ea24 10f8c503 4d147fbb 95115d43 e881db1a 9f2c3fca 8d978c61 619e3494
  //   b7c5e2b2 13b029ee a36bb06f 9505dd26 fc340b00 e00fff8e fec7d8b1 b90f784c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
  //   X&Y trace
  //   错误记录X&Y
  //   多路选择器自动测试
endmodule

// 4位数比较器
module ComparatorsFourBit (
  input  X3,
  input  Y3,
  input  X2,
  input  Y2,
  input  X1,
  input  Y1,
  input  X0,
  input  Y0,
  output Great,
  output Equal,
  output Less
);

  wire and_1_out, and_2_out, and_3_out, and_4_out, and_5_out, and_6_out, and_7_out, and_8_out, and_9_out,
       and_10_out, and_11_out, and_12_out, and_13_out, and_14_out, and_15_out, and_17_out, and_18_out,
       and_19_out, and_20_out, not_1_out, not_2_out, not_3_out, not_4_out, not_5_out, not_6_out, not_7_out,
       not_8_out, xnor_1_out, xnor_2_out, xnor_3_out, xnor_4_out, xnor_5_out, xnor_6_out, xnor_7_out,
       xnor_8_out, xnor_9_out, xnor_10_out;

  not not_1 (not_1_out, X3);
  not not_2 (not_2_out, Y3);
  not not_3 (not_3_out, X2);
  not not_4 (not_4_out, Y2);
  not not_5 (not_5_out, X1);
  not not_6 (not_6_out, Y1);
  not not_7 (not_7_out, X0);
  not not_8 (not_8_out, Y0);
  and and_1 (and_1_out, not_2_out, not_4_out, not_6_out, X0, not_8_out);
  and and_2 (and_2_out, not_2_out, not_4_out, X1, not_6_out);
  and and_3 (and_3_out, not_2_out, not_4_out, X1, X0, not_8_out);
  and and_4 (and_4_out, not_2_out, X2, not_4_out);
  and and_5 (and_5_out, not_2_out, X2, not_6_out, X0, not_8_out);
  and and_6 (and_6_out, not_2_out, X2, X1, not_6_out);
  and and_7 (and_7_out, not_2_out, X2, X1, X0, not_8_out);
  and and_8 (and_8_out, X3, not_2_out);
  and and_9 (and_9_out, X3, not_4_out, not_6_out, X0, not_8_out);
  and and_10 (and_10_out, X3, not_4_out, X1, not_6_out);
  and and_11 (and_11_out, X3, not_4_out, X1, X0, not_8_out);
  and and_12 (and_12_out, X3, X2, not_4_out);
  and and_13 (and_13_out, X3, X2, not_6_out, X0, not_8_out);
  and and_14 (and_14_out, X3, X2, X1, not_6_out);
  and and_15 (and_15_out, X3, X2, X1, X0, not_8_out);
  xnor xnor_1 (xnor_1_out, X3, Y3);
  xnor xnor_2 (xnor_2_out, X2, Y2);
  xnor xnor_3 (xnor_3_out, X1, Y1);
  xnor xnor_4 (xnor_4_out, X0, Y0);
  xnor xnor_5 (xnor_5_out, X3, Y3);
  xnor xnor_6 (xnor_6_out, X3, Y3);
  xnor xnor_7 (xnor_7_out, X2, Y2);
  xnor xnor_8 (xnor_8_out, X3, Y3);
  xnor xnor_9 (xnor_9_out, X2, Y2);
  xnor xnor_10 (xnor_10_out, X1, Y1);
  and and_16 (Equal, xnor_1_out, xnor_2_out, xnor_3_out, xnor_4_out);
  and and_17 (and_17_out, not_1_out, Y3);
  and and_18 (and_18_out, not_3_out, Y2, xnor_5_out);
  and and_19 (and_19_out, not_5_out, Y1, xnor_6_out, xnor_7_out);
  and and_20 (and_20_out, not_7_out, Y0, xnor_8_out, xnor_9_out, xnor_10_out);
  or or_1 (Great, and_1_out, and_2_out, and_3_out, and_4_out, and_5_out, and_6_out, and_7_out, and_8_out, and_9_out, and_10_out, and_11_out, and_12_out, and_13_out, and_14_out, and_15_out);
  or or_2 (Less, and_17_out, and_18_out, and_19_out, and_20_out);
endmodule

module ComparatorsHex (
  input  [15:0] X,
  input  [15:0] Y,
  output Great,
  output Equal,
  output Less
);

  wire and_1_out, and_2_out, and_3_out, and_4_out, and_5_out, and_6_out, comparatorsfourbit_1_equal,
       comparatorsfourbit_1_great, comparatorsfourbit_1_less, comparatorsfourbit_2_equal,
       comparatorsfourbit_2_great, comparatorsfourbit_2_less, comparatorsfourbit_3_equal,
       comparatorsfourbit_3_great, comparatorsfourbit_3_less, comparatorsfourbit_4_equal,
       comparatorsfourbit_4_great, comparatorsfourbit_4_less;

  // Probe on X
  // Probe on Y
  ComparatorsFourBit comparatorsfourbit_1 (
    .X3(X[15]), .Y3(Y[15]), .X2(X[14]), .Y2(Y[14]), .X1(X[13]), .Y1(Y[13]), .X0(X[12]), .Y0(Y[12]),
    .Great(comparatorsfourbit_1_great), .Equal(comparatorsfourbit_1_equal), .Less(comparatorsfourbit_1_less));
  ComparatorsFourBit comparatorsfourbit_2 (
    .X3(X[11]), .Y3(Y[11]), .X2(X[10]), .Y2(Y[10]), .X1(X[9]), .Y1(Y[9]), .X0(X[8]), .Y0(Y[8]),
    .Great(comparatorsfourbit_2_great), .Equal(comparatorsfourbit_2_equal), .Less(comparatorsfourbit_2_less));
  ComparatorsFourBit comparatorsfourbit_3 (
    .X3(X[7]), .Y3(Y[7]), .X2(X[6]), .Y2(Y[6]), .X1(X[5]), .Y1(Y[5]), .X0(X[4]), .Y0(Y[4]),
    .Great(comparatorsfourbit_3_great), .Equal(comparatorsfourbit_3_equal), .Less(comparatorsfourbit_3_less));
  ComparatorsFourBit comparatorsfourbit_4 (
    .X3(X[3]), .Y3(Y[3]), .X2(X[2]), .Y2(Y[2]), .X1(X[1]), .Y1(Y[1]), .X0(X[0]), .Y0(Y[0]),
    .Great(comparatorsfourbit_4_great), .Equal(comparatorsfourbit_4_equal), .Less(comparatorsfourbit_4_less));
  and and_1 (and_1_out, comparatorsfourbit_1_equal, comparatorsfourbit_2_great);
  and and_2 (and_2_out, comparatorsfourbit_1_equal, comparatorsfourbit_2_equal, comparatorsfourbit_3_great);
  and and_3 (and_3_out, comparatorsfourbit_1_equal, comparatorsfourbit_2_equal, comparatorsfourbit_3_equal, comparatorsfourbit_4_great);
  and and_4 (and_4_out, comparatorsfourbit_1_equal, comparatorsfourbit_2_less);
  and and_5 (and_5_out, comparatorsfourbit_1_equal, comparatorsfourbit_2_equal, comparatorsfourbit_3_less);
  and and_6 (and_6_out, comparatorsfourbit_1_equal, comparatorsfourbit_2_equal, comparatorsfourbit_3_equal, comparatorsfourbit_4_less);
  or or_1 (Great, comparatorsfourbit_1_great, and_1_out, and_2_out, and_3_out);
  and and_7 (Equal, comparatorsfourbit_1_equal, comparatorsfourbit_2_equal, comparatorsfourbit_3_equal, comparatorsfourbit_4_equal);
  or or_2 (Less, comparatorsfourbit_1_less, and_4_out, and_5_out, and_6_out);

  // Other names for the same wires on the sheet: X0[3:0] = X[3:0]; X1[3:0] = X[7:4]; X2[3:0] = X[11:8];
  //   X3[3:0] = X[15:12]; Y0[3:0] = Y[3:0]; Y1[3:0] = Y[7:4]; Y2[3:0] = Y[11:8]; Y3[3:0] = Y[15:12]

  // Notes on the sheet:
  //   电路功能：X,Y进行无符号比较，Great=(X>Y)?1:0;
  //   输入引脚区
  //   输出引脚区
endmodule

// 16位2-1 MUX
module ComparatorHexAutoTesting (
);

  wire CLK, comparator_2_eq, d_ff_1_q, Halt, NEQ;
  wire [2:0] comparator_1_gt, comparatorshex_1_great;
  wire [7:0] counter_1_q;
  wire [9:0] counter_2_q;
  wire [15:0] multiplexer_1_out, multiplexer_1_out_2;
  wire [31:0] XY;

  Clock clock_1 (.out(CLK));
  Counter #(.ongoal("stay")) counter_1 (.Q(counter_1_q), .clk(CLK), .clr(Halt));  // open: load, D, count, carry, up
  LED led_1 (.in(Halt));
  Counter #(.max('h3ff), .width(10)) counter_2 (
    .count(NEQ), .Q(counter_2_q), .clk(CLK), .clr(Halt));  // open: load, D, carry, up
  ROM #(.dataWidth(32)) rom_1 (.addr(counter_1_q), .data(XY));
  RAM #(.addrWidth(10), .dataWidth(32)) ram_1 (.addr(counter_2_q), .clk(CLK), .din(XY));  // open: we, oe, dout
  // AND_Gate and_1 has open pins: in0=NEQ, in1=Halt, out=open
  _7_Segment_Display u_7_segment_display_1 (
    .g(multiplexer_1_out[15]), .f(multiplexer_1_out[14]), .a(multiplexer_1_out[13]),
    .b(multiplexer_1_out[12]), .e(multiplexer_1_out_2[15]), .d(multiplexer_1_out_2[14]),
    .c(multiplexer_1_out_2[13]), .dp(multiplexer_1_out_2[12]));
  ComparatorsHex comparatorshex_1 (
    .Equal(comparatorshex_1_great[1]), .Less(comparatorshex_1_great[2]), .Great(comparatorshex_1_great[0]),
    .Y(XY[31:16]), .X(XY[15:0]));
  Comparator #(.mode("unsigned"), .width(16)) comparator_1 (
    .a(XY[15:0]), .b(XY[31:16]), .gt(comparator_1_gt[0]), .eq(comparator_1_gt[1]), .lt(comparator_1_gt[2]));
  _7_Segment_Display u_7_segment_display_2 (
    .g(multiplexer_1_out[11]), .f(multiplexer_1_out[10]), .a(multiplexer_1_out[9]), .b(multiplexer_1_out[8]),
    .e(multiplexer_1_out_2[11]), .d(multiplexer_1_out_2[10]), .c(multiplexer_1_out_2[9]),
    .dp(multiplexer_1_out_2[8]));
  _7_Segment_Display u_7_segment_display_3 (
    .g(multiplexer_1_out[7]), .f(multiplexer_1_out[6]), .a(multiplexer_1_out[5]), .b(multiplexer_1_out[4]),
    .e(multiplexer_1_out_2[7]), .d(multiplexer_1_out_2[6]), .c(multiplexer_1_out_2[5]),
    .dp(multiplexer_1_out_2[4]));
  D_Flip_Flop d_ff_1 (.clk(CLK), .D(NEQ), .Q(d_ff_1_q));  // open: Qn, preset, reset
  Comparator #(.width(3)) comparator_2 (
    .a(comparatorshex_1_great), .b(comparator_1_gt), .eq(comparator_2_eq));  // open: gt, lt
  _7_Segment_Display u_7_segment_display_4 (
    .g(multiplexer_1_out[3]), .f(multiplexer_1_out[2]), .a(multiplexer_1_out[1]), .b(multiplexer_1_out[0]),
    .e(multiplexer_1_out_2[3]), .d(multiplexer_1_out_2[2]), .c(multiplexer_1_out_2[1]),
    .dp(multiplexer_1_out_2[0]));
  not not_1 (NEQ, comparator_2_eq);
  Multiplexer #(.width(32)) multiplexer_1 (
    .in0(32'h8a66ffee), .in1(32'h8a8cef44), .out({multiplexer_1_out_2, multiplexer_1_out}), .sel(d_ff_1_q),
    .en(Halt));

  // Notes on the sheet:
  //   contents of rom_1 (hex, n*v repeats v):
  //   ffffffff ffff7fff ffffbfff ffffdfff ffffefff f7fff7ff fffff7ff fffffbff fffffdff fffffeff ff7fff7f
  //   ff7fff7f ffffff7f ffffffbf ffffffdf ffffffef fff7fff7 fffffff7 fffffffb fffffffd fffffffe 0 1 2 4 8
  //   100010 10 20 40 80 1000100 100 200 400 800 10001000 1000 2000 4000 8000 f4815766 588f50e1 691a47b9
  //   953cad65 f4d07a42 847bfafc 699a478c d3a3b941 45a67aa3 40ad61ed fbdbd7af ad681465 6d29551b f8b4a89f
  //   c46931ce 6da641d0 a32356fb c8596d72 c8d957f6 a225ef12 e2f0e69e dac18d78 2c29b6da e8498992 849a8fa0
  //   cc89dbb9 96e7ac10 d859e7c7 ed1b931f 9a6b0c71 5dc43051 905b4680 fd993c02 dc7a144e e08fe5be 3d2cda1d
  //   3953372f b7c73bb4 9541ca16 a38833d4 66592fd4 11325f9 a28ecd02 2689baee 3995efa0 b7850caa f7bc8a4b
  //   72bf7a08 2f844308 b9c16ec6 d7bd681f 5f4f8054 be5e184 167473ff 78485951 969b16d7 e01899d1 8f5743fd
  //   86828397 40d809aa 6d2a022d 6eb919b 3df509cb 916d453a 8dec9f 119c9a28 a7ed3a2b 4f740789 8c5fdf2d
  //   76a8d8a9 3509609a e92e56c fa5bd025 82bad13 14987cde e37be3cc 173e6657 fd23792 99971ce1 42aae4e6
  //   b700fd56 133aa7c6 7779af1 fc95a98b dd69adbb 9bb14002 ed880001 c452a662 dab9962 ecf24c8d aaabc9e7
  //   70cfed22 eb57bbac 61cc4ee1 f043d59d 890769da d2a27dbd eff19cf0 8682ad82 3d31b42a 2064ebd d1fcb45b
  //   d20f7b97 85ccb489 9f8f8018 7b9e81b9 8ebddfc3 d15f5d7e d4a1a5be fc21dbd8 144ea10 c737b8e8 2fcaba65
  //   42e372f4 ee4378ec c3f48937 793c47c3 c117402 93843b6a a87fbeb1 6fc6d2d5 85fa1fea 95579780 713300af
  //   fdb7cc1c 346496c5 70fdb449 25338adf 22be43dc abe31724 f27ee841 99a69e81 15fea25d 26c1f149 bf4cb8c
  //   1533c7ab 45c1a42b a42a6e6d 222a2e30 2a5e3686 5caeda57 c02aab14 765acad5 4706d961 fe025b53 922c42e5
  //   b89287ec 70e6f79d 60622e31 d91c7840 cd0cd37 b1c0a92e 4b6f62a6 b10aebaf f62577cd 73fa0e0d aca68551
  //   f99276ec 233c77e6 c9cfc487 eac76497 39b70c27 19695f22 460dfa7d d920e8e0 367a4942 d3592c2 c4c152a6
  //   efda30d8 245dff15 6b7761ed 8b08ddc9 c54931b0 603fecac 181c3fed e6866805 8d2b1b5b 2f6dee84 68346271
  //   777e5a0b 7396c0d3 dd85e1d3 ff7203cb 688c6e5f 46c54453 9ca87bbe e2328930 17e67a9c 9051479b 5ba54a2
  //   604bccfb 747a8cad c050e030 6ee2674d 5e3bcceb 20c99c16 66b28f9a 3a294443 95fcfc62 22340f2a ed897fa6
  //   b11038fb 92a57aa5 91815453 5d7942a2 302bab20 8e1b6d1f bcbfcf4f 303557a5 c33fe7d1 5a8cbd9f 72e5a6e
  //   180cb2c6 9313a6e2 c5fc7c97
  //   X&Y trace
  //   错误记录X&Y
  //   存储器保存未通过的测试用例
  //   16位数无符号比较器自动测试
  //   ctrl+K驱动时钟自动测试
endmodule

// 4位寄存器
module FourBitConcurrentLoadRegister (
  input  CLK,
  input  [3:0] Din,
  input  Enable,
  output [3:0] OutputQ
);

  wire multiplexerbin_1_out_4;

  MultiplexerBin multiplexerbin_1 (.out_4(multiplexerbin_1_out_4), .Sel(Enable), .X0(1'b0), .X1(CLK));
  D_Flip_Flop d_ff_1 (.clk(multiplexerbin_1_out_4), .D(Din[0]), .Q(OutputQ[0]));  // open: Qn, preset, reset
  D_Flip_Flop d_ff_2 (.clk(multiplexerbin_1_out_4), .D(Din[1]), .Q(OutputQ[1]));  // open: Qn, preset, reset
  D_Flip_Flop d_ff_3 (.clk(multiplexerbin_1_out_4), .D(Din[2]), .Q(OutputQ[2]));  // open: Qn, preset, reset
  D_Flip_Flop d_ff_4 (.clk(multiplexerbin_1_out_4), .D(Din[3]), .Q(OutputQ[3]));  // open: Qn, preset, reset
  // Probe on OutputQ

  // Other names for the same wires on the sheet: En = Enable; Q[3:0] = OutputQ

  // Notes on the sheet:
  //   输入引脚区
  //   4位并行加载寄存器，输入Din 4位；输出Q 4位；En：使能端；
  //   请勿增删改引脚，请在下方利用上方输入输出引脚的隧道标签信号构建电路，ctrl+d复制选择组件
  //   输出引脚区
endmodule

// 16位寄存器 SD
module HexConcurrentLoadRegister (
  input  CLK,
  input  [15:0] Din,
  input  Enable,
  output [15:0] OutputQ
);

  // Probe on Din
  FourBitConcurrentLoadRegister fourbitconcurrentloadregister_1 (
    .OutputQ(OutputQ[3:0]), .Enable(Enable), .Din(Din[3:0]), .CLK(CLK));
  FourBitConcurrentLoadRegister fourbitconcurrentloadregister_2 (
    .OutputQ(OutputQ[7:4]), .Enable(Enable), .Din(Din[7:4]), .CLK(CLK));
  FourBitConcurrentLoadRegister fourbitconcurrentloadregister_3 (
    .OutputQ(OutputQ[11:8]), .Enable(Enable), .Din(Din[11:8]), .CLK(CLK));
  FourBitConcurrentLoadRegister fourbitconcurrentloadregister_4 (
    .OutputQ(OutputQ[15:12]), .Enable(Enable), .Din(Din[15:12]), .CLK(CLK));
  // Probe on OutputQ

  // Other names for the same wires on the sheet: En = Enable; Q[15:0] = OutputQ

  // Notes on the sheet:
  //   输入引脚区
  //   16位并行加载寄存器，输入Din 16位；输出Q 16位；En：使能端；
  //   请勿增删改引脚，请在下方利用上方输入输出引脚的隧道标签信号构建电路，ctrl+d复制选择组件
  //   输出引脚区
endmodule

// 4位BCD计数器
module FourBitBCDCounter (
  input  CLK,
  input  Enable,
  input  AsynReset,
  output [3:0] OutputQ,
  output OutputCarryBit
);

  wire bcdcounterstateexchangeauto_1_n0, bcdcounterstateexchangeauto_1_n1, bcdcounterstateexchangeauto_1_n2,
       bcdcounterstateexchangeauto_1_n3, multiplexerbin_1_out_4;

  BCDCounterStateExchangeAuto bcdcounterstateexchangeauto_1 (
    .N1(bcdcounterstateexchangeauto_1_n1), .N0(bcdcounterstateexchangeauto_1_n0),
    .N3(bcdcounterstateexchangeauto_1_n3), .N2(bcdcounterstateexchangeauto_1_n2), .S1(OutputQ[1]),
    .S0(OutputQ[0]), .S3(OutputQ[3]), .S2(OutputQ[2]));
  MultiplexerBin multiplexerbin_1 (.out_4(multiplexerbin_1_out_4), .Sel(Enable), .X0(1'b0), .X1(CLK));
  // Probe on OutputQ
  D_Flip_Flop d_ff_1 (
    .D(bcdcounterstateexchangeauto_1_n0), .clk(multiplexerbin_1_out_4), .Q(OutputQ[0]), .reset(AsynReset));  // open: Qn, preset
  D_Flip_Flop d_ff_2 (
    .D(bcdcounterstateexchangeauto_1_n1), .clk(multiplexerbin_1_out_4), .Q(OutputQ[1]), .reset(AsynReset));  // open: Qn, preset
  D_Flip_Flop d_ff_3 (
    .D(bcdcounterstateexchangeauto_1_n2), .clk(multiplexerbin_1_out_4), .Q(OutputQ[2]), .reset(AsynReset));  // open: Qn, preset
  D_Flip_Flop d_ff_4 (
    .D(bcdcounterstateexchangeauto_1_n3), .clk(multiplexerbin_1_out_4), .Q(OutputQ[3]), .reset(AsynReset));  // open: Qn, preset
  BCDCounterInputFunctionAuto bcdcounterinputfunctionauto_1 (
    .Cout(OutputCarryBit), .S1(OutputQ[2]), .S0(OutputQ[3]), .S3(OutputQ[0]), .S2(OutputQ[1]));

  // Other names for the same wires on the sheet: Cout = OutputCarryBit; En = Enable; Q[3:0] = OutputQ;
  //   Rst = AsynReset

  // Notes on the sheet:
  //   输入引脚区
  //   4位BCD计数器，输出Q在0-9之间循环计数，EN：使能端；Rst：异步复位；Cout=(Q==9)?1:0;
  //   请勿增删改引脚，请在下方利用上方输入输出引脚的隧道标签信号构建电路，ctrl+d复制选择组件
  //   输出引脚区
endmodule

// 状态转换
module BCDCounterStateExchangeAuto (
  input  S3,
  input  S2,
  input  S1,
  input  S0,
  output N3,
  output N2,
  output N1,
  output N0
);

  wire and_1_out, and_2_out, and_3_out, and_4_out, and_5_out, and_6_out, and_7_out, and_8_out, and_9_out,
       and_10_out, and_11_out, and_12_out, and_13_out, and_14_out, and_15_out, not_1_out, not_2_out,
       not_3_out, not_4_out;

  not not_1 (not_1_out, S3);
  not not_2 (not_2_out, S2);
  not not_3 (not_3_out, S1);
  not not_4 (not_4_out, S0);
  and and_1 (and_1_out, not_1_out, S2, S1, S0);
  and and_2 (and_2_out, S3, not_2_out, not_3_out, not_4_out);
  and and_3 (and_3_out, not_1_out, not_2_out, S1, S0);
  and and_4 (and_4_out, not_1_out, S2, not_3_out, not_4_out);
  and and_5 (and_5_out, not_1_out, S2, not_3_out, S0);
  and and_6 (and_6_out, not_1_out, S2, S1, not_4_out);
  and and_7 (and_7_out, not_1_out, not_2_out, not_3_out, S0);
  and and_8 (and_8_out, not_1_out, not_2_out, S1, not_4_out);
  and and_9 (and_9_out, not_1_out, S2, not_3_out, S0);
  and and_10 (and_10_out, not_1_out, S2, S1, not_4_out);
  and and_11 (and_11_out, not_1_out, not_2_out, not_3_out, not_4_out);
  and and_12 (and_12_out, not_1_out, not_2_out, S1, not_4_out);
  and and_13 (and_13_out, not_1_out, S2, not_3_out, not_4_out);
  and and_14 (and_14_out, not_1_out, S2, S1, not_4_out);
  and and_15 (and_15_out, S3, not_2_out, not_3_out, not_4_out);
  or or_1 (N3, and_1_out, and_2_out);
  or or_2 (N2, and_3_out, and_4_out, and_5_out, and_6_out);
  or or_3 (N1, and_7_out, and_8_out, and_9_out, and_10_out);
  or or_4 (N0, and_11_out, and_12_out, and_13_out, and_14_out, and_15_out);
endmodule

module BCDCounterInputFunctionAuto (
  input  S3,
  input  S2,
  input  S1,
  input  S0,
  output Cout
);

  wire and_1_out, and_2_out;

  and and_1 (and_1_out, S3, ~S2);  // AND_Gate
  and and_2 (and_2_out, ~S1, S0);  // AND_Gate
  and and_3 (Cout, and_1_out, and_2_out);
endmodule

// 计时器 TM
module StopwatchCounter (
  input  CLK,
  input  En,
  input  Rst,
  output [15:0] OutputQ
);

  wire and_1_out, and_2_out, and_3_out, fourbitbcdcounter_1_outputcarrybit,
       fourbitbcdcounter_2_outputcarrybit, fourbitbcdcounter_3_outputcarrybit;

  // Probe on OutputQ
  and and_1 (and_1_out, En, fourbitbcdcounter_1_outputcarrybit, fourbitbcdcounter_3_outputcarrybit);
  and and_2 (and_2_out, En, fourbitbcdcounter_1_outputcarrybit);
  FourBitBCDCounter fourbitbcdcounter_1 (
    .OutputQ(OutputQ[3:0]), .OutputCarryBit(fourbitbcdcounter_1_outputcarrybit), .AsynReset(Rst), .CLK(CLK),
    .Enable(En));
  and and_3 (and_3_out, En, fourbitbcdcounter_1_outputcarrybit, fourbitbcdcounter_3_outputcarrybit, fourbitbcdcounter_2_outputcarrybit);
  FourBitBCDCounter fourbitbcdcounter_2 (
    .OutputQ(OutputQ[11:8]), .OutputCarryBit(fourbitbcdcounter_2_outputcarrybit), .AsynReset(Rst), .CLK(CLK),
    .Enable(and_1_out));
  FourBitBCDCounter fourbitbcdcounter_3 (
    .OutputQ(OutputQ[7:4]), .OutputCarryBit(fourbitbcdcounter_3_outputcarrybit), .AsynReset(Rst), .CLK(CLK),
    .Enable(and_2_out));
  FourBitBCDCounter fourbitbcdcounter_4 (
    .OutputQ(OutputQ[15:12]), .AsynReset(Rst), .CLK(CLK), .Enable(and_3_out));  // open: OutputCarryBit

  // Other names for the same wires on the sheet: Q[15:0] = OutputQ

  // Notes on the sheet:
  //   输入引脚区
  //   码表计数器，16位输出，包括4个BCD计数器，分别对应10秒、1秒、1/10秒、1/100秒。
  //   低位计数到9时，相邻高位在时钟到来时加1。                    En：使能端；Rst：异步复位；
  //   输出引脚区
endmodule

module StopwatchAutoTesting (
  input  Rst
);

  wire CLK_out;
  wire [3:0] stopwatchcounter_1_outputq_2, stopwatchcounter_1_outputq_3;
  wire [7:0] stopwatchcounter_1_outputq;

  Hex_Digit_Display hex_digit_display_1 (.value(stopwatchcounter_1_outputq_3));  // open: dp
  Hex_Digit_Display hex_digit_display_2 (.value(stopwatchcounter_1_outputq_2), .dp(1'b1));
  StopwatchCounter stopwatchcounter_1 (
    .OutputQ({stopwatchcounter_1_outputq_3, stopwatchcounter_1_outputq_2, stopwatchcounter_1_outputq}),
    .CLK(CLK_out), .En(1'b1), .Rst(Rst));
  Hex_Digit_Display hex_digit_display_3 (.value(stopwatchcounter_1_outputq[7:4]));  // open: dp
  Hex_Digit_Display hex_digit_display_4 (.value(stopwatchcounter_1_outputq[3:0]));  // open: dp
  Clock CLK (.out(CLK_out));

  // Notes on the sheet:
  //   En
  //   Ctrl+K驱动时钟自动测试
endmodule

// 码表显示 DP
module StopwatchDisplayDriver (
  input  [15:0] HexBitDin,
  output [31:0] DigitalTubeDisplayControl
);

  _7_Segment_Display u_7_segment_display_1 (
    .g(DigitalTubeDisplayControl[0]), .f(DigitalTubeDisplayControl[1]), .a(DigitalTubeDisplayControl[2]),
    .b(DigitalTubeDisplayControl[3]), .e(DigitalTubeDisplayControl[4]), .d(DigitalTubeDisplayControl[5]),
    .c(DigitalTubeDisplayControl[6]), .dp(1'b0));
  DigitalTubeDriver digitaltubedriver_1 (
    .Seq3(DigitalTubeDisplayControl[2]), .Seq4(DigitalTubeDisplayControl[3]),
    .Seq5(DigitalTubeDisplayControl[4]), .Seq6(DigitalTubeDisplayControl[5]),
    .Seq7(DigitalTubeDisplayControl[6]), .Seq1(DigitalTubeDisplayControl[0]),
    .Seq2(DigitalTubeDisplayControl[1]), .X1(HexBitDin[1]), .X0(HexBitDin[0]), .X3(HexBitDin[3]),
    .X2(HexBitDin[2]));
  DigitalTubeDriver digitaltubedriver_2 (
    .Seq3(DigitalTubeDisplayControl[10]), .Seq4(DigitalTubeDisplayControl[11]),
    .Seq5(DigitalTubeDisplayControl[12]), .Seq6(DigitalTubeDisplayControl[13]),
    .Seq7(DigitalTubeDisplayControl[14]), .Seq1(DigitalTubeDisplayControl[8]),
    .Seq2(DigitalTubeDisplayControl[9]), .X1(HexBitDin[5]), .X0(HexBitDin[4]), .X3(HexBitDin[7]),
    .X2(HexBitDin[6]));
  DigitalTubeDriver digitaltubedriver_3 (
    .Seq3(DigitalTubeDisplayControl[18]), .Seq4(DigitalTubeDisplayControl[19]),
    .Seq5(DigitalTubeDisplayControl[20]), .Seq6(DigitalTubeDisplayControl[21]),
    .Seq7(DigitalTubeDisplayControl[22]), .Seq1(DigitalTubeDisplayControl[16]),
    .Seq2(DigitalTubeDisplayControl[17]), .X1(HexBitDin[9]), .X0(HexBitDin[8]), .X3(HexBitDin[11]),
    .X2(HexBitDin[10]));
  DigitalTubeDriver digitaltubedriver_4 (
    .Seq3(DigitalTubeDisplayControl[26]), .Seq4(DigitalTubeDisplayControl[27]),
    .Seq5(DigitalTubeDisplayControl[28]), .Seq6(DigitalTubeDisplayControl[29]),
    .Seq7(DigitalTubeDisplayControl[30]), .Seq1(DigitalTubeDisplayControl[24]),
    .Seq2(DigitalTubeDisplayControl[25]), .X1(HexBitDin[13]), .X0(HexBitDin[12]), .X3(HexBitDin[15]),
    .X2(HexBitDin[14]));

  assign {DigitalTubeDisplayControl[31], DigitalTubeDisplayControl[23], DigitalTubeDisplayControl[15], DigitalTubeDisplayControl[7]} = 4'b0000;

  // Other names for the same wires on the sheet: Din[15:0] = HexBitDin;
  //   DispInfo (some bits) = {DigitalTubeDisplayControl[30:24], DigitalTubeDisplayControl[22:16], DigitalTubeDisplayControl[14:8], DigitalTubeDisplayControl[6:0]}

  // Notes on the sheet:
  //   输入引脚区
  //   码表计数显示输出驱动，将16位BCD数据输出到四个7段数码管，输出为4个数码管的控制信息，共32位。
  //   输出引脚区
endmodule

module SportStopwatch (
);

  wire CLK, DP_SEL, NewRecord, Reset, SD_EN, SD_SEL, Start, Stop, Store, TM_EN, TM_Reset;
  wire [15:0] hexconcurrentloadregister_1_outputq, multiplexerhex_1_out, multiplexerhex_2_out,
       stopwatchcounter_1_outputq;
  wire [31:0] DispInfo;

  Button u_Start (.out(Start));
  Button u_Stop (.out(Stop));
  Button u_Store (.out(Store));
  Button u_Reset (.out(Reset));
  _7_Segment_Display u_7_segment_display_1 (
    .g(DispInfo[24]), .f(DispInfo[25]), .a(DispInfo[26]), .b(DispInfo[27]), .e(DispInfo[28]),
    .d(DispInfo[29]), .c(DispInfo[30]), .dp(DispInfo[31]));
  _7_Segment_Display u_7_segment_display_2 (
    .g(DispInfo[16]), .f(DispInfo[17]), .a(DispInfo[18]), .b(DispInfo[19]), .e(DispInfo[20]),
    .d(DispInfo[21]), .c(DispInfo[22]), .dp(DispInfo[23]));
  _7_Segment_Display u_7_segment_display_3 (
    .g(DispInfo[8]), .f(DispInfo[9]), .a(DispInfo[10]), .b(DispInfo[11]), .e(DispInfo[12]), .d(DispInfo[13]),
    .c(DispInfo[14]), .dp(DispInfo[15]));
  _7_Segment_Display u_7_segment_display_4 (
    .g(DispInfo[0]), .f(DispInfo[1]), .a(DispInfo[2]), .b(DispInfo[3]), .e(DispInfo[4]), .d(DispInfo[5]),
    .c(DispInfo[6]), .dp(DispInfo[7]));
  // Probe on DispInfo
  Clock u_CLK (.out(CLK));
  StopwatchDisplayDriver stopwatchdisplaydriver_1 (
    .DigitalTubeDisplayControl(DispInfo), .HexBitDin(multiplexerhex_1_out));
  MultiplexerHex multiplexerhex_1 (
    .Out(multiplexerhex_1_out), .Y(hexconcurrentloadregister_1_outputq), .X(stopwatchcounter_1_outputq),
    .Sel(DP_SEL));
  StopwatchCounter stopwatchcounter_1 (.OutputQ(stopwatchcounter_1_outputq), .CLK(CLK), .En(TM_EN), .Rst(TM_Reset));
  HexConcurrentLoadRegister hexconcurrentloadregister_1 (
    .OutputQ(hexconcurrentloadregister_1_outputq), .Din(multiplexerhex_2_out), .Enable(SD_EN), .CLK(CLK));
  MultiplexerHex multiplexerhex_2 (
    .Out(multiplexerhex_2_out), .Y(stopwatchcounter_1_outputq), .X(16'h9999), .Sel(SD_SEL));
  ComparatorsHex comparatorshex_1 (
    .Great(NewRecord), .Y(stopwatchcounter_1_outputq), .X(hexconcurrentloadregister_1_outputq));  // open: Equal, Less
  // Probe on hexconcurrentloadregister_1_outputq
  StopwatchController stopwatchcontroller_1 (
    .DP_Sel(DP_SEL), .TMen(TM_EN), .TMreset(TM_Reset), .SDsel(SD_SEL), .SDen(SD_EN), .CLK(CLK),
    .start(Start), .stop(Stop), .store(Store), .reset(Reset), .NewRecord(NewRecord));

  // Other names for the same wires on the sheet: S1B[3:0] = DispInfo[3:0]; S1T[3:0] = DispInfo[7:4];
  //   S2B[3:0] = DispInfo[11:8]; S2T[3:0] = DispInfo[15:12]; S3B[3:0] = DispInfo[19:16]; S3T[3:0] = DispInfo[23:20];
  //   S4B[3:0] = DispInfo[27:24]; S4T[3:0] = DispInfo[31:28]

  // Notes on the sheet:
  //   控
  //   制
  //   信
  //   号
  //   运
  //   动
  //   码
  //   表
endmodule

// 码表控制器
module StopwatchController (
  input  start,
  input  stop,
  input  store,
  input  reset,
  input  NewRecord,
  input  CLK,
  output SDsel,
  output SDen,
  output DP_Sel,
  output TMen,
  output TMreset
);

  wire d_ff_1_q, d_ff_2_q, d_ff_3_q, stopwatchcontrollerstateconversionauto_1_n0,
       stopwatchcontrollerstateconversionauto_1_n1, stopwatchcontrollerstateconversionauto_1_n2;

  StopwatchControllerStateConversionAuto stopwatchcontrollerstateconversionauto_1 (
    .N0(stopwatchcontrollerstateconversionauto_1_n0), .N2(stopwatchcontrollerstateconversionauto_1_n2),
    .N1(stopwatchcontrollerstateconversionauto_1_n1), .store(store), .reset(reset), .NewRecord(NewRecord),
    .S2(d_ff_1_q), .S1(d_ff_2_q), .S0(d_ff_3_q), .start(start), .stop(stop));
  D_Flip_Flop d_ff_1 (
    .D(stopwatchcontrollerstateconversionauto_1_n2), .clk(CLK), .Q(d_ff_1_q));  // open: Qn, preset, reset
  D_Flip_Flop d_ff_2 (
    .D(stopwatchcontrollerstateconversionauto_1_n1), .clk(CLK), .Q(d_ff_2_q));  // open: Qn, preset, reset
  D_Flip_Flop d_ff_3 (
    .D(stopwatchcontrollerstateconversionauto_1_n0), .clk(CLK), .Q(d_ff_3_q));  // open: Qn, preset, reset
  StopwatchControllerInputFunctionAuto stopwatchcontrollerinputfunctionauto_1 (
    .DPSEL(DP_Sel), .TMSel(TMen), .TMReset(TMreset), .SDSel(SDsel), .SDEN(SDen), .S0(d_ff_3_q),
    .S2(d_ff_1_q), .S1(d_ff_2_q));
endmodule

// 状态转换
module StopwatchControllerStateConversionAuto (
  input  start,
  input  stop,
  input  store,
  input  reset,
  input  NewRecord,
  input  S2,
  input  S1,
  input  S0,
  output N2,
  output N1,
  output N0
);

  wire and_1_out, and_2_out, and_3_out, and_4_out, and_5_out, and_6_out, and_7_out, and_8_out, and_9_out,
       and_10_out, and_11_out, and_12_out, and_13_out, and_14_out, and_15_out, and_16_out, and_17_out,
       not_1_out, not_2_out, not_3_out, not_4_out, not_5_out, not_6_out, not_7_out, not_8_out;

  not not_1 (not_1_out, start);
  not not_2 (not_2_out, stop);
  not not_3 (not_3_out, store);
  not not_4 (not_4_out, reset);
  not not_5 (not_5_out, NewRecord);
  not not_6 (not_6_out, S2);
  not not_7 (not_7_out, S1);
  not not_8 (not_8_out, S0);
  and and_1 (and_1_out, not_2_out, store, not_5_out, not_6_out, S1, S0);
  and and_2 (and_2_out, not_2_out, store, NewRecord, not_6_out, S1, S0);
  and and_3 (and_3_out, store, S2, not_7_out, not_8_out);
  and and_4 (and_4_out, not_3_out, S2, not_7_out, not_8_out);
  and and_5 (and_5_out, start, not_6_out, not_7_out, S0);
  and and_6 (and_6_out, not_2_out, not_3_out, not_6_out, S1, S0);
  and and_7 (and_7_out, not_2_out, store, NewRecord, not_6_out, S1, S0);
  and and_8 (and_8_out, stop, not_6_out, S1, S0);
  and and_9 (and_9_out, start, not_4_out, not_6_out, S1, not_8_out);
  and and_10 (and_10_out, not_1_out, not_4_out, not_6_out, S1, not_8_out);
  and and_11 (and_11_out, not_3_out, S2, not_7_out, not_8_out);
  and and_12 (and_12_out, not_6_out, not_7_out, not_8_out);
  and and_13 (and_13_out, start, not_6_out, not_7_out, S0);
  and and_14 (and_14_out, not_1_out, not_6_out, not_7_out, S0);
  and and_15 (and_15_out, not_2_out, not_3_out, not_6_out, S1, S0);
  and and_16 (and_16_out, start, not_4_out, not_6_out, S1, not_8_out);
  and and_17 (and_17_out, not_3_out, S2, not_7_out, not_8_out);
  or or_1 (N2, and_1_out, and_2_out, and_3_out, and_4_out);
  or or_2 (N1, and_5_out, and_6_out, and_7_out, and_8_out, and_9_out, and_10_out, and_11_out);
  or or_3 (N0, and_12_out, and_13_out, and_14_out, and_15_out, and_16_out, and_17_out);
endmodule

// 输出函数
module StopwatchControllerInputFunctionAuto (
  input  S2,
  input  S1,
  input  S0,
  output SDSel,
  output SDEN,
  output DPSEL,
  output TMSel,
  output TMReset
);

  wire and_1_out, and_2_out, and_3_out, and_4_out, and_6_out, and_7_out, and_8_out, not_1_out, not_2_out,
       not_3_out;

  not not_1 (not_1_out, S2);
  not not_2 (not_2_out, S1);
  not not_3 (not_3_out, S0);
  and and_1 (and_1_out, S2, S1, not_3_out);
  and and_2 (and_2_out, S2, not_2_out, not_3_out);
  and and_3 (and_3_out, not_1_out, not_2_out, not_3_out);
  and and_4 (and_4_out, S2, S1, not_3_out);
  and and_5 (DPSEL, S2, not_2_out, not_3_out);
  and and_6 (and_6_out, not_1_out, S1, S0);
  and and_7 (and_7_out, S2, S1, not_3_out);
  and and_8 (and_8_out, S2, not_2_out, not_3_out);
  and and_9 (TMReset, not_1_out, not_2_out, S0);
  or or_1 (SDSel, and_1_out, and_2_out);
  or or_2 (SDEN, and_3_out, and_4_out);
  or or_3 (TMSel, and_6_out, and_7_out, and_8_out);
endmodule
