// Logisim project data.circ as structural Verilog: 23 circuits, main circuit NationalStandardTransitionAreaCode
module NationalStandardTransitionAreaCode (
  input  [15:0] GB2312,
  output [6:0] L_e0d75744,
  output [6:0] L_d0f54a78
);

  // Probe on GB2312
  // Probe on L_e0d75744
  Adder adder_1 ();  // open: a, b, out, cin, cout
  // Probe on L_d0f54a78

  // Notes on the sheet:
  //   请勿增改引脚，请勿修改子电路封装
  //   输入引脚区
  //   请在下方利用上方输入输出引脚的隧道标签信号构建电路，ctrl+d复制选择组件
  //   华中科技大学计算机学院 计算机组成原理课程组
  //   要求用加法器完成
  //   推荐用最新的logisim意大利hust改良版完成实验，EDU平台采用该版本进行测试
  //   输出引脚区
  //   探测区
endmodule

module ChineseCharacterDisplay (
  output [15:0] EduCoder
);

  wire clock_1_out;
  wire [6:0] nationalstandardtransitionareacode_1_l_d0f54a78, nationalstandardtransitionareacode_1_l_e0d75744;
  wire [7:0] counter_1_q;
  wire [31:0] letterlibrary_1_out_3, letterlibrary_1_out_4, letterlibrary_1_out_5, letterlibrary_1_out_6,
       letterlibrary_1_out_7, letterlibrary_1_out_8, letterlibrary_1_out_9, letterlibrary_1_out_10,
       letterlibrary_1_out_11, letterlibrary_1_out_12, letterlibrary_1_out_13, letterlibrary_1_out_14,
       letterlibrary_1_out_15, letterlibrary_1_out_16, letterlibrary_1_out_17, letterlibrary_1_out_18,
       letterlibrary_1_out_19, letterlibrary_1_out_20, letterlibrary_1_out_21, letterlibrary_1_out_22,
       letterlibrary_1_out_23, letterlibrary_1_out_24, letterlibrary_1_out_25, letterlibrary_1_out_26,
       letterlibrary_1_out_27, letterlibrary_1_out_28, letterlibrary_1_out_29, letterlibrary_1_out_30,
       letterlibrary_1_out_31, letterlibrary_1_out_32, letterlibrary_1_out_33, letterlibrary_1_out_34;

  ROM #(.dataWidth(16)) rom_1 (.addr(counter_1_q));  // open: data
  Counter counter_1 (.Q(counter_1_q), .clk(clock_1_out));  // open: load, D, count, carry, up, clr
  Clock clock_1 (.out(clock_1_out));
  NationalStandardTransitionAreaCode nationalstandardtransitionareacode_1 (
    .L_e0d75744(nationalstandardtransitionareacode_1_l_e0d75744),
    .L_d0f54a78(nationalstandardtransitionareacode_1_l_d0f54a78), .GB2312(EduCoder));
  DotMatrix #(.dotshape("circle"), .inputtype("row"), .matrixcols(32), .matrixrows(32)) dotmatrix_1 (
    .row0(letterlibrary_1_out_3), .row1(letterlibrary_1_out_4), .row2(letterlibrary_1_out_5),
    .row3(letterlibrary_1_out_6), .row4(letterlibrary_1_out_7), .row5(letterlibrary_1_out_8),
    .row6(letterlibrary_1_out_9), .row7(letterlibrary_1_out_10), .row8(letterlibrary_1_out_11),
    .row9(letterlibrary_1_out_12), .row10(letterlibrary_1_out_13), .row11(letterlibrary_1_out_14),
    .row12(letterlibrary_1_out_15), .row13(letterlibrary_1_out_16), .row14(letterlibrary_1_out_17),
    .row15(letterlibrary_1_out_18), .row16(letterlibrary_1_out_19), .row17(letterlibrary_1_out_20),
    .row18(letterlibrary_1_out_21), .row19(letterlibrary_1_out_22), .row20(letterlibrary_1_out_23),
    .row21(letterlibrary_1_out_24), .row22(letterlibrary_1_out_25), .row23(letterlibrary_1_out_26),
    .row24(letterlibrary_1_out_27), .row25(letterlibrary_1_out_28), .row26(letterlibrary_1_out_29),
    .row27(letterlibrary_1_out_30), .row28(letterlibrary_1_out_31), .row29(letterlibrary_1_out_32),
    .row30(letterlibrary_1_out_33), .row31(letterlibrary_1_out_34));
  LetterLibrary letterlibrary_1 (
    .out_14(letterlibrary_1_out_14), .out_30(letterlibrary_1_out_30), .out_15(letterlibrary_1_out_15),
    .out_31(letterlibrary_1_out_31), .out_16(letterlibrary_1_out_16), .out_32(letterlibrary_1_out_32),
    .out_17(letterlibrary_1_out_17), .out_33(letterlibrary_1_out_33), .out_18(letterlibrary_1_out_18),
    .out_34(letterlibrary_1_out_34), .out_4(letterlibrary_1_out_4), .out_20(letterlibrary_1_out_20),
    .out_5(letterlibrary_1_out_5), .out_21(letterlibrary_1_out_21), .out_6(letterlibrary_1_out_6),
    .out_22(letterlibrary_1_out_22), .out_7(letterlibrary_1_out_7), .out_23(letterlibrary_1_out_23),
    .out_8(letterlibrary_1_out_8), .out_24(letterlibrary_1_out_24), .out_9(letterlibrary_1_out_9),
    .out_25(letterlibrary_1_out_25), .out_10(letterlibrary_1_out_10), .out_26(letterlibrary_1_out_26),
    .out_3(letterlibrary_1_out_3), .out_19(letterlibrary_1_out_19), .out_11(letterlibrary_1_out_11),
    .out_27(letterlibrary_1_out_27), .out_12(letterlibrary_1_out_12), .out_28(letterlibrary_1_out_28),
    .out_13(letterlibrary_1_out_13), .out_29(letterlibrary_1_out_29),
    .L_e0d75744(nationalstandardtransitionareacode_1_l_e0d75744),
    .L_d0f54a78(nationalstandardtransitionareacode_1_l_d0f54a78));

  // Notes on the sheet:
  //   计数器
  //   contents of rom_1 (hex, n*v repeats v):
  //   bbaa d6d0 bfc6 bcbc b4f3 d1a7 bcc6 cbe3 bbfa d1a7 d4ba ccb7 d6be bba2
  //   GB2312
  //   实现国标转区位码电路，使得系统每个时钟正确显示一个汉字
  //   请将下面这段文字转换成GB2312替换ROM存储器中内容
  //   １２３４５ＡＢＣＤＥＦＧａｂｃｄｅｆｇ轻轻的我走了，正如我轻轻的来；我轻轻的招手，作别西天的云彩。那河畔的金柳，是夕阳中的新娘；波光里的艳影，在我的心头荡漾。
endmodule

// 偶校验编码
module L_b33f7de1 (
  input  [15:0] \原始数据 ,
  output [16:0] L_fc3bd895
);


  assign L_fc3bd895[15:0] = \原始数据 ;

  // Other names for the same wires on the sheet: D1 = \原始数据 [0]; Data[15:0] = \原始数据 ;
  //   L_5261a57e[16:0] = {L_fc3bd895[16], \原始数据 }; D2 = \原始数据 [1]; D3 = \原始数据 [2]; D4 = \原始数据 [3]; D5 = \原始数据 [4];
  //   D6 = \原始数据 [5]; D7 = \原始数据 [6]; D8 = \原始数据 [7]; D9 = \原始数据 [8]; D10 = \原始数据 [9]; D11 = \原始数据 [10];
  //   D12 = \原始数据 [11]; D13 = \原始数据 [12]; D14 = \原始数据 [13]; D15 = \原始数据 [14]; D16 = \原始数据 [15]

  // Notes on the sheet:
  //   输入引脚区
  //   请勿增改引脚，请勿修改子电路封装
  //   电路功能：实现16位数据位的偶校验编码，输入：16位数据；输出：17位校验码（数据位+校验位）
  //   请在下方利用上方输入输出引脚的隧道信号构建电路，ctrl+d复制选择部件
  //   输出引脚区
endmodule

// 偶校验检错
module L_8e5bae90 (
  input  [16:0] L_fc3bd895,
  output L_1425883c,
  output [15:0] L_d332f524
);


  assign L_d332f524 = L_fc3bd895[15:0];

  // Other names for the same wires on the sheet: D1 = L_fc3bd895[0]; L_4f73a4c7[16:0] = L_fc3bd895;
  //   D2 = L_fc3bd895[1]; D3 = L_fc3bd895[2]; D4 = L_fc3bd895[3]; D5 = L_fc3bd895[4]; D6 = L_fc3bd895[5];
  //   D7 = L_fc3bd895[6]; D8 = L_fc3bd895[7]; D9 = L_fc3bd895[8]; D10 = L_fc3bd895[9]; D11 = L_fc3bd895[10];
  //   D12 = L_fc3bd895[11]; D13 = L_fc3bd895[12]; D14 = L_fc3bd895[13]; D15 = L_fc3bd895[14]; D16 = L_fc3bd895[15];
  //   P1 = L_fc3bd895[16]

  // Notes on the sheet:
  //   输入引脚区
  //   请勿增改引脚，请勿修改子电路封装
  //   电路功能：实现17位偶校验编码的检错以及数据提取。输入：17位校验码；输出：检错位、数据位
  //   请在下方利用上方输入输出引脚的隧道信号构建电路，ctrl+d复制选择部件
  //   输出引脚区
endmodule

// 海明编码
module L_00584185 (
  input  [15:0] L_d11c89cc,
  output [21:0] L_ba8a574d
);


  assign {L_ba8a574d[20:16], L_ba8a574d[14:8], L_ba8a574d[6:4], L_ba8a574d[2]} = L_d11c89cc;

  // Other names for the same wires on the sheet: D12 = L_d11c89cc[11]; Data[15:0] = L_d11c89cc; D14 = L_d11c89cc[13];
  //   D15 = L_d11c89cc[14]; D16 = L_d11c89cc[15]; P1 = L_ba8a574d[0]; P2 = L_ba8a574d[1]; D1 = L_d11c89cc[0];
  //   P3 = L_ba8a574d[3]; D2 = L_d11c89cc[1]; D3 = L_d11c89cc[2]; D4 = L_d11c89cc[3]; P4 = L_ba8a574d[7];
  //   D5 = L_d11c89cc[4]; D6 = L_d11c89cc[5]; D7 = L_d11c89cc[6]; D8 = L_d11c89cc[7]; D9 = L_d11c89cc[8];
  //   D10 = L_d11c89cc[9]; D11 = L_d11c89cc[10]; P5 = L_ba8a574d[15]; D13 = L_d11c89cc[12]; P6 = L_ba8a574d[21]

  // Notes on the sheet:
  //   输入引脚区
  //   请勿增改引脚，请勿修改子电路封装
  //   电路功能：海明编码电路，可检两位错并纠一位错，输入：16位；输出：22位海明码（数据位+校验位）
  //   注意异或门需要设置多输入行为：奇数个1时输出为1，否则功能不正确
  //   请在下方利用上方输入输出引脚的隧道信号构建电路，ctrl+d复制选择部件
  //   输出引脚区
endmodule

// 海明解码
module L_455c5dad (
  input  [21:0] L_ba8a574d,
  output L_0_eb6a1b8d,
  output L_1_ef5de30d,
  output L_2_d93bbbb2,
  output [15:0] L_9904c55d
);


  // Other names for the same wires on the sheet: P1 = L_ba8a574d[0]; P2 = L_ba8a574d[1]; D1 = L_ba8a574d[2];
  //   P3 = L_ba8a574d[3]; D2 = L_ba8a574d[4]; D3 = L_ba8a574d[5]; D4 = L_ba8a574d[6]; P4 = L_ba8a574d[7];
  //   D5 = L_ba8a574d[8]; D6 = L_ba8a574d[9]; D7 = L_ba8a574d[10]; D8 = L_ba8a574d[11]; D9 = L_ba8a574d[12];
  //   D10 = L_ba8a574d[13]; D11 = L_ba8a574d[14]; P5 = L_ba8a574d[15]; D12 = L_ba8a574d[16]; D13 = L_ba8a574d[17];
  //   D14 = L_ba8a574d[18]; D15 = L_ba8a574d[19]; D16 = L_ba8a574d[20]; P6 = L_ba8a574d[21]

  // Notes on the sheet:
  //   输入引脚区
  //   输出引脚区
  //   注意异或门需要设置多输入行为：奇数个1时输出为1，否则功能不正确
  //   电路功能：
  //   请勿增改引脚，请勿修改子电路封装
  //   输入：22位海明码；输出：纠错后的数据、错误模式
  //   请在下方利用上方输入输出引脚的隧道信号构建电路，ctrl+d复制选择部件
  //   实现22位海明码的数据解码，能判断1位错，2位错，无错误，1位错自动纠错。
  //   总偶校验检错位
endmodule

// CRC编码
module L_CRC_4439dc43 (
  input  [15:0] L_d11c89cc,
  output [21:0] CRC_5864b47a
);


  // Other names for the same wires on the sheet: D1 = L_d11c89cc[0]; Data[15:0] = L_d11c89cc; D2 = L_d11c89cc[1];
  //   D3 = L_d11c89cc[2]; D4 = L_d11c89cc[3]; D5 = L_d11c89cc[4]; D6 = L_d11c89cc[5]; D7 = L_d11c89cc[6];
  //   D9 = L_d11c89cc[8]; CRC_1f12ebce[21:0] = CRC_5864b47a; D8 = L_d11c89cc[7]; D10 = L_d11c89cc[9];
  //   D11 = L_d11c89cc[10]; D12 = L_d11c89cc[11]; D13 = L_d11c89cc[12]; D14 = L_d11c89cc[13]; D15 = L_d11c89cc[14];
  //   D16 = L_d11c89cc[15]

  // Notes on the sheet:
  //   输入引脚区
  //   请勿增改引脚，请勿修改子电路封装
  //   注意异或门需要设置多输入行为：奇数个1时输出为1，否则功能不正确
  //   电路功能：CRC编码电路，可检两位错并纠一位错，输入：16位；输出：22位海明码（数据位+校验位）
  //   请在下方利用上方输入输出引脚的隧道信号构建电路，ctrl+d复制选择部件
  //   输出引脚区
endmodule

// CRC解码
module L_CRC_dc188f0d (
  input  [21:0] CRC_1f12ebce,
  output L_0_eb6a1b8d,
  output L_1_ef5de30d,
  output L_2_d93bbbb2,
  output [15:0] L_9904c55d
);


  // Other names for the same wires on the sheet: CRC[21:0] = CRC_1f12ebce; r1 = CRC_1f12ebce[0]; r2 = CRC_1f12ebce[1];
  //   r3 = CRC_1f12ebce[2]; r4 = CRC_1f12ebce[3]; r5 = CRC_1f12ebce[4]; r6 = CRC_1f12ebce[5]; D1 = CRC_1f12ebce[6];
  //   D2 = CRC_1f12ebce[7]; D3 = CRC_1f12ebce[8]; D4 = CRC_1f12ebce[9]; D5 = CRC_1f12ebce[10]; D6 = CRC_1f12ebce[11];
  //   D7 = CRC_1f12ebce[12]; D8 = CRC_1f12ebce[13]; D9 = CRC_1f12ebce[14]; D10 = CRC_1f12ebce[15];
  //   D11 = CRC_1f12ebce[16]; D12 = CRC_1f12ebce[17]; D13 = CRC_1f12ebce[18]; D14 = CRC_1f12ebce[19];
  //   D15 = CRC_1f12ebce[20]; D16 = CRC_1f12ebce[21]

  // Notes on the sheet:
  //   输入引脚区
  //   输出引脚区
  //   注意异或门需要设置多输入行为：奇数个1时输出为1，否则功能不正确
  //   电路功能：
  //   请勿增改引脚，请勿修改子电路封装
  //   输入：22位CRC编码；输出：纠错后的数据、错误模式
  //   请在下方利用上方输入输出引脚的隧道信号构建电路，ctrl+d复制选择部件
  //   实现22位海CRC编码的数据解码，能判断1位错，2位错，无错误，1位错自动纠错。
endmodule

module L_d4cd2d64 (
);

  wire and_1_out, comparator_1_eq, counter_1_p1, counter_1_p3, l_8e5bae90_1_l_1425883c, L_d237f850_out;
  wire [6:0] nationalstandardtransitionareacode_1_l_d0f54a78,
       nationalstandardtransitionareacode_1_l_e0d75744, nationalstandardtransitionareacode_2_l_d0f54a78,
       nationalstandardtransitionareacode_2_l_e0d75744;
  wire [7:0] counter_1_p2;
  wire [15:0] L_04ee53f0, L_8cdface8;
  wire [16:0] l_17_ebb656ca_1_l_d265d600, l_17_ebb656ca_1_l_d9787977, l_b33f7de1_1_l_fc3bd895;
  wire [31:0] letterlibrary_1_out_3, letterlibrary_1_out_4, letterlibrary_1_out_5, letterlibrary_1_out_6,
       letterlibrary_1_out_7, letterlibrary_1_out_8, letterlibrary_1_out_9, letterlibrary_1_out_10,
       letterlibrary_1_out_11, letterlibrary_1_out_12, letterlibrary_1_out_13, letterlibrary_1_out_14,
       letterlibrary_1_out_15, letterlibrary_1_out_16, letterlibrary_1_out_17, letterlibrary_1_out_18,
       letterlibrary_1_out_19, letterlibrary_1_out_20, letterlibrary_1_out_21, letterlibrary_1_out_22,
       letterlibrary_1_out_23, letterlibrary_1_out_24, letterlibrary_1_out_25, letterlibrary_1_out_26,
       letterlibrary_1_out_27, letterlibrary_1_out_28, letterlibrary_1_out_29, letterlibrary_1_out_30,
       letterlibrary_1_out_31, letterlibrary_1_out_32, letterlibrary_1_out_33, letterlibrary_1_out_34,
       letterlibrary_2_out_3, letterlibrary_2_out_4, letterlibrary_2_out_5, letterlibrary_2_out_6,
       letterlibrary_2_out_7, letterlibrary_2_out_8, letterlibrary_2_out_9, letterlibrary_2_out_10,
       letterlibrary_2_out_11, letterlibrary_2_out_12, letterlibrary_2_out_13, letterlibrary_2_out_14,
       letterlibrary_2_out_15, letterlibrary_2_out_16, letterlibrary_2_out_17, letterlibrary_2_out_18,
       letterlibrary_2_out_19, letterlibrary_2_out_20, letterlibrary_2_out_21, letterlibrary_2_out_22,
       letterlibrary_2_out_23, letterlibrary_2_out_24, letterlibrary_2_out_25, letterlibrary_2_out_26,
       letterlibrary_2_out_27, letterlibrary_2_out_28, letterlibrary_2_out_29, letterlibrary_2_out_30,
       letterlibrary_2_out_31, letterlibrary_2_out_32, letterlibrary_2_out_33, letterlibrary_2_out_34;

  // Counter counter_1: pin names not known; wires that end beside it: counter_1_p1, counter_1_p2, counter_1_p3, counter_1_p3
  Clock clock_1 (.out(counter_1_p1));
  NationalStandardTransitionAreaCode nationalstandardtransitionareacode_1 (
    .L_e0d75744(nationalstandardtransitionareacode_1_l_e0d75744),
    .L_d0f54a78(nationalstandardtransitionareacode_1_l_d0f54a78), .GB2312(L_04ee53f0));
  ROM #(.dataWidth(16)) rom_1 (.addr(counter_1_p2), .data(L_04ee53f0));
  DotMatrix #(.dotshape("circle"), .inputtype("row"), .matrixcols(32), .matrixrows(32)) dotmatrix_1 (
    .row0(letterlibrary_1_out_3), .row1(letterlibrary_1_out_4), .row2(letterlibrary_1_out_5),
    .row3(letterlibrary_1_out_6), .row4(letterlibrary_1_out_7), .row5(letterlibrary_1_out_8),
    .row6(letterlibrary_1_out_9), .row7(letterlibrary_1_out_10), .row8(letterlibrary_1_out_11),
    .row9(letterlibrary_1_out_12), .row10(letterlibrary_1_out_13), .row11(letterlibrary_1_out_14),
    .row12(letterlibrary_1_out_15), .row13(letterlibrary_1_out_16), .row14(letterlibrary_1_out_17),
    .row15(letterlibrary_1_out_18), .row16(letterlibrary_1_out_19), .row17(letterlibrary_1_out_20),
    .row18(letterlibrary_1_out_21), .row19(letterlibrary_1_out_22), .row20(letterlibrary_1_out_23),
    .row21(letterlibrary_1_out_24), .row22(letterlibrary_1_out_25), .row23(letterlibrary_1_out_26),
    .row24(letterlibrary_1_out_27), .row25(letterlibrary_1_out_28), .row26(letterlibrary_1_out_29),
    .row27(letterlibrary_1_out_30), .row28(letterlibrary_1_out_31), .row29(letterlibrary_1_out_32),
    .row30(letterlibrary_1_out_33), .row31(letterlibrary_1_out_34));
  LetterLibrary letterlibrary_1 (
    .out_14(letterlibrary_1_out_14), .out_30(letterlibrary_1_out_30), .out_15(letterlibrary_1_out_15),
    .out_31(letterlibrary_1_out_31), .out_16(letterlibrary_1_out_16), .out_32(letterlibrary_1_out_32),
    .out_17(letterlibrary_1_out_17), .out_33(letterlibrary_1_out_33), .out_18(letterlibrary_1_out_18),
    .out_34(letterlibrary_1_out_34), .out_4(letterlibrary_1_out_4), .out_20(letterlibrary_1_out_20),
    .out_5(letterlibrary_1_out_5), .out_21(letterlibrary_1_out_21), .out_6(letterlibrary_1_out_6),
    .out_22(letterlibrary_1_out_22), .out_7(letterlibrary_1_out_7), .out_23(letterlibrary_1_out_23),
    .out_8(letterlibrary_1_out_8), .out_24(letterlibrary_1_out_24), .out_9(letterlibrary_1_out_9),
    .out_25(letterlibrary_1_out_25), .out_10(letterlibrary_1_out_10), .out_26(letterlibrary_1_out_26),
    .out_3(letterlibrary_1_out_3), .out_19(letterlibrary_1_out_19), .out_11(letterlibrary_1_out_11),
    .out_27(letterlibrary_1_out_27), .out_12(letterlibrary_1_out_12), .out_28(letterlibrary_1_out_28),
    .out_13(letterlibrary_1_out_13), .out_29(letterlibrary_1_out_29),
    .L_e0d75744(nationalstandardtransitionareacode_1_l_e0d75744),
    .L_d0f54a78(nationalstandardtransitionareacode_1_l_d0f54a78));
  // Probe on L_04ee53f0
  L_b33f7de1 l_b33f7de1_1 (.L_fc3bd895(l_b33f7de1_1_l_fc3bd895), .\原始数据 (L_04ee53f0));
  // Probe on l_b33f7de1_1_l_fc3bd895
  // Probe on l_b33f7de1_1_l_fc3bd895
  // Probe on l_17_ebb656ca_1_l_d265d600
  L_17_ebb656ca l_17_ebb656ca_1 (
    .L_d265d600(l_17_ebb656ca_1_l_d265d600), .L_d9787977(l_17_ebb656ca_1_l_d9787977),
    .L_17_c666427e(l_b33f7de1_1_l_fc3bd895), .CLK(L_d237f850_out));
  Clock L_d237f850 (.out(L_d237f850_out));
  // Probe on l_17_ebb656ca_1_l_d9787977
  // Probe on l_17_ebb656ca_1_l_d9787977
  NationalStandardTransitionAreaCode nationalstandardtransitionareacode_2 (
    .L_e0d75744(nationalstandardtransitionareacode_2_l_e0d75744),
    .L_d0f54a78(nationalstandardtransitionareacode_2_l_d0f54a78), .GB2312(L_8cdface8));
  DotMatrix #(.dotshape("circle"), .inputtype("row"), .matrixcols(32), .matrixrows(32)) dotmatrix_2 (
    .row0(letterlibrary_2_out_3), .row1(letterlibrary_2_out_4), .row2(letterlibrary_2_out_5),
    .row3(letterlibrary_2_out_6), .row4(letterlibrary_2_out_7), .row5(letterlibrary_2_out_8),
    .row6(letterlibrary_2_out_9), .row7(letterlibrary_2_out_10), .row8(letterlibrary_2_out_11),
    .row9(letterlibrary_2_out_12), .row10(letterlibrary_2_out_13), .row11(letterlibrary_2_out_14),
    .row12(letterlibrary_2_out_15), .row13(letterlibrary_2_out_16), .row14(letterlibrary_2_out_17),
    .row15(letterlibrary_2_out_18), .row16(letterlibrary_2_out_19), .row17(letterlibrary_2_out_20),
    .row18(letterlibrary_2_out_21), .row19(letterlibrary_2_out_22), .row20(letterlibrary_2_out_23),
    .row21(letterlibrary_2_out_24), .row22(letterlibrary_2_out_25), .row23(letterlibrary_2_out_26),
    .row24(letterlibrary_2_out_27), .row25(letterlibrary_2_out_28), .row26(letterlibrary_2_out_29),
    .row27(letterlibrary_2_out_30), .row28(letterlibrary_2_out_31), .row29(letterlibrary_2_out_32),
    .row30(letterlibrary_2_out_33), .row31(letterlibrary_2_out_34));
  LetterLibrary letterlibrary_2 (
    .out_14(letterlibrary_2_out_14), .out_30(letterlibrary_2_out_30), .out_15(letterlibrary_2_out_15),
    .out_31(letterlibrary_2_out_31), .out_16(letterlibrary_2_out_16), .out_32(letterlibrary_2_out_32),
    .out_17(letterlibrary_2_out_17), .out_33(letterlibrary_2_out_33), .out_18(letterlibrary_2_out_18),
    .out_34(letterlibrary_2_out_34), .out_4(letterlibrary_2_out_4), .out_20(letterlibrary_2_out_20),
    .out_5(letterlibrary_2_out_5), .out_21(letterlibrary_2_out_21), .out_6(letterlibrary_2_out_6),
    .out_22(letterlibrary_2_out_22), .out_7(letterlibrary_2_out_7), .out_23(letterlibrary_2_out_23),
    .out_8(letterlibrary_2_out_8), .out_24(letterlibrary_2_out_24), .out_9(letterlibrary_2_out_9),
    .out_25(letterlibrary_2_out_25), .out_10(letterlibrary_2_out_10), .out_26(letterlibrary_2_out_26),
    .out_3(letterlibrary_2_out_3), .out_19(letterlibrary_2_out_19), .out_11(letterlibrary_2_out_11),
    .out_27(letterlibrary_2_out_27), .out_12(letterlibrary_2_out_12), .out_28(letterlibrary_2_out_28),
    .out_13(letterlibrary_2_out_13), .out_29(letterlibrary_2_out_29),
    .L_e0d75744(nationalstandardtransitionareacode_2_l_e0d75744),
    .L_d0f54a78(nationalstandardtransitionareacode_2_l_d0f54a78));
  LED L_1425883c (.in(l_8e5bae90_1_l_1425883c));
  L_8e5bae90 l_8e5bae90_1 (
    .L_d332f524(L_8cdface8), .L_1425883c(l_8e5bae90_1_l_1425883c), .L_fc3bd895(l_17_ebb656ca_1_l_d9787977));
  Comparator #(.width(16)) comparator_1 (.a(L_04ee53f0), .b(L_8cdface8), .eq(comparator_1_eq));  // open: gt, lt
  // Probe on L_8cdface8
  and and_1 (and_1_out, ~comparator_1_eq, ~l_8e5bae90_1_l_1425883c);  // AND_Gate
  LED L_40aec5df (.in(comparator_1_eq));
  LED L_16cc2df0 (.in(and_1_out));

  // Notes on the sheet:
  //   发送方
  //   计数器
  //   发送方
  //   汉字显示
  //   GB2312
  //   contents of rom_1 (hex, n*v repeats v):
  //   bbaa d6d0 bfc6 bcbc b4f3 d1a7 cac7 b9fa bcd2 bdcc d3fd b2bf d6b1 caf4 b5c4 c8ab b9fa d6d8 b5e3 b4f3
  //   d1a7 a3ac d3c9 d4ad bbaa d6d0 c0ed b9a4 b4f3 d1a7 a1a2 cdac bcc3 d2bd bfc6 b4f3 d1a7 a1a2 cee4 baba
  //   b3c7 cad0 bda8 c9e8 d1a7 d4ba d3da a3b2 a3b0 a3b0 a3b0 c4ea a3b5 d4c2 a3b2 a3b6 c8d5 bacf b2a2 b3c9
  //   c1a2 a3ac cac7 cad7 c5fa c1d0 c8eb b9fa bcd2 a1b0 a3b2 a3b1 a3b1 b9a4 b3cc a1b1 d6d8 b5e3 bda8 c9e8
  //   bacd b9fa bcd2 a1b0 a3b9 a3b8 a3b5 b9a4 b3cc a1b1 bda8 c9e8 b8df d0a3 d6ae d2bb a1a3 d1a7 d0a3 d0a3
  //   d4b0 d5bc b5d8 c6df c7a7 d3e0 c4b6 a3ac d4b0 c4da caf7 c4be b4d0 dcd7 a3ac b1cc b2dd c8e7 d2f0 a3ac
  //   bbb7 beb3 d3c5 d1c5 a3ac beb0 c9ab d0e3 c0f6 a3ac c2cc bbaf b8b2 b8c7 c2ca 3732 25a3 acb1 bbd3 fece
  //   aaa1 b0c9 adc1 d6ca bdb4 f3d1 a7a1 b1a1
  //   发送方在ROM预存了一段中文文字，通过计数器驱动电路每个时钟传输一个汉字到接收方
  //   用户实现了国标转区位码电路后，可在中间窗口观察发送方和接收方汉字显示是否一致以观察检错性能
  //   电路功能：测试偶校验编解码电路正确性，仿真时设置加扰控制位和原始数据，按CTRL+T触发不同的干扰，检验编解码电路功能
  //   偶校验编解码传输电路
  //   接收方
  //   汉字显示
  //   Ctrl+T  Ctrl+K 驱动时钟触发随机干扰变化
  //   接收方
  //   请将时钟频率调到8Hz
endmodule

module L_1_6c8f0ed3 (
  input  [15:0] L_d11c89cc,
  input  [1:0] L_7e85a9f4
);

  wire clock_1_out, comparator_1_eq, l_455c5dad_1_l_0_eb6a1b8d, l_455c5dad_1_l_1_ef5de30d,
       l_455c5dad_1_l_2_d93bbbb2;
  wire [15:0] l_455c5dad_1_l_9904c55d;
  wire [21:0] l_22_9fb87853_1_l_d265d600, l_22_9fb87853_1_l_d9787977, l_00584185_1_l_ba8a574d;

  // Probe on L_d11c89cc
  // Probe on l_00584185_1_l_ba8a574d
  L_00584185 l_00584185_1 (.L_ba8a574d(l_00584185_1_l_ba8a574d), .L_d11c89cc(L_d11c89cc));
  // Probe on l_00584185_1_l_ba8a574d
  // Probe on l_22_9fb87853_1_l_d265d600
  Clock clock_1 (.out(clock_1_out));
  // Probe on l_22_9fb87853_1_l_d9787977
  L_22_9fb87853 l_22_9fb87853_1 (
    .L_d265d600(l_22_9fb87853_1_l_d265d600), .L_d9787977(l_22_9fb87853_1_l_d9787977), .CLK(clock_1_out),
    .L_22_36bcc28c(l_00584185_1_l_ba8a574d), .L_f486a1f2(L_7e85a9f4));  // open: EDU, L_745543a0
  // Probe on l_22_9fb87853_1_l_d9787977
  LED L_f242517a (.in(l_455c5dad_1_l_1_ef5de30d));
  LED L_161fd229 (.in(l_455c5dad_1_l_2_d93bbbb2));
  LED OK (.in(l_455c5dad_1_l_0_eb6a1b8d));
  L_455c5dad l_455c5dad_1 (
    .L_0_eb6a1b8d(l_455c5dad_1_l_0_eb6a1b8d), .L_1_ef5de30d(l_455c5dad_1_l_1_ef5de30d),
    .L_2_d93bbbb2(l_455c5dad_1_l_2_d93bbbb2), .L_9904c55d(l_455c5dad_1_l_9904c55d),
    .L_ba8a574d(l_22_9fb87853_1_l_d9787977));
  // Probe on l_455c5dad_1_l_9904c55d
  Comparator #(.width(16)) comparator_1 (
    .a(L_d11c89cc), .b(l_455c5dad_1_l_9904c55d), .eq(comparator_1_eq));  // open: gt, lt
  LED L_40aec5df (.in(comparator_1_eq));

  // Notes on the sheet:
  //   发送方
  //   Ctrl+T 驱动时钟触发随机干扰变化
  //   海明编解码传输电路
  //   电路功能：测试海明编解码电路正确性，仿真时设置加扰控制位和原始数据，按CTRL+T触发不同的干扰，检验编解码电路功能
  //   加扰控制00：不加扰  01:1位加扰 10:2位加扰 11：随机加扰
  //   接收方
endmodule

module L_2_3c7a70f6 (
  input  [1:0] L_7e85a9f4
);

  wire CLK, comparator_1_eq, l_455c5dad_1_l_0_eb6a1b8d, l_455c5dad_1_l_1_ef5de30d, l_455c5dad_1_l_2_d93bbbb2;
  wire [6:0] nationalstandardtransitionareacode_1_l_d0f54a78,
       nationalstandardtransitionareacode_1_l_e0d75744, nationalstandardtransitionareacode_2_l_d0f54a78,
       nationalstandardtransitionareacode_2_l_e0d75744;
  wire [7:0] counter_1_p2;
  wire [15:0] L_04ee53f0, L_8cdface8;
  wire [21:0] l_22_9fb87853_1_l_d265d600, l_22_9fb87853_1_l_d9787977, l_00584185_1_l_ba8a574d;
  wire [31:0] letterlibrary_1_out_3, letterlibrary_1_out_4, letterlibrary_1_out_5, letterlibrary_1_out_6,
       letterlibrary_1_out_7, letterlibrary_1_out_8, letterlibrary_1_out_9, letterlibrary_1_out_10,
       letterlibrary_1_out_11, letterlibrary_1_out_12, letterlibrary_1_out_13, letterlibrary_1_out_14,
       letterlibrary_1_out_15, letterlibrary_1_out_16, letterlibrary_1_out_17, letterlibrary_1_out_18,
       letterlibrary_1_out_19, letterlibrary_1_out_20, letterlibrary_1_out_21, letterlibrary_1_out_22,
       letterlibrary_1_out_23, letterlibrary_1_out_24, letterlibrary_1_out_25, letterlibrary_1_out_26,
       letterlibrary_1_out_27, letterlibrary_1_out_28, letterlibrary_1_out_29, letterlibrary_1_out_30,
       letterlibrary_1_out_31, letterlibrary_1_out_32, letterlibrary_1_out_33, letterlibrary_1_out_34,
       letterlibrary_2_out_3, letterlibrary_2_out_4, letterlibrary_2_out_5, letterlibrary_2_out_6,
       letterlibrary_2_out_7, letterlibrary_2_out_8, letterlibrary_2_out_9, letterlibrary_2_out_10,
       letterlibrary_2_out_11, letterlibrary_2_out_12, letterlibrary_2_out_13, letterlibrary_2_out_14,
       letterlibrary_2_out_15, letterlibrary_2_out_16, letterlibrary_2_out_17, letterlibrary_2_out_18,
       letterlibrary_2_out_19, letterlibrary_2_out_20, letterlibrary_2_out_21, letterlibrary_2_out_22,
       letterlibrary_2_out_23, letterlibrary_2_out_24, letterlibrary_2_out_25, letterlibrary_2_out_26,
       letterlibrary_2_out_27, letterlibrary_2_out_28, letterlibrary_2_out_29, letterlibrary_2_out_30,
       letterlibrary_2_out_31, letterlibrary_2_out_32, letterlibrary_2_out_33, letterlibrary_2_out_34;

  // Counter counter_1: pin names not known; wires that end beside it: CLK, counter_1_p2
  Clock L_d237f850 (.out(CLK));
  NationalStandardTransitionAreaCode nationalstandardtransitionareacode_1 (
    .L_e0d75744(nationalstandardtransitionareacode_1_l_e0d75744),
    .L_d0f54a78(nationalstandardtransitionareacode_1_l_d0f54a78), .GB2312(L_04ee53f0));
  DotMatrix #(.dotshape("circle"), .inputtype("row"), .matrixcols(32), .matrixrows(32)) dotmatrix_1 (
    .row0(letterlibrary_1_out_3), .row1(letterlibrary_1_out_4), .row2(letterlibrary_1_out_5),
    .row3(letterlibrary_1_out_6), .row4(letterlibrary_1_out_7), .row5(letterlibrary_1_out_8),
    .row6(letterlibrary_1_out_9), .row7(letterlibrary_1_out_10), .row8(letterlibrary_1_out_11),
    .row9(letterlibrary_1_out_12), .row10(letterlibrary_1_out_13), .row11(letterlibrary_1_out_14),
    .row12(letterlibrary_1_out_15), .row13(letterlibrary_1_out_16), .row14(letterlibrary_1_out_17),
    .row15(letterlibrary_1_out_18), .row16(letterlibrary_1_out_19), .row17(letterlibrary_1_out_20),
    .row18(letterlibrary_1_out_21), .row19(letterlibrary_1_out_22), .row20(letterlibrary_1_out_23),
    .row21(letterlibrary_1_out_24), .row22(letterlibrary_1_out_25), .row23(letterlibrary_1_out_26),
    .row24(letterlibrary_1_out_27), .row25(letterlibrary_1_out_28), .row26(letterlibrary_1_out_29),
    .row27(letterlibrary_1_out_30), .row28(letterlibrary_1_out_31), .row29(letterlibrary_1_out_32),
    .row30(letterlibrary_1_out_33), .row31(letterlibrary_1_out_34));
  LetterLibrary letterlibrary_1 (
    .out_14(letterlibrary_1_out_14), .out_30(letterlibrary_1_out_30), .out_15(letterlibrary_1_out_15),
    .out_31(letterlibrary_1_out_31), .out_16(letterlibrary_1_out_16), .out_32(letterlibrary_1_out_32),
    .out_17(letterlibrary_1_out_17), .out_33(letterlibrary_1_out_33), .out_18(letterlibrary_1_out_18),
    .out_34(letterlibrary_1_out_34), .out_4(letterlibrary_1_out_4), .out_20(letterlibrary_1_out_20),
    .out_5(letterlibrary_1_out_5), .out_21(letterlibrary_1_out_21), .out_6(letterlibrary_1_out_6),
    .out_22(letterlibrary_1_out_22), .out_7(letterlibrary_1_out_7), .out_23(letterlibrary_1_out_23),
    .out_8(letterlibrary_1_out_8), .out_24(letterlibrary_1_out_24), .out_9(letterlibrary_1_out_9),
    .out_25(letterlibrary_1_out_25), .out_10(letterlibrary_1_out_10), .out_26(letterlibrary_1_out_26),
    .out_3(letterlibrary_1_out_3), .out_19(letterlibrary_1_out_19), .out_11(letterlibrary_1_out_11),
    .out_27(letterlibrary_1_out_27), .out_12(letterlibrary_1_out_12), .out_28(letterlibrary_1_out_28),
    .out_13(letterlibrary_1_out_13), .out_29(letterlibrary_1_out_29),
    .L_e0d75744(nationalstandardtransitionareacode_1_l_e0d75744),
    .L_d0f54a78(nationalstandardtransitionareacode_1_l_d0f54a78));
  ROM #(.dataWidth(16)) rom_1 (.addr(counter_1_p2), .data(L_04ee53f0));
  // Probe on L_04ee53f0
  // Probe on l_00584185_1_l_ba8a574d
  L_00584185 l_00584185_1 (.L_ba8a574d(l_00584185_1_l_ba8a574d), .L_d11c89cc(L_04ee53f0));
  // Probe on l_00584185_1_l_ba8a574d
  // Probe on l_22_9fb87853_1_l_d265d600
  L_22_9fb87853 l_22_9fb87853_1 (
    .L_d265d600(l_22_9fb87853_1_l_d265d600), .L_d9787977(l_22_9fb87853_1_l_d9787977), .CLK(CLK),
    .L_22_36bcc28c(l_00584185_1_l_ba8a574d), .L_f486a1f2(L_7e85a9f4));  // open: EDU, L_745543a0
  NationalStandardTransitionAreaCode nationalstandardtransitionareacode_2 (
    .L_e0d75744(nationalstandardtransitionareacode_2_l_e0d75744),
    .L_d0f54a78(nationalstandardtransitionareacode_2_l_d0f54a78), .GB2312(L_8cdface8));
  // Probe on l_22_9fb87853_1_l_d9787977
  // Probe on l_22_9fb87853_1_l_d9787977
  LetterLibrary letterlibrary_2 (
    .out_14(letterlibrary_2_out_14), .out_30(letterlibrary_2_out_30), .out_15(letterlibrary_2_out_15),
    .out_31(letterlibrary_2_out_31), .out_16(letterlibrary_2_out_16), .out_32(letterlibrary_2_out_32),
    .out_17(letterlibrary_2_out_17), .out_33(letterlibrary_2_out_33), .out_18(letterlibrary_2_out_18),
    .out_34(letterlibrary_2_out_34), .out_4(letterlibrary_2_out_4), .out_20(letterlibrary_2_out_20),
    .out_5(letterlibrary_2_out_5), .out_21(letterlibrary_2_out_21), .out_6(letterlibrary_2_out_6),
    .out_22(letterlibrary_2_out_22), .out_7(letterlibrary_2_out_7), .out_23(letterlibrary_2_out_23),
    .out_8(letterlibrary_2_out_8), .out_24(letterlibrary_2_out_24), .out_9(letterlibrary_2_out_9),
    .out_25(letterlibrary_2_out_25), .out_10(letterlibrary_2_out_10), .out_26(letterlibrary_2_out_26),
    .out_3(letterlibrary_2_out_3), .out_19(letterlibrary_2_out_19), .out_11(letterlibrary_2_out_11),
    .out_27(letterlibrary_2_out_27), .out_12(letterlibrary_2_out_12), .out_28(letterlibrary_2_out_28),
    .out_13(letterlibrary_2_out_13), .out_29(letterlibrary_2_out_29),
    .L_e0d75744(nationalstandardtransitionareacode_2_l_e0d75744),
    .L_d0f54a78(nationalstandardtransitionareacode_2_l_d0f54a78));
  LED L_f242517a (.in(l_455c5dad_1_l_1_ef5de30d));
  LED L_161fd229 (.in(l_455c5dad_1_l_2_d93bbbb2));
  LED OK (.in(l_455c5dad_1_l_0_eb6a1b8d));
  DotMatrix #(.dotshape("circle"), .inputtype("row"), .matrixcols(32), .matrixrows(32)) dotmatrix_2 (
    .row0(letterlibrary_2_out_3), .row1(letterlibrary_2_out_4), .row2(letterlibrary_2_out_5),
    .row3(letterlibrary_2_out_6), .row4(letterlibrary_2_out_7), .row5(letterlibrary_2_out_8),
    .row6(letterlibrary_2_out_9), .row7(letterlibrary_2_out_10), .row8(letterlibrary_2_out_11),
    .row9(letterlibrary_2_out_12), .row10(letterlibrary_2_out_13), .row11(letterlibrary_2_out_14),
    .row12(letterlibrary_2_out_15), .row13(letterlibrary_2_out_16), .row14(letterlibrary_2_out_17),
    .row15(letterlibrary_2_out_18), .row16(letterlibrary_2_out_19), .row17(letterlibrary_2_out_20),
    .row18(letterlibrary_2_out_21), .row19(letterlibrary_2_out_22), .row20(letterlibrary_2_out_23),
    .row21(letterlibrary_2_out_24), .row22(letterlibrary_2_out_25), .row23(letterlibrary_2_out_26),
    .row24(letterlibrary_2_out_27), .row25(letterlibrary_2_out_28), .row26(letterlibrary_2_out_29),
    .row27(letterlibrary_2_out_30), .row28(letterlibrary_2_out_31), .row29(letterlibrary_2_out_32),
    .row30(letterlibrary_2_out_33), .row31(letterlibrary_2_out_34));
  L_455c5dad l_455c5dad_1 (
    .L_0_eb6a1b8d(l_455c5dad_1_l_0_eb6a1b8d), .L_1_ef5de30d(l_455c5dad_1_l_1_ef5de30d),
    .L_2_d93bbbb2(l_455c5dad_1_l_2_d93bbbb2), .L_9904c55d(L_8cdface8), .L_ba8a574d(l_22_9fb87853_1_l_d9787977));
  // Probe on L_8cdface8
  Comparator #(.width(16)) comparator_1 (.a(L_04ee53f0), .b(L_8cdface8), .eq(comparator_1_eq));  // open: gt, lt
  LED L_40aec5df (.in(comparator_1_eq));

  // Notes on the sheet:
  //   发送方
  //   计数器
  //   发送方
  //   汉字显示
  //   GB2312
  //   contents of rom_1 (hex, n*v repeats v):
  //   bbaa d6d0 bfc6 bcbc b4f3 d1a7 cac7 b9fa bcd2 bdcc d3fd b2bf d6b1 caf4 b5c4 c8ab b9fa d6d8 b5e3 b4f3
  //   d1a7 a3ac d3c9 d4ad bbaa d6d0 c0ed b9a4 b4f3 d1a7 a1a2 cdac bcc3 d2bd bfc6 b4f3 d1a7 a1a2 cee4 baba
  //   b3c7 cad0 bda8 c9e8 d1a7 d4ba d3da a3b2 a3b0 a3b0 a3b0 c4ea a3b5 d4c2 a3b2 a3b6 c8d5 bacf b2a2 b3c9
  //   c1a2 a3ac cac7 cad7 c5fa c1d0 c8eb b9fa bcd2 a1b0 a3b2 a3b1 a3b1 b9a4 b3cc a1b1 d6d8 b5e3 bda8 c9e8
  //   bacd b9fa bcd2 a1b0 a3b9 a3b8 a3b5 b9a4 b3cc a1b1 bda8 c9e8 b8df d0a3 d6ae d2bb a1a3 d1a7 d0a3 d0a3
  //   d4b0 d5bc b5d8 c6df c7a7 d3e0 c4b6 a3ac d4b0 c4da caf7 c4be b4d0 dcd7 a3ac b1cc b2dd c8e7 d2f0 a3ac
  //   bbb7 beb3 d3c5 d1c5 a3ac beb0 c9ab d0e3 c0f6 a3ac c2cc bbaf b8b2 b8c7 c2ca 3732 25a3 acb1 bbd3 fece
  //   aaa1 b0c9 adc1 d6ca bdb4 f3d1 a7a1 b1a1
  //   Ctrl+T 驱动时钟触发随机干扰变化
  //   发送方在ROM预存了一段中文文字，通过计数器驱动电路每个时钟传输一个汉字到接收方
  //   电路功能：测试海明编解码电路正确性，仿真时设置加扰控制位和原始数据，按CTRL+T触发不同的干扰，检验编解码电路功能
  //   用户实现了国标转区位码电路后，可在中间窗口观察发送方和接收方汉字显示是否一致以观察海明检错纠错性能
  //   海明编解码传输电路
  //   接收方
  //   汉字显示
  //   Ctrl+T 驱动时钟触发随机干扰变化
  //   加扰控制00：不加扰  01:1位加扰 10:2位加扰 11：随机加扰
  //   加扰控制00：不加扰  01:1位加扰 10:2位加扰 11：随机加扰
  //   接收方
  //   请将时钟频率调到8Hz
endmodule

// Hamming
module L_be134dae (
  input  L_7d930fa3,
  input  EDU,
  output L_1err_a3df68ae,
  output L_2err_26a15d6f,
  output clr2,
  output clr3,
  output clr4,
  output en5
);

  wire CLK, l_16_b4f519f1_1_l_out_103436ad, l_22_793ae84e_1_l_out_103436ad, l_22_793ae84e_2_l_out_103436ad,
       l_455c5dad_1_l_0_eb6a1b8d;
  wire [6:0] nationalstandardtransitionareacode_1_l_d0f54a78,
       nationalstandardtransitionareacode_1_l_e0d75744, nationalstandardtransitionareacode_2_l_d0f54a78,
       nationalstandardtransitionareacode_2_l_e0d75744;
  wire [7:0] CNT, register_1_p1;
  wire [15:0] L_04ee53f0, L_8cdface8, l_16_b4f519f1_1_dout16, l_455c5dad_1_l_9904c55d;
  wire [21:0] l_22_9fb87853_1_l_d9787977, l_22_793ae84e_1_dout22, l_22_793ae84e_2_dout22,
       l_00584185_1_l_ba8a574d;
  wire [31:0] letterlibrary_1_out_3, letterlibrary_1_out_4, letterlibrary_1_out_5, letterlibrary_1_out_6,
       letterlibrary_1_out_7, letterlibrary_1_out_8, letterlibrary_1_out_9, letterlibrary_1_out_10,
       letterlibrary_1_out_11, letterlibrary_1_out_12, letterlibrary_1_out_13, letterlibrary_1_out_14,
       letterlibrary_1_out_15, letterlibrary_1_out_16, letterlibrary_1_out_17, letterlibrary_1_out_18,
       letterlibrary_1_out_19, letterlibrary_1_out_20, letterlibrary_1_out_21, letterlibrary_1_out_22,
       letterlibrary_1_out_23, letterlibrary_1_out_24, letterlibrary_1_out_25, letterlibrary_1_out_26,
       letterlibrary_1_out_27, letterlibrary_1_out_28, letterlibrary_1_out_29, letterlibrary_1_out_30,
       letterlibrary_1_out_31, letterlibrary_1_out_32, letterlibrary_1_out_33, letterlibrary_1_out_34,
       letterlibrary_2_out_3, letterlibrary_2_out_4, letterlibrary_2_out_5, letterlibrary_2_out_6,
       letterlibrary_2_out_7, letterlibrary_2_out_8, letterlibrary_2_out_9, letterlibrary_2_out_10,
       letterlibrary_2_out_11, letterlibrary_2_out_12, letterlibrary_2_out_13, letterlibrary_2_out_14,
       letterlibrary_2_out_15, letterlibrary_2_out_16, letterlibrary_2_out_17, letterlibrary_2_out_18,
       letterlibrary_2_out_19, letterlibrary_2_out_20, letterlibrary_2_out_21, letterlibrary_2_out_22,
       letterlibrary_2_out_23, letterlibrary_2_out_24, letterlibrary_2_out_25, letterlibrary_2_out_26,
       letterlibrary_2_out_27, letterlibrary_2_out_28, letterlibrary_2_out_29, letterlibrary_2_out_30,
       letterlibrary_2_out_31, letterlibrary_2_out_32, letterlibrary_2_out_33, letterlibrary_2_out_34;

  // Register register_1: pin names not known; wires that end beside it: register_1_p1, CNT, CLK
  Clock L_d237f850 (.out(CLK));
  NationalStandardTransitionAreaCode nationalstandardtransitionareacode_1 (
    .L_e0d75744(nationalstandardtransitionareacode_1_l_e0d75744),
    .L_d0f54a78(nationalstandardtransitionareacode_1_l_d0f54a78), .GB2312(L_04ee53f0));
  Adder adder_1 (.a(8'h1), .b(CNT), .out(register_1_p1));  // open: cin, cout
  DotMatrix #(.dotshape("circle"), .inputtype("row"), .matrixcols(32), .matrixrows(32)) dotmatrix_1 (
    .row0(letterlibrary_1_out_3), .row1(letterlibrary_1_out_4), .row2(letterlibrary_1_out_5),
    .row3(letterlibrary_1_out_6), .row4(letterlibrary_1_out_7), .row5(letterlibrary_1_out_8),
    .row6(letterlibrary_1_out_9), .row7(letterlibrary_1_out_10), .row8(letterlibrary_1_out_11),
    .row9(letterlibrary_1_out_12), .row10(letterlibrary_1_out_13), .row11(letterlibrary_1_out_14),
    .row12(letterlibrary_1_out_15), .row13(letterlibrary_1_out_16), .row14(letterlibrary_1_out_17),
    .row15(letterlibrary_1_out_18), .row16(letterlibrary_1_out_19), .row17(letterlibrary_1_out_20),
    .row18(letterlibrary_1_out_21), .row19(letterlibrary_1_out_22), .row20(letterlibrary_1_out_23),
    .row21(letterlibrary_1_out_24), .row22(letterlibrary_1_out_25), .row23(letterlibrary_1_out_26),
    .row24(letterlibrary_1_out_27), .row25(letterlibrary_1_out_28), .row26(letterlibrary_1_out_29),
    .row27(letterlibrary_1_out_30), .row28(letterlibrary_1_out_31), .row29(letterlibrary_1_out_32),
    .row30(letterlibrary_1_out_33), .row31(letterlibrary_1_out_34));
  LetterLibrary letterlibrary_1 (
    .out_14(letterlibrary_1_out_14), .out_30(letterlibrary_1_out_30), .out_15(letterlibrary_1_out_15),
    .out_31(letterlibrary_1_out_31), .out_16(letterlibrary_1_out_16), .out_32(letterlibrary_1_out_32),
    .out_17(letterlibrary_1_out_17), .out_33(letterlibrary_1_out_33), .out_18(letterlibrary_1_out_18),
    .out_34(letterlibrary_1_out_34), .out_4(letterlibrary_1_out_4), .out_20(letterlibrary_1_out_20),
    .out_5(letterlibrary_1_out_5), .out_21(letterlibrary_1_out_21), .out_6(letterlibrary_1_out_6),
    .out_22(letterlibrary_1_out_22), .out_7(letterlibrary_1_out_7), .out_23(letterlibrary_1_out_23),
    .out_8(letterlibrary_1_out_8), .out_24(letterlibrary_1_out_24), .out_9(letterlibrary_1_out_9),
    .out_25(letterlibrary_1_out_25), .out_10(letterlibrary_1_out_10), .out_26(letterlibrary_1_out_26),
    .out_3(letterlibrary_1_out_3), .out_19(letterlibrary_1_out_19), .out_11(letterlibrary_1_out_11),
    .out_27(letterlibrary_1_out_27), .out_12(letterlibrary_1_out_12), .out_28(letterlibrary_1_out_28),
    .out_13(letterlibrary_1_out_13), .out_29(letterlibrary_1_out_29),
    .L_e0d75744(nationalstandardtransitionareacode_1_l_e0d75744),
    .L_d0f54a78(nationalstandardtransitionareacode_1_l_d0f54a78));
  ROM #(.dataWidth(16)) rom_1 (.addr(CNT), .data(L_04ee53f0));
  L_16_b4f519f1 l_16_b4f519f1_1 (
    .Dout16(l_16_b4f519f1_1_dout16), .L_Out_103436ad(l_16_b4f519f1_1_l_out_103436ad), .CLK(CLK),
    .L_In_e788f716(1'b1), .Din16(L_04ee53f0), .L_762d2466(clr2));  // open: L_stall_55967050
  L_00584185 l_00584185_1 (.L_ba8a574d(l_00584185_1_l_ba8a574d), .L_d11c89cc(l_16_b4f519f1_1_dout16));
  L_22_793ae84e l_22_793ae84e_1 (
    .Dout22(l_22_793ae84e_1_dout22), .L_Out_103436ad(l_22_793ae84e_1_l_out_103436ad), .CLK(CLK),
    .L_In_e788f716(l_16_b4f519f1_1_l_out_103436ad), .Din22(l_00584185_1_l_ba8a574d), .L_762d2466(clr3));  // open: L_stall_55967050
  L_22_9fb87853 l_22_9fb87853_1 (
    .L_d9787977(l_22_9fb87853_1_l_d9787977), .EDU(EDU), .CLK(CLK), .L_22_36bcc28c(l_22_793ae84e_1_dout22),
    .L_f486a1f2(2'b11), .L_745543a0(L_7d930fa3));  // open: L_d265d600
  LetterLibrary letterlibrary_2 (
    .out_14(letterlibrary_2_out_14), .out_30(letterlibrary_2_out_30), .out_15(letterlibrary_2_out_15),
    .out_31(letterlibrary_2_out_31), .out_16(letterlibrary_2_out_16), .out_32(letterlibrary_2_out_32),
    .out_17(letterlibrary_2_out_17), .out_33(letterlibrary_2_out_33), .out_18(letterlibrary_2_out_18),
    .out_34(letterlibrary_2_out_34), .out_4(letterlibrary_2_out_4), .out_20(letterlibrary_2_out_20),
    .out_5(letterlibrary_2_out_5), .out_21(letterlibrary_2_out_21), .out_6(letterlibrary_2_out_6),
    .out_22(letterlibrary_2_out_22), .out_7(letterlibrary_2_out_7), .out_23(letterlibrary_2_out_23),
    .out_8(letterlibrary_2_out_8), .out_24(letterlibrary_2_out_24), .out_9(letterlibrary_2_out_9),
    .out_25(letterlibrary_2_out_25), .out_10(letterlibrary_2_out_10), .out_26(letterlibrary_2_out_26),
    .out_3(letterlibrary_2_out_3), .out_19(letterlibrary_2_out_19), .out_11(letterlibrary_2_out_11),
    .out_27(letterlibrary_2_out_27), .out_12(letterlibrary_2_out_12), .out_28(letterlibrary_2_out_28),
    .out_13(letterlibrary_2_out_13), .out_29(letterlibrary_2_out_29),
    .L_e0d75744(nationalstandardtransitionareacode_2_l_e0d75744),
    .L_d0f54a78(nationalstandardtransitionareacode_2_l_d0f54a78));
  NationalStandardTransitionAreaCode nationalstandardtransitionareacode_2 (
    .L_e0d75744(nationalstandardtransitionareacode_2_l_e0d75744),
    .L_d0f54a78(nationalstandardtransitionareacode_2_l_d0f54a78), .GB2312(L_8cdface8));
  L_22_793ae84e l_22_793ae84e_2 (
    .Dout22(l_22_793ae84e_2_dout22), .L_Out_103436ad(l_22_793ae84e_2_l_out_103436ad), .CLK(CLK),
    .L_In_e788f716(l_22_793ae84e_1_l_out_103436ad), .Din22(l_22_9fb87853_1_l_d9787977), .L_762d2466(clr4));  // open: L_stall_55967050
  DotMatrix #(.dotshape("circle"), .inputtype("row"), .matrixcols(32), .matrixrows(32)) dotmatrix_2 (
    .row0(letterlibrary_2_out_3), .row1(letterlibrary_2_out_4), .row2(letterlibrary_2_out_5),
    .row3(letterlibrary_2_out_6), .row4(letterlibrary_2_out_7), .row5(letterlibrary_2_out_8),
    .row6(letterlibrary_2_out_9), .row7(letterlibrary_2_out_10), .row8(letterlibrary_2_out_11),
    .row9(letterlibrary_2_out_12), .row10(letterlibrary_2_out_13), .row11(letterlibrary_2_out_14),
    .row12(letterlibrary_2_out_15), .row13(letterlibrary_2_out_16), .row14(letterlibrary_2_out_17),
    .row15(letterlibrary_2_out_18), .row16(letterlibrary_2_out_19), .row17(letterlibrary_2_out_20),
    .row18(letterlibrary_2_out_21), .row19(letterlibrary_2_out_22), .row20(letterlibrary_2_out_23),
    .row21(letterlibrary_2_out_24), .row22(letterlibrary_2_out_25), .row23(letterlibrary_2_out_26),
    .row24(letterlibrary_2_out_27), .row25(letterlibrary_2_out_28), .row26(letterlibrary_2_out_29),
    .row27(letterlibrary_2_out_30), .row28(letterlibrary_2_out_31), .row29(letterlibrary_2_out_32),
    .row30(letterlibrary_2_out_33), .row31(letterlibrary_2_out_34));
  LED L_f242517a (.in(L_1err_a3df68ae));
  LED L_161fd229 (.in(L_2err_26a15d6f));
  LED L_68afa87c (.in(l_455c5dad_1_l_0_eb6a1b8d));
  L_455c5dad l_455c5dad_1 (
    .L_0_eb6a1b8d(l_455c5dad_1_l_0_eb6a1b8d), .L_1_ef5de30d(L_1err_a3df68ae), .L_2_d93bbbb2(L_2err_26a15d6f),
    .L_9904c55d(l_455c5dad_1_l_9904c55d), .L_ba8a574d(l_22_793ae84e_2_dout22));
  L_16_b4f519f1 l_16_b4f519f1_2 (
    .Dout16(L_8cdface8), .CLK(CLK), .L_In_e788f716(l_22_793ae84e_2_l_out_103436ad),
    .Din16(l_455c5dad_1_l_9904c55d), .L_stall_55967050(en5));  // open: L_Out_103436ad, L_762d2466
  // Probe on L_8cdface8

  // Notes on the sheet:
  //   海明码流水传输电路
  //   寄存器
  //   发送方
  //   汉字显示
  //   加法器
  //   GB2312
  //   1.取数阶段
  //   contents of rom_1 (hex, n*v repeats v):
  //   bbaa d6d0 bfc6 bcbc b4f3 d1a7 cac7 b9fa bcd2 bdcc d3fd b2bf d6b1 caf4 b5c4 c8ab b9fa d6d8 b5e3 b4f3
  //   d1a7 a3ac d3c9 d4ad bbaa d6d0 c0ed b9a4 b4f3 d1a7 a1a2 cdac bcc3 d2bd bfc6 b4f3 d1a7 a1a2 cee4 baba
  //   b3c7 cad0 bda8 c9e8 d1a7 d4ba d3da a3b2 a3b0 a3b0 a3b0 c4ea a3b5 d4c2 a3b2 a3b6 c8d5 bacf b2a2 b3c9
  //   c1a2 a3ac cac7 cad7 c5fa c1d0 c8eb b9fa bcd2 a1b0 a3b2 a3b1 a3b1 b9a4 b3cc a1b1 d6d8 b5e3 bda8 c9e8
  //   bacd b9fa bcd2 a1b0 a3b9 a3b8 a3b5 b9a4 b3cc a1b1 bda8 c9e8 b8df d0a3 d6ae d2bb a1a3 d1a7 d0a3 d0a3
  //   d4b0 d5bc b5d8 c6df c7a7 d3e0 c4b6 a3ac d4b0 c4da caf7 c4be b4d0 dcd7 a3ac b1cc b2dd c8e7 d2f0 a3ac
  //   bbb7 beb3 d3c5 d1c5 a3ac beb0 c9ab d0e3 c0f6 a3ac c2cc bbaf b8b2 b8c7 c2ca 3732 25a3 acb1 bbd3 fece
  //   aaa1 b0c9 adc1 d6ca bdb4 f3d1 a7a1 b1a1
  //   ~使能/Stall
  //   发送方在ROM预存了一段中文文字，通过计数器驱动电路每个时钟传输一个汉字
  //   同步清零
  //   用户实现了国标转区位码电路后，可在中间窗口观察发送方和接收方汉字显示是否一致以观察海明检错纠错性能
  //   数据状态：高电平有效
  //   2.编码阶段
  //   接收方
  //   汉字显示
  //   电路功能：采用流水方式进行数据编码传输，测试海明编码检错纠错能力，当出现2位错时，发送重传信号要求发送方重传，保证接收方按ROM中的地址顺序接受所有汉字
  //   3.传输阶段
  //   4.解码阶段
  //   此电路可帮助学生理解指令流水线工作原理，重传类似指令流水线中的分支指令
  //   5.显示阶段
  //   请将时钟频率调到8Hz
  //   Ctrl+ K启动电路自动仿真
  //   EDUCODER在线测试引脚
  //   请勿增删改引脚
endmodule

module L_CRC_1_691ca3c6 (
  input  [15:0] L_d11c89cc,
  input  [1:0] L_7e85a9f4
);

  wire clock_1_out, comparator_1_eq, l_crc_dc188f0d_1_l_0_eb6a1b8d, l_crc_dc188f0d_1_l_1_ef5de30d,
       l_crc_dc188f0d_1_l_2_d93bbbb2;
  wire [15:0] l_crc_dc188f0d_1_l_9904c55d;
  wire [21:0] l_22_9fb87853_1_l_d265d600, l_22_9fb87853_1_l_d9787977, l_crc_4439dc43_1_crc_5864b47a;

  // Probe on L_d11c89cc
  // Probe on l_crc_4439dc43_1_crc_5864b47a
  L_CRC_4439dc43 l_crc_4439dc43_1 (.CRC_5864b47a(l_crc_4439dc43_1_crc_5864b47a), .L_d11c89cc(L_d11c89cc));
  // Probe on l_crc_4439dc43_1_crc_5864b47a
  // Probe on l_22_9fb87853_1_l_d265d600
  Clock clock_1 (.out(clock_1_out));
  // Probe on l_22_9fb87853_1_l_d9787977
  L_22_9fb87853 l_22_9fb87853_1 (
    .L_d265d600(l_22_9fb87853_1_l_d265d600), .L_d9787977(l_22_9fb87853_1_l_d9787977), .CLK(clock_1_out),
    .L_22_36bcc28c(l_crc_4439dc43_1_crc_5864b47a), .L_f486a1f2(L_7e85a9f4));  // open: EDU, L_745543a0
  // Probe on l_22_9fb87853_1_l_d9787977
  LED L_f242517a (.in(l_crc_dc188f0d_1_l_1_ef5de30d));
  LED L_161fd229 (.in(l_crc_dc188f0d_1_l_2_d93bbbb2));
  LED OK (.in(l_crc_dc188f0d_1_l_0_eb6a1b8d));
  L_CRC_dc188f0d l_crc_dc188f0d_1 (
    .L_0_eb6a1b8d(l_crc_dc188f0d_1_l_0_eb6a1b8d), .L_1_ef5de30d(l_crc_dc188f0d_1_l_1_ef5de30d),
    .L_2_d93bbbb2(l_crc_dc188f0d_1_l_2_d93bbbb2), .L_9904c55d(l_crc_dc188f0d_1_l_9904c55d),
    .CRC_1f12ebce(l_22_9fb87853_1_l_d9787977));
  // Probe on l_crc_dc188f0d_1_l_9904c55d
  Comparator #(.width(16)) comparator_1 (
    .a(L_d11c89cc), .b(l_crc_dc188f0d_1_l_9904c55d), .eq(comparator_1_eq));  // open: gt, lt
  LED L_40aec5df (.in(comparator_1_eq));

  // Notes on the sheet:
  //   发送方
  //   Ctrl+T 驱动时钟触发随机干扰变化
  //   CRC编解码传输电路
  //   电路功能：测试CRC编解码电路正确性，仿真时设置加扰控制位和原始数据，按CTRL+T触发不同的干扰，检验编解码电路功能
  //   加扰控制00：不加扰  01:1位加扰 10:2位加扰 11：随机加扰
  //   接收方
endmodule

module L_CRC_2_5f638d8f (
  input  [1:0] L_7e85a9f4
);

  wire CLK, comparator_1_eq, l_crc_dc188f0d_1_l_0_eb6a1b8d, l_crc_dc188f0d_1_l_1_ef5de30d,
       l_crc_dc188f0d_1_l_2_d93bbbb2;
  wire [6:0] nationalstandardtransitionareacode_1_l_d0f54a78,
       nationalstandardtransitionareacode_1_l_e0d75744, nationalstandardtransitionareacode_2_l_d0f54a78,
       nationalstandardtransitionareacode_2_l_e0d75744;
  wire [7:0] counter_1_p2;
  wire [15:0] L_04ee53f0, L_8cdface8;
  wire [21:0] l_22_9fb87853_1_l_d265d600, l_22_9fb87853_1_l_d9787977, l_crc_4439dc43_1_crc_5864b47a;
  wire [31:0] letterlibrary_1_out_3, letterlibrary_1_out_4, letterlibrary_1_out_5, letterlibrary_1_out_6,
       letterlibrary_1_out_7, letterlibrary_1_out_8, letterlibrary_1_out_9, letterlibrary_1_out_10,
       letterlibrary_1_out_11, letterlibrary_1_out_12, letterlibrary_1_out_13, letterlibrary_1_out_14,
       letterlibrary_1_out_15, letterlibrary_1_out_16, letterlibrary_1_out_17, letterlibrary_1_out_18,
       letterlibrary_1_out_19, letterlibrary_1_out_20, letterlibrary_1_out_21, letterlibrary_1_out_22,
       letterlibrary_1_out_23, letterlibrary_1_out_24, letterlibrary_1_out_25, letterlibrary_1_out_26,
       letterlibrary_1_out_27, letterlibrary_1_out_28, letterlibrary_1_out_29, letterlibrary_1_out_30,
       letterlibrary_1_out_31, letterlibrary_1_out_32, letterlibrary_1_out_33, letterlibrary_1_out_34,
       letterlibrary_2_out_3, letterlibrary_2_out_4, letterlibrary_2_out_5, letterlibrary_2_out_6,
       letterlibrary_2_out_7, letterlibrary_2_out_8, letterlibrary_2_out_9, letterlibrary_2_out_10,
       letterlibrary_2_out_11, letterlibrary_2_out_12, letterlibrary_2_out_13, letterlibrary_2_out_14,
       letterlibrary_2_out_15, letterlibrary_2_out_16, letterlibrary_2_out_17, letterlibrary_2_out_18,
       letterlibrary_2_out_19, letterlibrary_2_out_20, letterlibrary_2_out_21, letterlibrary_2_out_22,
       letterlibrary_2_out_23, letterlibrary_2_out_24, letterlibrary_2_out_25, letterlibrary_2_out_26,
       letterlibrary_2_out_27, letterlibrary_2_out_28, letterlibrary_2_out_29, letterlibrary_2_out_30,
       letterlibrary_2_out_31, letterlibrary_2_out_32, letterlibrary_2_out_33, letterlibrary_2_out_34;

  // Counter counter_1: pin names not known; wires that end beside it: CLK, counter_1_p2
  Clock L_d237f850 (.out(CLK));
  NationalStandardTransitionAreaCode nationalstandardtransitionareacode_1 (
    .L_e0d75744(nationalstandardtransitionareacode_1_l_e0d75744),
    .L_d0f54a78(nationalstandardtransitionareacode_1_l_d0f54a78), .GB2312(L_04ee53f0));
  DotMatrix #(.dotshape("circle"), .inputtype("row"), .matrixcols(32), .matrixrows(32)) dotmatrix_1 (
    .row0(letterlibrary_1_out_3), .row1(letterlibrary_1_out_4), .row2(letterlibrary_1_out_5),
    .row3(letterlibrary_1_out_6), .row4(letterlibrary_1_out_7), .row5(letterlibrary_1_out_8),
    .row6(letterlibrary_1_out_9), .row7(letterlibrary_1_out_10), .row8(letterlibrary_1_out_11),
    .row9(letterlibrary_1_out_12), .row10(letterlibrary_1_out_13), .row11(letterlibrary_1_out_14),
    .row12(letterlibrary_1_out_15), .row13(letterlibrary_1_out_16), .row14(letterlibrary_1_out_17),
    .row15(letterlibrary_1_out_18), .row16(letterlibrary_1_out_19), .row17(letterlibrary_1_out_20),
    .row18(letterlibrary_1_out_21), .row19(letterlibrary_1_out_22), .row20(letterlibrary_1_out_23),
    .row21(letterlibrary_1_out_24), .row22(letterlibrary_1_out_25), .row23(letterlibrary_1_out_26),
    .row24(letterlibrary_1_out_27), .row25(letterlibrary_1_out_28), .row26(letterlibrary_1_out_29),
    .row27(letterlibrary_1_out_30), .row28(letterlibrary_1_out_31), .row29(letterlibrary_1_out_32),
    .row30(letterlibrary_1_out_33), .row31(letterlibrary_1_out_34));
  LetterLibrary letterlibrary_1 (
    .out_14(letterlibrary_1_out_14), .out_30(letterlibrary_1_out_30), .out_15(letterlibrary_1_out_15),
    .out_31(letterlibrary_1_out_31), .out_16(letterlibrary_1_out_16), .out_32(letterlibrary_1_out_32),
    .out_17(letterlibrary_1_out_17), .out_33(letterlibrary_1_out_33), .out_18(letterlibrary_1_out_18),
    .out_34(letterlibrary_1_out_34), .out_4(letterlibrary_1_out_4), .out_20(letterlibrary_1_out_20),
    .out_5(letterlibrary_1_out_5), .out_21(letterlibrary_1_out_21), .out_6(letterlibrary_1_out_6),
    .out_22(letterlibrary_1_out_22), .out_7(letterlibrary_1_out_7), .out_23(letterlibrary_1_out_23),
    .out_8(letterlibrary_1_out_8), .out_24(letterlibrary_1_out_24), .out_9(letterlibrary_1_out_9),
    .out_25(letterlibrary_1_out_25), .out_10(letterlibrary_1_out_10), .out_26(letterlibrary_1_out_26),
    .out_3(letterlibrary_1_out_3), .out_19(letterlibrary_1_out_19), .out_11(letterlibrary_1_out_11),
    .out_27(letterlibrary_1_out_27), .out_12(letterlibrary_1_out_12), .out_28(letterlibrary_1_out_28),
    .out_13(letterlibrary_1_out_13), .out_29(letterlibrary_1_out_29),
    .L_e0d75744(nationalstandardtransitionareacode_1_l_e0d75744),
    .L_d0f54a78(nationalstandardtransitionareacode_1_l_d0f54a78));
  ROM #(.dataWidth(16)) rom_1 (.addr(counter_1_p2), .data(L_04ee53f0));
  // Probe on L_04ee53f0
  // Probe on l_crc_4439dc43_1_crc_5864b47a
  L_CRC_4439dc43 l_crc_4439dc43_1 (.CRC_5864b47a(l_crc_4439dc43_1_crc_5864b47a), .L_d11c89cc(L_04ee53f0));
  // Probe on l_crc_4439dc43_1_crc_5864b47a
  // Probe on l_22_9fb87853_1_l_d265d600
  L_22_9fb87853 l_22_9fb87853_1 (
    .L_d265d600(l_22_9fb87853_1_l_d265d600), .L_d9787977(l_22_9fb87853_1_l_d9787977), .CLK(CLK),
    .L_22_36bcc28c(l_crc_4439dc43_1_crc_5864b47a), .L_f486a1f2(L_7e85a9f4));  // open: EDU, L_745543a0
  NationalStandardTransitionAreaCode nationalstandardtransitionareacode_2 (
    .L_e0d75744(nationalstandardtransitionareacode_2_l_e0d75744),
    .L_d0f54a78(nationalstandardtransitionareacode_2_l_d0f54a78), .GB2312(L_8cdface8));
  // Probe on l_22_9fb87853_1_l_d9787977
  // Probe on l_22_9fb87853_1_l_d9787977
  LetterLibrary letterlibrary_2 (
    .out_14(letterlibrary_2_out_14), .out_30(letterlibrary_2_out_30), .out_15(letterlibrary_2_out_15),
    .out_31(letterlibrary_2_out_31), .out_16(letterlibrary_2_out_16), .out_32(letterlibrary_2_out_32),
    .out_17(letterlibrary_2_out_17), .out_33(letterlibrary_2_out_33), .out_18(letterlibrary_2_out_18),
    .out_34(letterlibrary_2_out_34), .out_4(letterlibrary_2_out_4), .out_20(letterlibrary_2_out_20),
    .out_5(letterlibrary_2_out_5), .out_21(letterlibrary_2_out_21), .out_6(letterlibrary_2_out_6),
    .out_22(letterlibrary_2_out_22), .out_7(letterlibrary_2_out_7), .out_23(letterlibrary_2_out_23),
    .out_8(letterlibrary_2_out_8), .out_24(letterlibrary_2_out_24), .out_9(letterlibrary_2_out_9),
    .out_25(letterlibrary_2_out_25), .out_10(letterlibrary_2_out_10), .out_26(letterlibrary_2_out_26),
    .out_3(letterlibrary_2_out_3), .out_19(letterlibrary_2_out_19), .out_11(letterlibrary_2_out_11),
    .out_27(letterlibrary_2_out_27), .out_12(letterlibrary_2_out_12), .out_28(letterlibrary_2_out_28),
    .out_13(letterlibrary_2_out_13), .out_29(letterlibrary_2_out_29),
    .L_e0d75744(nationalstandardtransitionareacode_2_l_e0d75744),
    .L_d0f54a78(nationalstandardtransitionareacode_2_l_d0f54a78));
  LED L_f242517a (.in(l_crc_dc188f0d_1_l_1_ef5de30d));
  LED L_161fd229 (.in(l_crc_dc188f0d_1_l_2_d93bbbb2));
  LED L_68afa87c (.in(l_crc_dc188f0d_1_l_0_eb6a1b8d));
  DotMatrix #(.dotshape("circle"), .inputtype("row"), .matrixcols(32), .matrixrows(32)) dotmatrix_2 (
    .row0(letterlibrary_2_out_3), .row1(letterlibrary_2_out_4), .row2(letterlibrary_2_out_5),
    .row3(letterlibrary_2_out_6), .row4(letterlibrary_2_out_7), .row5(letterlibrary_2_out_8),
    .row6(letterlibrary_2_out_9), .row7(letterlibrary_2_out_10), .row8(letterlibrary_2_out_11),
    .row9(letterlibrary_2_out_12), .row10(letterlibrary_2_out_13), .row11(letterlibrary_2_out_14),
    .row12(letterlibrary_2_out_15), .row13(letterlibrary_2_out_16), .row14(letterlibrary_2_out_17),
    .row15(letterlibrary_2_out_18), .row16(letterlibrary_2_out_19), .row17(letterlibrary_2_out_20),
    .row18(letterlibrary_2_out_21), .row19(letterlibrary_2_out_22), .row20(letterlibrary_2_out_23),
    .row21(letterlibrary_2_out_24), .row22(letterlibrary_2_out_25), .row23(letterlibrary_2_out_26),
    .row24(letterlibrary_2_out_27), .row25(letterlibrary_2_out_28), .row26(letterlibrary_2_out_29),
    .row27(letterlibrary_2_out_30), .row28(letterlibrary_2_out_31), .row29(letterlibrary_2_out_32),
    .row30(letterlibrary_2_out_33), .row31(letterlibrary_2_out_34));
  L_CRC_dc188f0d l_crc_dc188f0d_1 (
    .L_0_eb6a1b8d(l_crc_dc188f0d_1_l_0_eb6a1b8d), .L_1_ef5de30d(l_crc_dc188f0d_1_l_1_ef5de30d),
    .L_2_d93bbbb2(l_crc_dc188f0d_1_l_2_d93bbbb2), .L_9904c55d(L_8cdface8),
    .CRC_1f12ebce(l_22_9fb87853_1_l_d9787977));
  // Probe on L_8cdface8
  Comparator #(.width(16)) comparator_1 (.a(L_04ee53f0), .b(L_8cdface8), .eq(comparator_1_eq));  // open: gt, lt
  LED L_40aec5df (.in(comparator_1_eq));

  // Notes on the sheet:
  //   发送方
  //   计数器
  //   发送方
  //   汉字显示
  //   GB2312
  //   contents of rom_1 (hex, n*v repeats v):
  //   bbaa d6d0 bfc6 bcbc b4f3 d1a7 cac7 b9fa bcd2 bdcc d3fd b2bf d6b1 caf4 b5c4 c8ab b9fa d6d8 b5e3 b4f3
  //   d1a7 a3ac d3c9 d4ad bbaa d6d0 c0ed b9a4 b4f3 d1a7 a1a2 cdac bcc3 d2bd bfc6 b4f3 d1a7 a1a2 cee4 baba
  //   b3c7 cad0 bda8 c9e8 d1a7 d4ba d3da a3b2 a3b0 a3b0 a3b0 c4ea a3b5 d4c2 a3b2 a3b6 c8d5 bacf b2a2 b3c9
  //   c1a2 a3ac cac7 cad7 c5fa c1d0 c8eb b9fa bcd2 a1b0 a3b2 a3b1 a3b1 b9a4 b3cc a1b1 d6d8 b5e3 bda8 c9e8
  //   bacd b9fa bcd2 a1b0 a3b9 a3b8 a3b5 b9a4 b3cc a1b1 bda8 c9e8 b8df d0a3 d6ae d2bb a1a3 d1a7 d0a3 d0a3
  //   d4b0 d5bc b5d8 c6df c7a7 d3e0 c4b6 a3ac d4b0 c4da caf7 c4be b4d0 dcd7 a3ac b1cc b2dd c8e7 d2f0 a3ac
  //   bbb7 beb3 d3c5 d1c5 a3ac beb0 c9ab d0e3 c0f6 a3ac c2cc bbaf b8b2 b8c7 c2ca 3732 25a3 acb1 bbd3 fece
  //   aaa1 b0c9 adc1 d6ca bdb4 f3d1 a7a1 b1a1
  //   Ctrl+T 驱动时钟触发随机干扰变化
  //   电路功能：测试CRC编解码电路正确性，仿真时设置加扰控制位和原始数据，按CTRL+T触发不同的干扰，检验编解码电路功能
  //   发送方在ROM预存了一段中文文字，通过计数器驱动电路每个时钟传输一个汉字到接收方
  //   用户实现了国标转区位码电路后，可在中间窗口观察发送方和接收方汉字显示是否一致以观察海明检错纠错性能
  //   CRC编解码传输电路
  //   接收方
  //   汉字显示
  //   Ctrl+T 驱动时钟触发随机干扰变化
  //   加扰控制00：不加扰  01:1位加扰 10:2位加扰 11：随机加扰
  //   加扰控制00：不加扰  01:1位加扰 10:2位加扰 11：随机加扰
  //   接收方
  //   请将时钟频率调到8Hz
endmodule

// CRC
module L_CRC_e0b66718 (
  input  L_7d930fa3,
  input  EDU,
  output L_1err_a3df68ae,
  output L_2err_26a15d6f,
  output clr2,
  output clr3,
  output clr4,
  output en5
);

  wire CLK, l_16_b4f519f1_1_l_out_103436ad, l_22_793ae84e_1_l_out_103436ad, l_22_793ae84e_2_l_out_103436ad,
       l_crc_dc188f0d_1_l_0_eb6a1b8d;
  wire [6:0] nationalstandardtransitionareacode_1_l_d0f54a78,
       nationalstandardtransitionareacode_1_l_e0d75744, nationalstandardtransitionareacode_2_l_d0f54a78,
       nationalstandardtransitionareacode_2_l_e0d75744;
  wire [7:0] CNT, register_1_p1;
  wire [15:0] L_04ee53f0, L_8cdface8, l_16_b4f519f1_1_dout16, l_crc_dc188f0d_1_l_9904c55d;
  wire [21:0] l_22_9fb87853_1_l_d9787977, l_22_793ae84e_1_dout22, l_22_793ae84e_2_dout22,
       l_crc_4439dc43_1_crc_5864b47a;
  wire [31:0] letterlibrary_1_out_3, letterlibrary_1_out_4, letterlibrary_1_out_5, letterlibrary_1_out_6,
       letterlibrary_1_out_7, letterlibrary_1_out_8, letterlibrary_1_out_9, letterlibrary_1_out_10,
       letterlibrary_1_out_11, letterlibrary_1_out_12, letterlibrary_1_out_13, letterlibrary_1_out_14,
       letterlibrary_1_out_15, letterlibrary_1_out_16, letterlibrary_1_out_17, letterlibrary_1_out_18,
       letterlibrary_1_out_19, letterlibrary_1_out_20, letterlibrary_1_out_21, letterlibrary_1_out_22,
       letterlibrary_1_out_23, letterlibrary_1_out_24, letterlibrary_1_out_25, letterlibrary_1_out_26,
       letterlibrary_1_out_27, letterlibrary_1_out_28, letterlibrary_1_out_29, letterlibrary_1_out_30,
       letterlibrary_1_out_31, letterlibrary_1_out_32, letterlibrary_1_out_33, letterlibrary_1_out_34,
       letterlibrary_2_out_3, letterlibrary_2_out_4, letterlibrary_2_out_5, letterlibrary_2_out_6,
       letterlibrary_2_out_7, letterlibrary_2_out_8, letterlibrary_2_out_9, letterlibrary_2_out_10,
       letterlibrary_2_out_11, letterlibrary_2_out_12, letterlibrary_2_out_13, letterlibrary_2_out_14,
       letterlibrary_2_out_15, letterlibrary_2_out_16, letterlibrary_2_out_17, letterlibrary_2_out_18,
       letterlibrary_2_out_19, letterlibrary_2_out_20, letterlibrary_2_out_21, letterlibrary_2_out_22,
       letterlibrary_2_out_23, letterlibrary_2_out_24, letterlibrary_2_out_25, letterlibrary_2_out_26,
       letterlibrary_2_out_27, letterlibrary_2_out_28, letterlibrary_2_out_29, letterlibrary_2_out_30,
       letterlibrary_2_out_31, letterlibrary_2_out_32, letterlibrary_2_out_33, letterlibrary_2_out_34;

  // Register register_1: pin names not known; wires that end beside it: register_1_p1, CNT, CLK
  Clock L_d237f850 (.out(CLK));
  NationalStandardTransitionAreaCode nationalstandardtransitionareacode_1 (
    .L_e0d75744(nationalstandardtransitionareacode_1_l_e0d75744),
    .L_d0f54a78(nationalstandardtransitionareacode_1_l_d0f54a78), .GB2312(L_04ee53f0));
  Adder adder_1 (.a(8'h1), .b(CNT), .out(register_1_p1));  // open: cin, cout
  DotMatrix #(.dotshape("circle"), .inputtype("row"), .matrixcols(32), .matrixrows(32)) dotmatrix_1 (
    .row0(letterlibrary_1_out_3), .row1(letterlibrary_1_out_4), .row2(letterlibrary_1_out_5),
    .row3(letterlibrary_1_out_6), .row4(letterlibrary_1_out_7), .row5(letterlibrary_1_out_8),
    .row6(letterlibrary_1_out_9), .row7(letterlibrary_1_out_10), .row8(letterlibrary_1_out_11),
    .row9(letterlibrary_1_out_12), .row10(letterlibrary_1_out_13), .row11(letterlibrary_1_out_14),
    .row12(letterlibrary_1_out_15), .row13(letterlibrary_1_out_16), .row14(letterlibrary_1_out_17),
    .row15(letterlibrary_1_out_18), .row16(letterlibrary_1_out_19), .row17(letterlibrary_1_out_20),
    .row18(letterlibrary_1_out_21), .row19(letterlibrary_1_out_22), .row20(letterlibrary_1_out_23),
    .row21(letterlibrary_1_out_24), .row22(letterlibrary_1_out_25), .row23(letterlibrary_1_out_26),
    .row24(letterlibrary_1_out_27), .row25(letterlibrary_1_out_28), .row26(letterlibrary_1_out_29),
    .row27(letterlibrary_1_out_30), .row28(letterlibrary_1_out_31), .row29(letterlibrary_1_out_32),
    .row30(letterlibrary_1_out_33), .row31(letterlibrary_1_out_34));
  LetterLibrary letterlibrary_1 (
    .out_14(letterlibrary_1_out_14), .out_30(letterlibrary_1_out_30), .out_15(letterlibrary_1_out_15),
    .out_31(letterlibrary_1_out_31), .out_16(letterlibrary_1_out_16), .out_32(letterlibrary_1_out_32),
    .out_17(letterlibrary_1_out_17), .out_33(letterlibrary_1_out_33), .out_18(letterlibrary_1_out_18),
    .out_34(letterlibrary_1_out_34), .out_4(letterlibrary_1_out_4), .out_20(letterlibrary_1_out_20),
    .out_5(letterlibrary_1_out_5), .out_21(letterlibrary_1_out_21), .out_6(letterlibrary_1_out_6),
    .out_22(letterlibrary_1_out_22), .out_7(letterlibrary_1_out_7), .out_23(letterlibrary_1_out_23),
    .out_8(letterlibrary_1_out_8), .out_24(letterlibrary_1_out_24), .out_9(letterlibrary_1_out_9),
    .out_25(letterlibrary_1_out_25), .out_10(letterlibrary_1_out_10), .out_26(letterlibrary_1_out_26),
    .out_3(letterlibrary_1_out_3), .out_19(letterlibrary_1_out_19), .out_11(letterlibrary_1_out_11),
    .out_27(letterlibrary_1_out_27), .out_12(letterlibrary_1_out_12), .out_28(letterlibrary_1_out_28),
    .out_13(letterlibrary_1_out_13), .out_29(letterlibrary_1_out_29),
    .L_e0d75744(nationalstandardtransitionareacode_1_l_e0d75744),
    .L_d0f54a78(nationalstandardtransitionareacode_1_l_d0f54a78));
  ROM #(.dataWidth(16)) rom_1 (.addr(CNT), .data(L_04ee53f0));
  L_16_b4f519f1 l_16_b4f519f1_1 (
    .Dout16(l_16_b4f519f1_1_dout16), .L_Out_103436ad(l_16_b4f519f1_1_l_out_103436ad), .CLK(CLK),
    .L_In_e788f716(1'b1), .Din16(L_04ee53f0), .L_762d2466(clr2));  // open: L_stall_55967050
  L_CRC_4439dc43 l_crc_4439dc43_1 (.CRC_5864b47a(l_crc_4439dc43_1_crc_5864b47a), .L_d11c89cc(l_16_b4f519f1_1_dout16));
  L_22_793ae84e l_22_793ae84e_1 (
    .Dout22(l_22_793ae84e_1_dout22), .L_Out_103436ad(l_22_793ae84e_1_l_out_103436ad), .CLK(CLK),
    .L_In_e788f716(l_16_b4f519f1_1_l_out_103436ad), .Din22(l_crc_4439dc43_1_crc_5864b47a), .L_762d2466(clr3));  // open: L_stall_55967050
  L_22_9fb87853 l_22_9fb87853_1 (
    .L_d9787977(l_22_9fb87853_1_l_d9787977), .EDU(EDU), .CLK(CLK), .L_22_36bcc28c(l_22_793ae84e_1_dout22),
    .L_f486a1f2(2'b11), .L_745543a0(L_7d930fa3));  // open: L_d265d600
  LetterLibrary letterlibrary_2 (
    .out_14(letterlibrary_2_out_14), .out_30(letterlibrary_2_out_30), .out_15(letterlibrary_2_out_15),
    .out_31(letterlibrary_2_out_31), .out_16(letterlibrary_2_out_16), .out_32(letterlibrary_2_out_32),
    .out_17(letterlibrary_2_out_17), .out_33(letterlibrary_2_out_33), .out_18(letterlibrary_2_out_18),
    .out_34(letterlibrary_2_out_34), .out_4(letterlibrary_2_out_4), .out_20(letterlibrary_2_out_20),
    .out_5(letterlibrary_2_out_5), .out_21(letterlibrary_2_out_21), .out_6(letterlibrary_2_out_6),
    .out_22(letterlibrary_2_out_22), .out_7(letterlibrary_2_out_7), .out_23(letterlibrary_2_out_23),
    .out_8(letterlibrary_2_out_8), .out_24(letterlibrary_2_out_24), .out_9(letterlibrary_2_out_9),
    .out_25(letterlibrary_2_out_25), .out_10(letterlibrary_2_out_10), .out_26(letterlibrary_2_out_26),
    .out_3(letterlibrary_2_out_3), .out_19(letterlibrary_2_out_19), .out_11(letterlibrary_2_out_11),
    .out_27(letterlibrary_2_out_27), .out_12(letterlibrary_2_out_12), .out_28(letterlibrary_2_out_28),
    .out_13(letterlibrary_2_out_13), .out_29(letterlibrary_2_out_29),
    .L_e0d75744(nationalstandardtransitionareacode_2_l_e0d75744),
    .L_d0f54a78(nationalstandardtransitionareacode_2_l_d0f54a78));
  NationalStandardTransitionAreaCode nationalstandardtransitionareacode_2 (
    .L_e0d75744(nationalstandardtransitionareacode_2_l_e0d75744),
    .L_d0f54a78(nationalstandardtransitionareacode_2_l_d0f54a78), .GB2312(L_8cdface8));
  L_22_793ae84e l_22_793ae84e_2 (
    .Dout22(l_22_793ae84e_2_dout22), .L_Out_103436ad(l_22_793ae84e_2_l_out_103436ad), .CLK(CLK),
    .L_In_e788f716(l_22_793ae84e_1_l_out_103436ad), .Din22(l_22_9fb87853_1_l_d9787977), .L_762d2466(clr4));  // open: L_stall_55967050
  DotMatrix #(.dotshape("circle"), .inputtype("row"), .matrixcols(32), .matrixrows(32)) dotmatrix_2 (
    .row0(letterlibrary_2_out_3), .row1(letterlibrary_2_out_4), .row2(letterlibrary_2_out_5),
    .row3(letterlibrary_2_out_6), .row4(letterlibrary_2_out_7), .row5(letterlibrary_2_out_8),
    .row6(letterlibrary_2_out_9), .row7(letterlibrary_2_out_10), .row8(letterlibrary_2_out_11),
    .row9(letterlibrary_2_out_12), .row10(letterlibrary_2_out_13), .row11(letterlibrary_2_out_14),
    .row12(letterlibrary_2_out_15), .row13(letterlibrary_2_out_16), .row14(letterlibrary_2_out_17),
    .row15(letterlibrary_2_out_18), .row16(letterlibrary_2_out_19), .row17(letterlibrary_2_out_20),
    .row18(letterlibrary_2_out_21), .row19(letterlibrary_2_out_22), .row20(letterlibrary_2_out_23),
    .row21(letterlibrary_2_out_24), .row22(letterlibrary_2_out_25), .row23(letterlibrary_2_out_26),
    .row24(letterlibrary_2_out_27), .row25(letterlibrary_2_out_28), .row26(letterlibrary_2_out_29),
    .row27(letterlibrary_2_out_30), .row28(letterlibrary_2_out_31), .row29(letterlibrary_2_out_32),
    .row30(letterlibrary_2_out_33), .row31(letterlibrary_2_out_34));
  LED L_f242517a (.in(L_1err_a3df68ae));
  LED L_161fd229 (.in(L_2err_26a15d6f));
  LED L_68afa87c (.in(l_crc_dc188f0d_1_l_0_eb6a1b8d));
  L_CRC_dc188f0d l_crc_dc188f0d_1 (
    .L_0_eb6a1b8d(l_crc_dc188f0d_1_l_0_eb6a1b8d), .L_1_ef5de30d(L_1err_a3df68ae),
    .L_2_d93bbbb2(L_2err_26a15d6f), .L_9904c55d(l_crc_dc188f0d_1_l_9904c55d),
    .CRC_1f12ebce(l_22_793ae84e_2_dout22));
  L_16_b4f519f1 l_16_b4f519f1_2 (
    .Dout16(L_8cdface8), .CLK(CLK), .L_In_e788f716(l_22_793ae84e_2_l_out_103436ad),
    .Din16(l_crc_dc188f0d_1_l_9904c55d), .L_stall_55967050(en5));  // open: L_Out_103436ad, L_762d2466
  // Probe on L_8cdface8

  // Notes on the sheet:
  //   CRC编码流水传输电路
  //   寄存器
  //   发送方
  //   汉字显示
  //   加法器
  //   GB2312
  //   1.取数阶段
  //   contents of rom_1 (hex, n*v repeats v):
  //   bbaa d6d0 bfc6 bcbc b4f3 d1a7 cac7 b9fa bcd2 bdcc d3fd b2bf d6b1 caf4 b5c4 c8ab b9fa d6d8 b5e3 b4f3
  //   d1a7 a3ac d3c9 d4ad bbaa d6d0 c0ed b9a4 b4f3 d1a7 a1a2 cdac bcc3 d2bd bfc6 b4f3 d1a7 a1a2 cee4 baba
  //   b3c7 cad0 bda8 c9e8 d1a7 d4ba d3da a3b2 a3b0 a3b0 a3b0 c4ea a3b5 d4c2 a3b2 a3b6 c8d5 bacf b2a2 b3c9
  //   c1a2 a3ac cac7 cad7 c5fa c1d0 c8eb b9fa bcd2 a1b0 a3b2 a3b1 a3b1 b9a4 b3cc a1b1 d6d8 b5e3 bda8 c9e8
  //   bacd b9fa bcd2 a1b0 a3b9 a3b8 a3b5 b9a4 b3cc a1b1 bda8 c9e8 b8df d0a3 d6ae d2bb a1a3 d1a7 d0a3 d0a3
  //   d4b0 d5bc b5d8 c6df c7a7 d3e0 c4b6 a3ac d4b0 c4da caf7 c4be b4d0 dcd7 a3ac b1cc b2dd c8e7 d2f0 a3ac
  //   bbb7 beb3 d3c5 d1c5 a3ac beb0 c9ab d0e3 c0f6 a3ac c2cc bbaf b8b2 b8c7 c2ca 3732 25a3 acb1 bbd3 fece
  //   aaa1 b0c9 adc1 d6ca bdb4 f3d1 a7a1 b1a1
  //   ~使能/Stall
  //   发送方在ROM预存了一段中文文字，通过计数器驱动电路每个时钟传输一个汉字
  //   同步清零
  //   用户实现了国标转区位码电路后，可在中间窗口观察发送方和接收方汉字显示是否一致以观察海明检错纠错性能
  //   数据状态：高电平有效
  //   2.编码阶段
  //   接收方
  //   汉字显示
  //   电路功能：采用流水方式进行数据编码传输，测试海明编码检错纠错能力，当出现2位错时，发送重传信号要求发送方重传，保证接收方按ROM中的地址顺序接受所有汉字
  //   3.传输阶段
  //   4.解码阶段
  //   此电路可帮助学生理解指令流水线工作原理，重传类似指令流水线中的分支指令
  //   5.显示阶段
  //   请将时钟频率调到8Hz
  //   Ctrl+ K启动电路自动仿真
  //   EDUCODER在线测试引脚
  //   请勿增删改引脚
endmodule

// 随机干扰
module L_22_9fb87853 (
  input  CLK,
  input  [21:0] L_22_36bcc28c,
  input  EDU,
  input  [1:0] L_f486a1f2,
  input  L_745543a0,
  output [21:0] L_d265d600,
  output [21:0] L_d9787977
);

  wire comparator_1_eq, random_3_p3;
  wire [1:0] EDUerr, multiplexer_3_out, random_3_p2;
  wire [3:0] L_fb47bba6_p2, L_fb47bba6_p3, random_1_p3;
  wire [7:0] counter_1_p2;
  wire [15:0] L_1_A_e8e70e38;
  wire [21:0] L_1_6eefe46d, L_2_32261194, L_3_d566a9e0, L_a1f58df6, multiplexer_1_out, multiplexer_5_out,
       shifter_1_out;
  wire [21:6] L_1_B_43df9c35, L_1_C_6ae7f598;

  Decoder #(.disabled("Z"), .enable("false"), .select(4)) decoder_1 (
    .out0(L_1_A_e8e70e38[0]), .out1(L_1_A_e8e70e38[1]), .out2(L_1_A_e8e70e38[2]), .out3(L_1_A_e8e70e38[3]),
    .out4(L_1_A_e8e70e38[4]), .out5(L_1_A_e8e70e38[5]), .out6(L_1_A_e8e70e38[6]), .out7(L_1_A_e8e70e38[7]),
    .out8(L_1_A_e8e70e38[8]), .out9(L_1_A_e8e70e38[9]), .out10(L_1_A_e8e70e38[10]),
    .out11(L_1_A_e8e70e38[11]), .out12(L_1_A_e8e70e38[12]), .out13(L_1_A_e8e70e38[13]),
    .out14(L_1_A_e8e70e38[14]), .out15(L_1_A_e8e70e38[15]), .sel(L_fb47bba6_p2));
  // Random #(.width(4)) L_fb47bba6: pin names not known; wires that end beside it: CLK, L_fb47bba6_p2, L_fb47bba6_p3
  Decoder #(.disabled("Z"), .enable("false"), .select(4)) decoder_2 (
    .out0(L_1_B_43df9c35[6]), .out1(L_1_B_43df9c35[7]), .out2(L_1_B_43df9c35[8]), .out3(L_1_B_43df9c35[9]),
    .out4(L_1_B_43df9c35[10]), .out5(L_1_B_43df9c35[11]), .out6(L_1_B_43df9c35[12]),
    .out7(L_1_B_43df9c35[13]), .out8(L_1_B_43df9c35[14]), .out9(L_1_B_43df9c35[15]),
    .out10(L_1_B_43df9c35[16]), .out11(L_1_B_43df9c35[17]), .out12(L_1_B_43df9c35[18]),
    .out13(L_1_B_43df9c35[19]), .out14(L_1_B_43df9c35[20]), .out15(L_1_B_43df9c35[21]), .sel(L_fb47bba6_p3));
  // Random #(.seed(18), .width(4)) random_1: pin names not known; wires that end beside it: CLK, L_fb47bba6_p3, random_1_p3
  Random #(.seed(3), .width(4)) random_2 ();  // open: clr, next, clk, out
  // Random #(.seed(21), .width(2)) random_3: pin names not known; wires that end beside it: CLK, random_3_p2, random_3_p3
  // Random #(.seed(31), .width(1)) random_4: pin names not known; wires that end beside it: random_3_p3, L_f486a1f2
  Decoder #(.disabled("Z"), .enable("false"), .select(4)) decoder_3 (
    .out0(L_1_C_6ae7f598[6]), .out1(L_1_C_6ae7f598[7]), .out2(L_1_C_6ae7f598[8]), .out3(L_1_C_6ae7f598[9]),
    .out4(L_1_C_6ae7f598[10]), .out5(L_1_C_6ae7f598[11]), .out6(L_1_C_6ae7f598[12]),
    .out7(L_1_C_6ae7f598[13]), .out8(L_1_C_6ae7f598[14]), .out9(L_1_C_6ae7f598[15]),
    .out10(L_1_C_6ae7f598[16]), .out11(L_1_C_6ae7f598[17]), .out12(L_1_C_6ae7f598[18]),
    .out13(L_1_C_6ae7f598[19]), .out14(L_1_C_6ae7f598[20]), .out15(L_1_C_6ae7f598[21]), .sel(random_1_p3));
  Pull_Resistor #(.pull(1)) pull_resistor_1 (.node(L_f486a1f2));
  Pull_Resistor pull_resistor_2 (.node(L_745543a0));
  Multiplexer #(.disabled("Z"), .enable("false"), .width(22)) multiplexer_1 (
    .in0({L_1_B_43df9c35, {6{1'b0}}}), .in1(L_3_d566a9e0), .out(multiplexer_1_out), .sel(L_745543a0));
  Multiplexer #(.disabled("Z"), .enable("false"), .select(2), .width(22)) multiplexer_2 (
    .in0({22{1'b0}}), .in1({{6{1'b0}}, L_1_A_e8e70e38}), .in2(L_2_32261194), .in3(multiplexer_1_out),
    .out(L_a1f58df6), .sel(random_3_p2));
  Pull_Resistor pull_resistor_3 (.node(EDU));
  Multiplexer #(.disabled("Z"), .enable("false"), .width(2)) multiplexer_3 (
    .in0(L_f486a1f2), .in1(EDUerr), .out(multiplexer_3_out), .sel(EDU));
  Shifter #(.shift("rl"), .width(22)) shifter_1 (
    .in({{6{1'b0}}, L_1_A_e8e70e38}), .\dist (5'b00001), .out(shifter_1_out));
  Comparator #(.mode("unsigned"), .width(22)) comparator_1 (
    .a({{6{1'b0}}, L_1_A_e8e70e38}), .b({L_1_B_43df9c35, {6{1'b0}}}), .eq(comparator_1_eq));  // open: gt, lt
  Multiplexer #(.disabled("Z"), .enable("false"), .select(2), .width(22)) multiplexer_4 (
    .in0({22{1'b0}}), .in1(L_1_6eefe46d), .in2(L_2_32261194), .in3(L_a1f58df6), .out(L_d265d600),
    .sel(multiplexer_3_out));
  Multiplexer #(.disabled("Z"), .enable("false"), .width(22)) multiplexer_5 (
    .in0({{6{1'b0}}, L_1_A_e8e70e38}), .in1(shifter_1_out), .out(multiplexer_5_out), .sel(comparator_1_eq));
  // Counter counter_1: pin names not known; wires that end beside it: CLK, counter_1_p2
  assign L_2_32261194 = multiplexer_5_out ^ {L_1_B_43df9c35, {6{1'b0}}};  // XOR_Gate xor_1, 22 bits wide
  assign L_3_d566a9e0 = L_2_32261194 ^ {L_1_C_6ae7f598, {6{1'b0}}};  // XOR_Gate xor_2, 22 bits wide
  ROM #(.dataWidth(2)) rom_1 (.addr(counter_1_p2), .data(EDUerr));
  Multiplexer #(.disabled("Z"), .enable("false"), .width(22)) multiplexer_6 (
    .in0(multiplexer_5_out), .in1({L_1_B_43df9c35, {6{1'b0}}}), .out(L_1_6eefe46d), .sel(random_3_p3));
  assign L_d9787977 = L_d265d600 ^ L_22_36bcc28c;  // XOR_Gate xor_3, 22 bits wide

  // Notes on the sheet:
  //   在随机加扰模式中增加三位错
  //   两个随机信号分别负责高16位和第16位
  //   22位信道加扰屏蔽字生成电路，加扰模式引脚00：不加扰  01:1位加扰 10:2位加扰 11：0-2位随机加扰
  //   如果两个信号相同，其中一个移位
  //   contents of rom_1 (hex, n*v repeats v):
  //   2 2 6*1 0 1 0 0 2 0 2 1 0 1 2
endmodule

// 随机加扰
module L_17_ebb656ca (
  input  CLK,
  input  [16:0] L_17_c666427e,
  output [16:0] L_d265d600,
  output [16:0] L_d9787977
);

  wire [4:0] L_386a2347_p3, random_1_p2, random_1_p3;
  wire [16:0] or_1_out;
  wire [31:0] decoder_1_out31, decoder_2_out31, decoder_3_out31;

  Decoder #(.disabled("Z"), .enable("false"), .select(5)) decoder_1 (
    .out0(decoder_1_out31[31]), .out1(decoder_1_out31[30]), .out2(decoder_1_out31[29]),
    .out3(decoder_1_out31[28]), .out4(decoder_1_out31[27]), .out5(decoder_1_out31[26]),
    .out6(decoder_1_out31[25]), .out7(decoder_1_out31[24]), .out8(decoder_1_out31[23]),
    .out9(decoder_1_out31[22]), .out10(decoder_1_out31[21]), .out11(decoder_1_out31[20]),
    .out12(decoder_1_out31[19]), .out13(decoder_1_out31[18]), .out14(decoder_1_out31[17]),
    .out15(decoder_1_out31[16]), .out16(decoder_1_out31[15]), .out17(decoder_1_out31[14]),
    .out18(decoder_1_out31[13]), .out19(decoder_1_out31[12]), .out20(decoder_1_out31[11]),
    .out21(decoder_1_out31[10]), .out22(decoder_1_out31[9]), .out23(decoder_1_out31[8]),
    .out24(decoder_1_out31[7]), .out25(decoder_1_out31[6]), .out26(decoder_1_out31[5]),
    .out27(decoder_1_out31[4]), .out28(decoder_1_out31[3]), .out29(decoder_1_out31[2]),
    .out30(decoder_1_out31[1]), .out31(decoder_1_out31[0]), .sel(random_1_p2));
  // Random #(.width(5)) random_1: pin names not known; wires that end beside it: CLK, random_1_p2, random_1_p3
  Decoder #(.disabled("Z"), .enable("false"), .select(5)) decoder_2 (
    .out0(decoder_2_out31[31]), .out1(decoder_2_out31[30]), .out2(decoder_2_out31[29]),
    .out3(decoder_2_out31[28]), .out4(decoder_2_out31[27]), .out5(decoder_2_out31[26]),
    .out6(decoder_2_out31[25]), .out7(decoder_2_out31[24]), .out8(decoder_2_out31[23]),
    .out9(decoder_2_out31[22]), .out10(decoder_2_out31[21]), .out11(decoder_2_out31[20]),
    .out12(decoder_2_out31[19]), .out13(decoder_2_out31[18]), .out14(decoder_2_out31[17]),
    .out15(decoder_2_out31[16]), .out16(decoder_2_out31[15]), .out17(decoder_2_out31[14]),
    .out18(decoder_2_out31[13]), .out19(decoder_2_out31[12]), .out20(decoder_2_out31[11]),
    .out21(decoder_2_out31[10]), .out22(decoder_2_out31[9]), .out23(decoder_2_out31[8]),
    .out24(decoder_2_out31[7]), .out25(decoder_2_out31[6]), .out26(decoder_2_out31[5]),
    .out27(decoder_2_out31[4]), .out28(decoder_2_out31[3]), .out29(decoder_2_out31[2]),
    .out30(decoder_2_out31[1]), .out31(decoder_2_out31[0]), .sel(random_1_p3));
  // Random #(.seed(18), .width(5)) L_386a2347: pin names not known; wires that end beside it: CLK, random_1_p3, L_386a2347_p3
  Decoder #(.disabled("Z"), .enable("false"), .select(5)) decoder_3 (
    .out0(decoder_3_out31[31]), .out1(decoder_3_out31[30]), .out2(decoder_3_out31[29]),
    .out3(decoder_3_out31[28]), .out4(decoder_3_out31[27]), .out5(decoder_3_out31[26]),
    .out6(decoder_3_out31[25]), .out7(decoder_3_out31[24]), .out8(decoder_3_out31[23]),
    .out9(decoder_3_out31[22]), .out10(decoder_3_out31[21]), .out11(decoder_3_out31[20]),
    .out12(decoder_3_out31[19]), .out13(decoder_3_out31[18]), .out14(decoder_3_out31[17]),
    .out15(decoder_3_out31[16]), .out16(decoder_3_out31[15]), .out17(decoder_3_out31[14]),
    .out18(decoder_3_out31[13]), .out19(decoder_3_out31[12]), .out20(decoder_3_out31[11]),
    .out21(decoder_3_out31[10]), .out22(decoder_3_out31[9]), .out23(decoder_3_out31[8]),
    .out24(decoder_3_out31[7]), .out25(decoder_3_out31[6]), .out26(decoder_3_out31[5]),
    .out27(decoder_3_out31[4]), .out28(decoder_3_out31[3]), .out29(decoder_3_out31[2]),
    .out30(decoder_3_out31[1]), .out31(decoder_3_out31[0]), .sel(L_386a2347_p3));
  Random #(.seed(3), .width(5)) random_2 ();  // open: clr, next, clk, out
  assign or_1_out = decoder_1_out31[16:0] | decoder_2_out31[16:0];  // OR_Gate or_1, 17 bits wide
  assign L_d265d600 = or_1_out | decoder_3_out31[16:0];  // OR_Gate or_2, 17 bits wide
  assign L_d9787977 = L_d265d600 ^ L_17_c666427e;  // XOR_Gate xor_1, 17 bits wide
endmodule

module L_22_793ae84e (
  input  [21:0] Din22,
  input  L_In_e788f716,
  input  CLK,
  input  L_762d2466,
  input  L_stall_55967050,
  output [21:0] Dout22,
  output L_Out_103436ad
);

  wire multiplexer_2_out, pull_resistor_2_node;
  wire [21:0] multiplexer_1_out;

  Multiplexer #(.disabled("Z"), .enable("false"), .width(22)) multiplexer_1 (
    .in0(Din22), .in1({22{1'b0}}), .out(multiplexer_1_out), .sel(L_762d2466));
  Multiplexer #(.disabled("Z"), .enable("false")) multiplexer_2 (
    .in0(L_In_e788f716), .in1(1'b0), .out(multiplexer_2_out), .sel(L_762d2466));
  Pull_Resistor pull_resistor_1 (.node(L_762d2466));
  Register #(.width(22)) register_1 (
    .D(multiplexer_1_out), .en(pull_resistor_2_node), .Q(Dout22), .clk(CLK));  // open: clr
  Register #(.width(1)) register_2 (
    .D(multiplexer_2_out), .en(pull_resistor_2_node), .Q(L_Out_103436ad), .clk(CLK));  // open: clr
  Pull_Resistor pull_resistor_2 (.node(pull_resistor_2_node));
  not not_1 (pull_resistor_2_node, L_stall_55967050);

  // Notes on the sheet:
  //   L_762d2466: pull=down
  //   L_stall_55967050: pull=down
endmodule

module L_16_b4f519f1 (
  input  [15:0] Din16,
  input  L_In_e788f716,
  input  CLK,
  input  L_762d2466,
  input  L_stall_55967050,
  output [15:0] Dout16,
  output L_Out_103436ad
);

  wire multiplexer_2_out, pull_resistor_2_node;
  wire [15:0] multiplexer_1_out;

  Multiplexer #(.disabled("Z"), .enable("false"), .width(16)) multiplexer_1 (
    .in0(Din16), .in1({16{1'b0}}), .out(multiplexer_1_out), .sel(L_762d2466));
  Multiplexer #(.disabled("Z"), .enable("false")) multiplexer_2 (
    .in0(L_In_e788f716), .in1(1'b0), .out(multiplexer_2_out), .sel(L_762d2466));
  Pull_Resistor pull_resistor_1 (.node(L_762d2466));
  Register #(.width(16)) register_1 (
    .D(multiplexer_1_out), .en(pull_resistor_2_node), .Q(Dout16), .clk(CLK));  // open: clr
  Register #(.width(1)) register_2 (
    .D(multiplexer_2_out), .en(pull_resistor_2_node), .Q(L_Out_103436ad), .clk(CLK));  // open: clr
  Pull_Resistor pull_resistor_2 (.node(pull_resistor_2_node));
  not not_1 (pull_resistor_2_node, L_stall_55967050);
endmodule

module L_2b0de25b (
);

  wire L_d237f850_out;
  wire [15:0] counter_1_p2, l_16_b4f519f1_1_dout16, l_16_b4f519f1_2_dout16, l_16_b4f519f1_3_dout16,
       l_16_b4f519f1_4_dout16, l_724b3708_1_out_2, l_724b3708_2_out_2, l_724b3708_3_out_2;

  Clock L_d237f850 (.out(L_d237f850_out));
  // Counter #(.max('hffff), .width(16)) counter_1: pin names not known; wires that end beside it: L_d237f850_out, counter_1_p2
  // Probe on counter_1_p2
  L_16_b4f519f1 l_16_b4f519f1_1 (
    .Dout16(l_16_b4f519f1_1_dout16), .CLK(L_d237f850_out), .Din16(counter_1_p2));  // open: L_Out_103436ad, L_In_e788f716, L_762d2466, L_stall_55967050
  // Probe on l_16_b4f519f1_1_dout16
  L_724b3708 l_724b3708_1 (.out_2(l_724b3708_1_out_2), .in_1(l_16_b4f519f1_1_dout16));
  L_16_b4f519f1 l_16_b4f519f1_2 (
    .Dout16(l_16_b4f519f1_2_dout16), .CLK(L_d237f850_out), .Din16(l_724b3708_1_out_2));  // open: L_Out_103436ad, L_In_e788f716, L_762d2466, L_stall_55967050
  // Probe on l_16_b4f519f1_2_dout16
  L_724b3708 l_724b3708_2 (.out_2(l_724b3708_2_out_2), .in_1(l_16_b4f519f1_2_dout16));
  L_16_b4f519f1 l_16_b4f519f1_3 (
    .Dout16(l_16_b4f519f1_3_dout16), .CLK(L_d237f850_out), .Din16(l_724b3708_2_out_2));  // open: L_Out_103436ad, L_In_e788f716, L_762d2466, L_stall_55967050
  // Probe on l_16_b4f519f1_3_dout16
  L_724b3708 l_724b3708_3 (.out_2(l_724b3708_3_out_2), .in_1(l_16_b4f519f1_3_dout16));
  L_16_b4f519f1 l_16_b4f519f1_4 (
    .Dout16(l_16_b4f519f1_4_dout16), .CLK(L_d237f850_out), .Din16(l_724b3708_3_out_2));  // open: L_Out_103436ad, L_In_e788f716, L_762d2466, L_stall_55967050
  // Probe on l_16_b4f519f1_4_dout16

  // Notes on the sheet:
  //   计数器
  //   阶段1
  //   阶段2
  //   阶段3
  //   利用ctrl+T驱动该电路时钟，观察数据在流水线中传递的过程
  //   阶段4
  //   阶段5
endmodule

// 组合逻辑
module L_724b3708 (
  input  [15:0] in_1,
  output [15:0] out_2
);


  assign out_2 = in_1;
endmodule
// 字库
module LetterLibrary (
  input  [6:0] L_e0d75744,
  input  [6:0] L_d0f54a78,
  output [31:0] out_3,
  output [31:0] out_4,
  output [31:0] out_5,
  output [31:0] out_6,
  output [31:0] out_7,
  output [31:0] out_8,
  output [31:0] out_9,
  output [31:0] out_10,
  output [31:0] out_11,
  output [31:0] out_12,
  output [31:0] out_13,
  output [31:0] out_14,
  output [31:0] out_15,
  output [31:0] out_16,
  output [31:0] out_17,
  output [31:0] out_18,
  output [31:0] out_19,
  output [31:0] out_20,
  output [31:0] out_21,
  output [31:0] out_22,
  output [31:0] out_23,
  output [31:0] out_24,
  output [31:0] out_25,
  output [31:0] out_26,
  output [31:0] out_27,
  output [31:0] out_28,
  output [31:0] out_29,
  output [31:0] out_30,
  output [31:0] out_31,
  output [31:0] out_32,
  output [31:0] out_33,
  output [31:0] out_34
);

  wire [6:0] multiplier_1_cout, multiplier_1_out, subtractor_1_out;
  wire [13:0] adder_1_out, bit_extender_1_out, undriven;

  ROM #(.addrWidth(14), .dataWidth(32)) rom_1 ();  // open: addr, data
  ROM #(.addrWidth(14), .dataWidth(32)) rom_2 ();  // open: addr, data
  ROM #(.addrWidth(14), .dataWidth(32)) rom_3 ();  // open: addr, data
  ROM #(.addrWidth(14), .dataWidth(32)) rom_4 ();  // open: addr, data
  ROM #(.addrWidth(14), .dataWidth(32)) rom_5 ();  // open: addr, data
  ROM #(.addrWidth(14), .dataWidth(32)) rom_6 (.data(out_8));  // open: addr
  ROM #(.addrWidth(14), .dataWidth(32)) rom_7 (.data(out_9));  // open: addr
  ROM #(.addrWidth(14), .dataWidth(32)) rom_8 (.data(out_10));  // open: addr
  Subtractor #(.width(7)) subtractor_1 (.a(L_e0d75744), .b(7'b0000001), .out(subtractor_1_out));  // open: bin, bout
  Multiplier #(.width(7)) multiplier_1 (
    .a(subtractor_1_out), .b(7'b1011110), .out(multiplier_1_out), .cout(multiplier_1_cout));  // open: cin
  ROM #(.addrWidth(14), .dataWidth(32)) rom_9 (.addr(undriven), .data(out_15));
  ROM #(.addrWidth(14), .dataWidth(32)) rom_10 (.addr(undriven), .data(out_16));
  ROM #(.addrWidth(14), .dataWidth(32)) rom_11 (.addr(undriven), .data(out_17));
  ROM #(.addrWidth(14), .dataWidth(32)) rom_12 (.addr(undriven), .data(out_18));
  assign bit_extender_1_out = {{7{1'b0}}, L_d0f54a78};  // Bit_Extender bit_extender_1
  ROM #(.addrWidth(14), .dataWidth(32)) rom_13 ();  // open: addr, data
  ROM #(.addrWidth(14), .dataWidth(32)) rom_14 ();  // open: addr, data
  Adder #(.width(14)) adder_1 (
    .a({multiplier_1_cout, multiplier_1_out}), .b(bit_extender_1_out), .out(adder_1_out));  // open: cin, cout
  ROM #(.addrWidth(14), .dataWidth(32)) rom_15 ();  // open: addr, data
  ROM #(.addrWidth(14), .dataWidth(32)) rom_16 ();  // open: addr, data
  ROM #(.addrWidth(14), .dataWidth(32)) rom_17 (.addr(undriven), .data(out_21));
  Subtractor #(.width(14)) subtractor_2 (.a(adder_1_out), .b(14'h1));  // open: out, bin, bout
  ROM #(.addrWidth(14), .dataWidth(32)) rom_18 ();  // open: addr, data
  ROM #(.addrWidth(14), .dataWidth(32)) rom_19 ();  // open: addr, data
  ROM #(.addrWidth(14), .dataWidth(32)) rom_20 ();  // open: addr, data
  ROM #(.addrWidth(14), .dataWidth(32)) rom_21 ();  // open: addr, data
  ROM #(.addrWidth(14), .dataWidth(32)) rom_22 ();  // open: addr, data
  ROM #(.addrWidth(14), .dataWidth(32)) rom_23 ();  // open: addr, data
  ROM #(.addrWidth(14), .dataWidth(32)) rom_24 ();  // open: addr, data
  ROM #(.addrWidth(14), .dataWidth(32)) rom_25 ();  // open: addr, data
  ROM #(.addrWidth(14), .dataWidth(32)) rom_26 ();  // open: addr, data
  ROM #(.addrWidth(14), .dataWidth(32)) rom_27 ();  // open: addr, data
  ROM #(.addrWidth(14), .dataWidth(32)) rom_28 ();  // open: addr, data
  ROM #(.addrWidth(14), .dataWidth(32)) rom_29 ();  // open: addr, data
  ROM #(.addrWidth(14), .dataWidth(32)) rom_30 ();  // open: addr, data
  ROM #(.addrWidth(14), .dataWidth(32)) rom_31 ();  // open: addr, data
  ROM #(.addrWidth(14), .dataWidth(32)) rom_32 ();  // open: addr, data
  DotMatrix #(.dotshape("circle"), .inputtype("row"), .matrixcols(32), .matrixrows(32)) dotmatrix_1 ();  // open: row0, row1, row2, row3, row4, row5, row6, row7, row8, row9, row10, row11, row12, row13, row14, row15, row16, row17, row18, row19, row20, row21, row22, row23, row24, row25, row26, row27, row28, row29, row30, row31

  // Other names for the same wires on the sheet: D0[31:0] = out_3; D1[31:0] = out_4; D2[31:0] = out_5;
  //   D3[31:0] = out_6; D4[31:0] = out_7; D5[31:0] = out_8; D6[31:0] = out_9; D7[31:0] = out_10; D8[31:0] = out_11;
  //   D9[31:0] = out_12; D10[31:0] = out_13; D11[31:0] = out_14; D12[31:0] = out_15; D13[31:0] = out_16;
  //   D14[31:0] = out_17; D15[31:0] = out_18; D16[31:0] = out_19; D17[31:0] = out_20; D18[31:0] = out_21;
  //   D19[31:0] = out_22; D20[31:0] = out_23; D21[31:0] = out_24; D22[31:0] = out_25; D23[31:0] = out_26;
  //   D24[31:0] = out_27; D25[31:0] = out_28; D26[31:0] = out_29; D27[31:0] = out_30; D28[31:0] = out_31;
  //   D29[31:0] = out_32; D30[31:0] = out_33; D31[31:0] = out_34

  // Notes on the sheet:
  //   contents of rom_1 (hex, n*v repeats v):
  //   ffffffff 60000000 18000 3c000 0 0 18000 3c000 0 0 18000 3c000 18000 18000 3c000 3c000 18000 18000
  //   3c000 3c000 18000 18000 3c000 18000 3c000 3c000 18000 3c000 18000 18000 3c000 18000 3c000 3c000
  //   18000 3c000 3c000 18000 3c000 3c000 3c000 18000 18000 3c000 18000 3c000 3c000 3c000
  //   contents of rom_2 (hex, n*v repeats v):
  //   1c000 ffffffff 10000 0 60000000 60000000 3c000 3c000 0 0 3c000 3c000 0 0 3c000 3c000 8000 2000 8000
  //   8000 400000 1000 80 10000 40000 20000 4000 20000 40000 2000 1000000 8000 2000 800000 40000 20 20000
  //   2000 100 800000 200 1000000 200200 1000000 800000 800000 8000 10000 0 8000 10000 800000 0 0
  //   4*1000000 20000 1000 20000 800000 800000
  //   contents of rom_3 (hex, n*v repeats v):
  //   1ffc00 ff000 7ff0 0 ffe0000 10000 1c0000 60000006 0 60000006 40000002 38000 0 60000000 e0000000
  //   181800 0 0 0 e6000 3c000 3c000 0 0 3c000 3c000 0 0 3c000 3c000 1800 1801800 8100 3000 60000 c00 c000
  //   383800 7000020 181800 0 e0 0 c200c00 1800000 30000 c06000 1003000 3000 1c000 1000 70000 2000 0 18000
  //   0 600c00 e00800 e00000 3000020 1040300 60000 6007000 6000 181800 3000018 1800000 0 0 3801800 0 8000
  //   0 3006000 2000 6100000 1800000 1800000 3000000 80 0 100800 20000 1800c00 0 3000000 800000 1800 80000
  //   301800 0 8000 30000 1800020 c00000 8 3800040 e00020 1000400 1801800 603000 c000100 30000 60000 1c00
  //   700000 300000 3818000 3803800 1800 18000 3803800 1800 1000c00 6003800 c06000 3000 181000 4000 200000
  //   30000 10 181c00 80 e00000 0 300c000 60000 3006000 1000000 100 181800 3001800 6040020 c00000 1c00
  //   1c3800 60000 102000 c3000 182000 0 2000000 602000 0 180000 c0000 2002000 6000c00 30000 380c00 18000
  //   1003000 1c000 0 8 0 c00 40180 0 70000 4000 0 1801000 1001c00 600 383000 381800 600c000 6004000
  //   c00c000 c0 18000 e000 1800000 400600 600c00 0 1800 c00 c00 200 400 c606000 3000 3000 30 18000 800000
  //   70000 40000 600c200 6000300 4018200 3000 3800000 300000 0 30000 c00800 400800 20 e000 180c000 200
  //   70000 3000 30000 3001000 0 2000 3000000 0 380 60000c0 2000000 c000 400400 c00 101000 10000c0 1001800
  //   3001800 1c00 4003300 e00e00 3801b80 3000c00 1800c00 c03000 30000 c00600 c00 1900 30100 0 0 3001000
  //   60000 3000 1000800 1c00 0 30000 1c000 3803000 c00000 2000000 3003000 1c00 603800 1c001c0 3000 1c0 20
  //   0 1e0 1c000 183000 1c1c00 300000 20000 c0 3000 6020000 6006000 1000c00 301800 800800 18000 6000
  //   183000 2000000 3000300 3806300 c3000 181800 0 c01800 1800000 0 0 0 c0 3000000 0 101800 301c00 1c000
  //   1800 1018300 38000 6000 800400 2000 3000020 202000 100180 380c000 3803000 30080c0 2004000 8000 1800
  //   3001800 30000 6000000 c00000 100 0 3000000 18000 18200 800000 1803000 0 0 600700 1800000 0 400000
  //   c00000 1800800 2000600 600000 30000 40000 60c080 1c00 3000800 60000 1000800 2020080 1380030 1040000
  //   40100 2010000 0 0 18000 1000080 6001800 0 3000 c00c00 2000180 3000c00 3000 600 3000000 8000 0 380
  //   100000 400000 0 c00 0 0 c00 100000 6000 c000 3001800 0 8000000 0 0 c00 300 1c000 403000 0 1c000
  //   3000000 180 3800000 60000 1800 18000 1c000 70000 3000800 10 1c00 c00 100000 1c00 1c00c00 0 800000 0
  //   0 60000 3000000 10000 7000000 10 c180 180 3000400 8000400 1800 600e00 400 800 18000 3006000 1800200
  //   0 3800c00 0 30000 3006000 601000 c00000 1800 18000 c000 38000 2003000 18000 0 400000 6000 1002000
  //   3000000 2000040 100 70000 3807000 800 0 6000 1800 70000 600 1800 c000 101000 c0 3200 1800 200c00
  //   18000 0 3800 300010 0 c000 80 181800 30000 200000 401000 201800 4000 1c00000 30c0 1c00800 c00000
  //   1800 1801800 30000 1000800 18000 c01c00 6000 c000 1803000 6000 60 1c001c0 70000 1800 8080 2000000
  //   1000080 300c300 3001000 200e100 1008100 4003000 1801800 6000 800000 38000 0 0 806000 300c00 418400
  //   c00 600000 e1ee00 408000 c03800 3000 30000 1800 1000000 800100 600c00 60000 3810180 0 0 1800000 0
  //   2020180 0 0 10180 20 10000 1000800 18000 181800 3801800 0 3003000 30 1800000 e0000 3000c00 100 10
  //   100010 2001800 8060180 c000 1001800 400000 c01800 0 1000000 0 1800c00 0 4100 0 2000000 c00000 e000
  //   1000 1800 800800 1000 8000 20020 3003000 1000000 30000 1800 381c00 1801800 30000 400c00 20100 3000
  //   e00000 1001000 1000 6600 38000 c6000 1800800 c03000 30000 400000 600000 18000 6001800 300c00 6000 0
  //   0 0 100 0 0 3001800 0 1000 0 c00 181800 1880 3001840 1000 3180 200 0 0 0 2000000 8 200 3001800 20000
  //   0 100 30000 80000 183800 300c700 800 3801000 1800000 6000000 2000 8000000 10000 1800100 1000 1c00 0
  //   0 c000 600000 600000 38000 1801c00 800 3000 3000 3000 1800 1800000 3001800 800 18000 2000 1800800
  //   c00 3000000 6002000 40000 300000 1000000 2000c00 400c00 1000 0 20300c0 1000 8080 c00e00 1800008 0
  //   3000c00 180 c0 3000000 1000 18000 30000 2000000 e00000 0 0 c00 0 3007000 3000 600 200 200600 1800c00
  //   1800008 8600 3000700 0 0 1000000 0 0 6000200 300000 2000000 0 0 1a00 c1000 20 800800 60c000 0
  //   2000000 1800 1800 381800 3000000 180 0 180218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
  //   contents of rom_4 (hex, n*v repeats v):
  //   c3000 40 2000000 10 8000000 80 0 1ff0 100000 1ff0 f80000 1fff0 fff8000 1ffe0 7ff0000 800 3800 10000
  //   18000 0 c00000 c20000 0 18000 0 0 0 400 3e000 0 10000 10000 18000 c00000 3ffe00 7ff0 1800000 ffe0000
  //   0 0 300 1c0 18000 3c00000 1c0 80000 1e0380 0 0 0 180 70 20000 0 0 18000 0 0 80 0 0 0 3c0 0 0 1e0 c0
  //   6000 0 0 0 e0000 3800001c 0 7000000e 60000006 38000 0 60000000 e0000000 1c1c00 0 0 0 e7000 200000
  //   18180000 6000000 60000 0 0 300000 0 0 6000 30000 3000 0 0 0 20000 0 300 0 38000 3000 0 0 30000 0 0
  //   2000000 60000 3c000 3c000 0 0 3c000 3c000 0 0 3c000 3c000 218008 30600008 3801c00 1c01c00 e380 3800
  //   38000 1800e00 6000 383010 78001f0 1c1c00 18030 1ff0 2301c0 e380600 3c00000 18000 e07000 3c01800 1800
  //   301e000 1800 38000 8103000 3ffff80 1c000 0 700e00 e00e00 e00000 18000f0 1ce0700 70000 7007000
  //   800e000 1c1c00 380001c 1c00700 600 0 3803c00 2000 e000 0 3807200 3800 7180000 1c00000 1c00000
  //   3800000 3ffffc0 6000060 380f00 38000 1c00e00 10 3840010 1e00000 83c00 3c0000 f83800 60000 e000
  //   3038000 1c000e0 c04080 41fffc 38001e0 e00070 1c00600 1c01c00 703800 6000180 38000 70000 1801c00
  //   601008 300010 3818000 3801c00 8200c00 3018000 3803800 e00 1c00e00 7001c00 e03800 8003800 1c3800 7000
  //   780000 18000 1001c 1c1c00 3ffffc0 e40040 e40080 780f000 38000 380f000 1c30060 1ffff80 3c3800 3801c00
  //   70ffff0 e00000 1c00 1c3800 70000 3c3800 c3810 1c3800 800080 3800000 f03000 180000 1c0000 1e0200
  //   3803800 3000c00 38000 380e00 1c000 3c03800 381c060 1800008 18 18 10230c30 c0301c0 8000030 60200
  //   6007000 c018808 1c01c00 1801c00 600 383800 381c00 700e000 700e000 e00e000 fe0 c000 7000 1c00000
  //   700700 8710e00 c0000 e00 e00 8040600 8000380 10270700 e706000 6003800 1801c00 800f0 1c000 e00008
  //   38000 70000 300e380 3000380 701c380 c003800 3800000 380000 8 38000 8e60c00 8720c00 4010038 7000
  //   1c0e000 4000380 18060008 c001800 18000 3801c00 700 10003800 3800000 10 1f80 70180e0 3800000 e000
  //   300e00 c00 1c1c00 18007e0 1c01c00 7801c00 c001c00 70039c0 e00e00 3801dc0 3800e00 1c01e00 f03c00
  //   30000 e00700 8000e00 c201cc0 18030180 4001c00 180070 3801d00 70000 3b00 1801c00 3801c00 18 38000
  //   1c000 3803800 600000 7807000 3801800 301c00 703c00 1e001e0 3800 100c01c0 1f0 f0 7ff0 fe030 183800
  //   181c00 380000 70000 7ffffe0 3800 7070008 7007000 1c00e00 381c00 e01e00 3c000 c007000 1c3000 7020100
  //   3000380 3007380 c3800 1c1c00 4000008 e01c00 1c00018 2040040 c202038 6000060 c0e0 38000e0 80 381c00
  //   381c00 1c000 1c00 381c380 1c000 c2000 600f00 8003800 38000e0 303800 3801c0 380e000 3807000 38060e0
  //   700e000 601c000 1000c00 3800e00 38000 3000000 e00018 ffff80 180000 3800180 1c100 c18300 e00300
  //   1e03800 c1000c0 18 700700 1c00040 20020 700000 e00000 1c00e00 3800700 700000 30400 18060000 70e1c0
  //   1e00 3800e00 f0000 1c00e00 30301c0 1b80038 3870000 8060180 3018000 4000030 20 1c000 1ffffc0 7001c00
  //   c000000 10203800 e00e00 18001c0 3800e00 383800 3800680 3004840 e600 1800100 7fc0 790010 e00020
  //   c004840 6000ec0 300 c0600c0 e00 380000 7000 e000 3801c00 6061000 e003800 4000000 1c00 e00 380 1c000
  //   603800 0 1c000 3800000 7c0 3c00000 30000 1c00 1c000 301c060 38000 3800e00 301c 1e00 18180e00 7a0008
  //   381e00 1c01e00 71c000 1e00008 6180 0 70000 1c00000 1c000 7000000 6000038 e180 60001c0 7806700
  //   c000700 10203800 700e00 700 1c01c00 38030 3803800 1c00380 c00c00 3c00e00 1c00070 1c000 3806000
  //   701c00 e06040 1c00 18000 e000 1c000 3801800 1c000 1800000 f00018 7800 1c07800 38000e0 38001e0 1f80
  //   78000 3007800 e00 30 8007000 3801c00 70040 c0c700 3801c00 6000 1c1c00 80e0 3303b00 180c00 380e00
  //   c01c000 c000010 383c00 300038 10118030 1800f000 880e0 1c1c00 38000 380000 701c00 701c00 f000 1c00000
  //   38c0 1c01c00 e00040 10300c00 1c03c00 18000 3800e00 301c040 1ec1c00 7000 e000 1c01800 3000 ffe7ff0
  //   1e001c0 78000 1c00 c1c0 383ffe0 38081c0 380e380 3801c00 380e380 381c380 6003800 1c01c00 7000 1c00000
  //   38000 1ffff80 10 e07000 380e80 71c700 e00 706000 f0c780 e0ee00 1e03800 c003800 78000 41c00 1c00000
  //   ffff00 300e00 3070000 38181c0 8300000 0 1c00000 c00000 38181c0 4003800 10000030 181c0 ffffff0 1c000
  //   1c01e00 1c200 1c1c00 3801c00 0 3c03000 1001f8 1c00018 e0000 3800e00 1ffff80 c01c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
  //   contents of rom_5 (hex, n*v repeats v):
  //   40000 0 0 c3000 0 20 3c00000 1820 3c70000 e0 6000000 30 18000000 198 19800000 1800 100000 1830
  //   d80000 1ffe0 7ff8000 1ffc0 7ff0000 18000 0 0 0 18000 7e000 3c00 7c00 30000 c000 10 4000000 0 0 0
  //   18000 ff000 800000 1c00000 1c70000 2000000 18000 18000018 0 c000 7000c00 ff800 0 18000 18000 3c000
  //   7e000 7e000 18000 18000 0 0 18000 18000 0 0 0 18000 18000 3ffffff8 18000 301c00 4008060 3000000 0
  //   180 820 8000 2000000 4000 1c000 c000 0 c0e00 0 0 8000 0 1000 0 1000 0 0 10300 0 1ff00 3000 0 1c01000
  //   1000180 1c00180 4*0 1ff800 1fe7fc0 7fdffbfe 1fffc0fc 7f81fe0 7fc1fffc 7f07fffe 7e0ffffe 3fffc1fc
  //   7fc1fc0 1fe0fffc 7f83fffe 1f8000 1c00000 20 4000000 c00 f80700 7000 c00000 e0000 18000 0 700 38000
  //   780 18000 e00000 0 30000 70000 0 0 0 80000 1c000 30000 0 0 0 e000 0 0 c0000 180000 0 0 180 0 0 0
  //   80000 0 0 0 300000 0 0 180 260 30000 10000 c000 3000 0 20000 c000 0 e0000 e0980 70000 601c0 40000
  //   1800c0 0 c0 7000 6040 0 0 0 180 0 300 600 38 38000 100 7000 6000 0 e0400 30 c00 30 e0000 0 38000 0 0
  //   1e000 2000 0 60 0 300000 0 240 0 60 120 0 100 200 18000 40180 1e0 0 f0000 30000 3000 c00 0 780000
  //   18000 0 0 0 c00 7000 0 c00 3c0000 700c0 18000 e0000 10000 0 7f000 1e000078 0 3000000c 3000000c 38000
  //   0 60000000 60000000 181c00 0 0 0 7e000 600000 c300000 7000000 300000 70000 0 0 380000 60000 3000
  //   7000 100400 0 0 3800 10000 0 38000 3000 400 0 200 38000 18000 300 0 1c000 c03c00 7f0 0 38000 0 7c00
  //   3800000 78000 60000 c000 70000 300 3c000 3c000 0 0 3c000 3c000 0 0 3c000 3c000 3ffffc 3ff3fffc
  //   3803800 1803800 c380 7000 1c000 3800c00 7010 383038 7003ff0 181c00 dfff8 7ffff0 1ff181c0 c300700
  //   3800020 1c000 c0e000 3801c00 1c00 381c070 1fe00c00 18000 ff81c00 3ffffc0 18000 10 600e00 e10c00
  //   c00000 1c007f0 38e0700 40000 7006000 600c000 181800 38c1018 1c08600 8600 60 3023810 103000 6000 0
  //   3806380 8183300 6184010 1800010 1818030 383fff0 18000 7fffff0 7003c0 78000 1800c00 1ffffff8 387fff8
  //   1c00018 1ffc3800 1fc0018 7f83000 330018 30c008 3030420 18003f0 1807fc0 221fffc 3800ff0 18c003f0
  //   1804600 1801800 e03000 70030c0 38000 60000 1c01c20 601ffc 309ff8 3018618 3000c00 1ff00e08 3818010
  //   3803000 100e10 1800c00 7000c00 1c01800 6001c10 1c3800 c10e000 700000 1c018 fff8018 181c08 3ffffc0
  //   c7ffe0 e7ffc0 700e000 38000 300e000 183fff0 1c00180 703800 3003800 70e0060 c00018 181800 1c3000
  //   c0000 383800 c3ff8 1c3070 ffffc0 383fff0 e01800 101d0018 380200 1fff00 3801800 3800c00 30000 380c00
  //   18000 3803800 381c070 38ff7fc 1ffffffc 3ffffffc 1ff30c38 7018380 c1ffff8 ffff00 7007000 fffcffc
  //   3803808 3c01800 60c00 383818 381808 700e000 600e060 e00e060 1ffe0 e000 3008 e00030 10620e00 e638c00
  //   60300 c040600 c040600 ffe0610 e10c180 1ff60600 c60e008 3003000 3800c00 1ffc0ff8 c000 1e0001c 1c008
  //   38000 380c180 3860180 3018180 6001800 3800070 304030 1feffffc 38000 ee71c00 c671c00 7ff8038 3008
  //   180c030 6000340 c06001c 6081800 1c000 3000c00 7f80 18003000 3000018 3ffffff8 fffc0 700c0c0 380001c
  //   7000 380e00 c00 181800 180ffe0 1831d80 7001800 7001800 60038c0 e00e00 38018e0 3800c00 3801c00 e03800
  //   60000 c00600 ff00c00 ff01ce0 c030180 7001c00 1ffc00f0 30019c0 70000 31c0 c01c00 3801800 3ffffffc
  //   78000 1c000 7027010 700808 7007000 3001c00 30781808 703900 1c001c0 3000 1ffe01c0 10203ff8 1ff01ff0
  //   3ffffc0 3ffc038 183808 181c38 3f8030 f0000 7ffffe0 c3900 607001c 700e000 1800e00 381c00 1c01c00
  //   78000 6007000 183018 703ff80 30c1380 3006300 c3000 181810 7fffffc 1c01800 3a00018 3fc7fc0 63ff038
  //   7fffff0 183060c0 3000ff0 7ffffc0 381800 301c08 18000 301c00 3818300 400c008 1e3000 300e00 6001800
  //   38007f0 303020 f001c0 381c100 380e000 30070c0 700e100 301c200 3c00600 7000600 1c000 187fff0 617ffc
  //   ffff80 303b0030 387ffc0 1818380 e18700 e00780 1c03860 ffbffe0 3ffff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
  //   contents of rom_6 (hex, n*v repeats v):
  //   1ff800 300c00 181800 0 70000 0 0 c3000 0 c0 3c00000 20c0 3cf8000 1c0 3000000 30 c000000 1b0 18c00000
  //   1800 100000 1bf0 d80000 180c0 3018000 1ffc0 3ff0000 18000 0 0 0 18000 c000030 7ffff80 1ffffff8 180
  //   18000 8060 0 0 3ffc00 6e00 ce00 300 30000 c000 70 7800000 0 0 0 18000 1e7800 7e00000 1c00000 1c70000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
  //   contents of rom_7 (hex, n*v repeats v):
  //   3ffc00 1c3800 3c3c00 0 60000 0 0 c3000 0 180 3c00000 6180 3cf8000 180 1800000 60 c000000 330 cc00000
  //   1800 100000 1be0 d80000 18180 1818000 1ff80 1ff0000 18000 80 38000 18000 3c000 c000030 3ffff80
  //   ffffff0 0 3c000 0 1800180 180 18000 c060 18 0 780e00 ce00 cc00 300 30000 c000 3e0 3e00000 0 1c00380
  //   3c00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
  //   contents of rom_8 (hex, n*v repeats v):
  //   77000 3c3c00 0 60000 0 0 c3000 0 180 3c00000 c180 3c78000 300 c00000 60 6000000 320 c600000 1800
  //   100000 1a00 d80000 18180 1c18000 1ff00 ff0000 18000 30001c0 7c000 3c000 3c000 6000060 3800380
  //   1c00380 1800180 1ff800 0 3c003c0 180 18000 180c0 70 0 1c00300 c000 c000 600 30000 c000 1f00 7c0000 0
  //   3e007c0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
  //   contents of rom_9 (hex, n*v repeats v):
  //   71c00 360600 0 0 c3000 0 3c0 4000000 1e3c0 4180000 400 600000 300 1800000 1980 1980000 1800 100000
  //   1a00 d80000 18c00 318000 1fc00 3f0000 18000 183800 0 0 c1800 1800180 780000 1c00380 1800180 1800180
  //   3800000 0 600 18000 c0300 e00 38001c0 c000030 18000 7f000 0 1c018038 70f0018 7803fc0 3fc07f0
  //   1ffffff0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
  //   contents of rom_10 (hex, n*v repeats v):
  //   0 0 0 3c000 0 0 0 73800 200600 0 1e00000 c3000 0 80 0 4080 0 400 600000 300 c00000 1980 18c0000 1800
  //   100000 1a00 d80000 18800 318000 1f800 3f0000 18000 c7000 0 0 181800 c00300 380000 1c00380 1800180
  //   1800180 3000000 0 600 18000 c0600 1c00 60000e0 c000030 18000 fb800 0 1c030038 c03c030 e0070e0
  //   70f1e00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
  //   contents of rom_11 (hex, n*v repeats v):
  //   0 0 0 7e000 0 0 0 63800 400c00 0 7f80008 c3000 e03c070 400 600000 600 c00000 3300 cc0000 1800 100000
  //   1a00 d80000 19800 118000 1f800 3f0000 7ffffe0 6e000 0 0 181800 c00300 1c0000 1c00380 1800180 1800180
  //   3000000 0 c00 18000 180600 3800 e000070 1c038030 18000 198c00 0 c070030 1800f0e0 c00c030 c03b000 c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
  //   contents of rom_12 (hex, n*v repeats v):
  //   0 0 0 ff000 0 0 0 e3000 800c00 0 e1f0018 c3000 1f07c0f8 400 600000 600 600000 3300 c60000 1800
  //   100000 1a00 d80000 19800 198000 1f800 3f0000 7ffffe0 3c000 0 0 300c00 600600 1e0000 1c00380 1800180
  //   1800180 3ffff80 0 c00 18000 180c00 6000 c000030 1807c030 18000 198c00 0 e0e0070 3fc0 1801c030
  //   1801e000 c0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
  //   contents of rom_13 (hex, n*v repeats v):
  //   3c000 181800 0 c0000 0 0 c3000 0 300 c00000 1c300 c30000 600 600000 c0 6000000 660 6600000 1800
  //   100000 1a00 d80000 18300 c18000 1ff00 ff0000 18000 1800380 7c000 7e000 66000 6000060 1c00080 1c00380
  //   1800180 7ffe00 3fffc0 3e007c0 300 18000 380c0 e0 7e000 3800180 c000 c000 0 1800f80 0 0 0 c00 30038
  //   1e00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
  //   contents of rom_14 (hex, n*v repeats v):
  //   18000 0 0 c0300 0 0 c3000 0 3c0 1800000 1e3c0 1830000 400 600000 c0 3000000 660 6300000 1800 100000
  //   1a00 d80000 18600 618000 1fe00 7f0000 18000 c00700 7c000 3c000 66000 30000c0 e000c0 1c00380 1800180
  //   e00700 7fffc0 3e007c0 300 18000 30180 1c0 3ffc00 30000c0 18000 1c000 0 7803fe0 0 0 0 c00 301f0 fc0c0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
  //   contents of rom_15 (hex, n*v repeats v):
  //   187f80 0 0 c3000 0 7c0 1000000 1f7c0 1060000 400 600000 180 3000000 cc0 3300000 1800 100000 1a00
  //   d80000 18600 618000 1fc00 7f0000 18000 600e00 38000 3c000 63000 30000c0 e00040 1c00380 1800180
  //   c00300 e00000 3c003c0 300 18000 60180 380 f00f00 6000060 18000 1c000 ffffff0 e007070 f00000 0 0 1800
  //   30f80 1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
  //   contents of rom_16 (hex, n*v repeats v):
  //   31c00 1ff700 0 0 c3000 0 3c0 2000000 1f3c0 20c0000 400 600000 180 1800000 cc0 3180000 1800 100000
  //   1a00 d80000 18c00 318000 1fc00 3f0000 18000 301c00 0 0 c3000 1800180 700000 1c00380 1800180 1c00380
  //   1800000 800100 600 18000 60300 700 1c00380 e000060 18000 1c000 1ffffff8 c00c030 3fc0000 800700
  //   f000c0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
  //   contents of rom_17 (hex, n*v repeats v):
  //   0 0 0 fe000 0 0 0 186000 3000 0 20000fc0 c3000 e03c0f0 400 600000 600 c00000 3300 cc0000 1800 100000
  //   1a00 d80000 19800 118000 1f800 3f0000 18000 6e000 0 0 600600 300c00 60000 1c00380 1800180 1800180
  //   3000000 0 181800 18000 603800 30000 10000008 1c03c030 18000 199c00 0 0 70f0018 c0e0070 e03b800 30000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
  //   contents of rom_18 (hex, n*v repeats v):
  //   0 0 0 ff000 0 0 0 c7000 1800 ffffffff 1803e030 c3000 1f07e1f8 400 600000 c00 600000 6600 460000 1800
  //   100000 1a00 d80000 19800 198000 1f800 3f0000 18000 38000 ffffff0 0 300c00 600600 e0000 1c00380
  //   1800180 1800180 3ffffc0 0 c00 18000 301c00 c000 18000018 1807e038 18000 198c00 1ffffff8 7fc01e0
  //   f00f00 1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
  //   contents of rom_19 (hex, n*v repeats v):
  //   0 0 0 ff000 0 0 0 c6000 1000 0 10007fe0 c3000 1f07c0f8 400 600000 600 600000 3300 c60000 1800 100000
  //   1a00 d80000 19800 198000 1f800 3f0000 18000 3c000 7ffffe0 0 600600 300c00 70000 1c00380 1800180
  //   1800180 3ffff80 0 1800 18000 301800 18000 18000018 1807c030 18000 198c00 0 1f00180 3fc0000 1c030030
  //   c01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
  //   contents of rom_20 (hex, n*v repeats v):
  //   10c000 36000 0 0 c3000 400 600000 300 1800000 1980 1980000 1800 100000 1a00 d80000 18c00 318000
  //   1fc00 3f0000 18000 183800 0 0 c00300 181800 180000 1c00380 1800180 1800180 3800000 0 6e3000 18000
  //   c06000 c0000 0 c000030 18000 7f000 0 1ffffff8 1800f0e0 3f803c0 3fc07e0 1ffffff0 7e000 7c000 f8001f0
  //   f0001f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
  //   contents of rom_21 (hex, n*v repeats v):
  //   0 f000000 7e00000 200000 e000 0 0 c3000 400 600000 180 3000000 cc0 3300000 1800 100000 1a00 d80000
  //   18600 618000 1fc00 7f0000 18000 600e00 38000 38000 1800180 c3000 300000 1c00380 c00300 1800180
  //   e00000 3c003c0 73000 18000 180c000 300000 0 6000060 18000 18000 ffffff0 0 f00 0 0 180000 31f80
  //   1f0c000 7e0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
  //   contents of rom_22 (hex, n*v repeats v):
  //   0 3c00000 c200000 7000 0 0 c3000 400 600000 c0 3000000 c60 6300000 1800 100000 1a00 d80000 18600
  //   e18000 1fe00 7f0000 18000 c00700 7c000 7c000 1000180 67000 600040 1c00380 e00600 1800180 7fff80
  //   3c007c0 3f000 18000 180c000 600000 0 70000e0 38000 18000 300000 303f0 f80c000 fc000 3f000 0 7e000
  //   3e00fc0 7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
  //   contents of rom_23 (hex, n*v repeats v):
  //   0 0 0 7e000 0 0 0 18c000 42000 0 100 c3000 400 600000 300 c00000 3180 18c0000 1800 100000 1a00
  //   d80000 18800 318000 1f800 3f0000 18000 c7000 0 0 c00300 181c00 c0000 1c00380 1800180 1800180 3000000
  //   0 3c1800 18000 603000 60000 0 c000030 18000 db800 0 0 c03c030 7bc01e0 7ff1ff0 1ffffff0 3f0000 f800
  //   1c000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
  //   contents of rom_24 (hex, n*v repeats v):
  //   0 1c000000 3c00000 308000 1c000 0 0 c3000 400 600000 180 1800000 18c0 3180000 1800 100000 1a00
  //   d80000 18c00 218000 1fc00 7f0000 18000 301c00 0 0 1800180 c3800 380000 1c00380 1800300 1800180
  //   1800000 0 73000 18000 c06000 180000 0 c000070 18000 3c000 1ffffff8 ffffff0 3fc0 0 0 c0000 3fc00
  //   3ec000 3f00030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
  //   contents of rom_25 (hex, n*v repeats v):
  //   0 e00000 6600000 1000 0 0 c3000 300 1800000 60 c000000 330 cc00000 1800 100000 1a00 fd80000 18180
  //   3818000 1ff80 1ff0000 0 80 38000 38000 6000060 3c000 1ffff80 1c00380 7c000 1800180 0 1800380 e000
  //   18000 6030000 7000000 0 f00f00 330000 3b0000 0 ffffff0 0 0 0 c00000 30000 c000 7e0 3e00000 0 3c000
  //   1c007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
  //   contents of rom_26 (hex, n*v repeats v):
  //   0 600000 3c00000 c3000 180 3000000 60 c000000 330 18c00000 1800 100000 1a00 fd80000 180c0 3018000
  //   1ff80 3ff0000 7ffffe0 0 0 0 6000060 1c000 3ffff80 ff01ff0 4000 ffffff0 6030000 fffffe0 0 3ffc00
  //   330000 3f0000 400000 30000 c000 f0 7000000 0 0 0 1ff800 18000 0 0 0 1fc00 dff800 c1ff830 180000 0
  //   1807e1f8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
  //   contents of rom_27 (hex, n*v repeats v):
  //   0 1e00000 c300000 7800 0 0 c3000 400 600000 c0 6000000 660 6600000 1800 100000 1a00 d80000 18300
  //   c18000 1fe00 ff0000 18000 1800380 7c000 7c000 30000c0 66000 c000c0 1c00380 7c3c00 1800180 3fffc0
  //   7e007c0 1e000 18000 3018000 c00000 0 38001c0 30000 18000 300000 30078 1e00c000 1f800 f8000 0 7e000
  //   7e00fc0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
  //   contents of rom_28 (hex, n*v repeats v):
  //   0 600000 1000000 c3000 c0 6000000 30 18000000 198 19800000 1800 100000 1a00 c180000 18060 7ff8000
  //   1ffc0 7ff0000 7ffffe0 0 0 0 c000030 18000 7ffff80 ff01ff0 ff000 3e0000 3e0000 30000 c000 10 fe000
  //   18000 7e000 18018010 0 0 3c0f0 1c7000 0 1800180 1800180 7e000 3c000 3c000 18000 18000 0 0 1ffffff8
  //   1ffff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
  //   contents of rom_29 (hex, n*v repeats v):
  //   c3000 40 0 10 8000000 108 10800000 1800 ff00000 1e00 ff80000 1fff0 fff8000 1ffe0 7ff0000 20 8000
  //   80000 18000 18000 fe000 0 1000080 1000080 18000 f00700 8000000 0 0 200000 3000000 1ffc00 700 7ff0
  //   380 7fe0000 3ff800 0 0 ff0000 180000 1c00 7e0000 0 3c0 18000 3c00000 700 1e000 38000 0 60000000
  //   60000000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
  //   contents of rom_30 (hex, n*v repeats v):
  //   7f00000 e00 7f00000 0 0 ffe0 7fe0000 6000000 3c000 7ff0 0 ffe0000 1fe000 0 0 7e0000 7e0000 7f00
  //   3c0000 0 0 10000 38000 0 60000000 70000000 300000 38700000 80000 3c000 3c000 0 0 3c000 3c000 0 0
  //   3a00 1c600000 300060 10000000 f00018 3380008 e00010 1e00010 100000 0 20000020 e0 7e0018 38000010 180
  //   13e000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
  //   contents of rom_31 (hex, n*v repeats v):
  //   7fc0000 0 ffffffff 7e0000 3e00 10000 0 60000000 70000000 1fe00000 3c000 3c000 0 0 3c000 3c000 0 0
  //   3c00 fc0ffff 1000000 4 800000 800000 80000 400000 200000 20000 0 0 2000 40000 20000000 0 0 0 200
  //   20000000 0 0 2000000 80000 1000 0 0 0 100 0 0 2000000 10000 4000 20000000 400 10000000 40000 4000
  //   4000 10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
  //   contents of rom_32 (hex, n*v repeats v):
  //   0 e00000 c300000 3800 0 0 c3000 600 c00000 60 6000000 660 c600000 1800 100000 1a00 d80000 18300
  //   1818000 1ff00 1ff0000 0 30001c0 7c000 3c000 30000c0 3e000 1c00180 1c00380 1ff800 1800180 0 3c007c0
  //   e000 18000 7018000 3800000 0 1c00380 30000 30000 0 ffffff0 0 0 0 600000 30000 c000 3f00 7c0000 0
  //   7e000 3e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
endmodule

module L_07a38aff (
);

  wire l_8e5bae90_1_l_1425883c, l_455c5dad_1_l_0_eb6a1b8d, l_455c5dad_1_l_1_ef5de30d,
       l_455c5dad_1_l_2_d93bbbb2, l_be134dae_1_clr2, l_be134dae_1_clr3, l_be134dae_1_clr4, l_be134dae_1_en5,
       l_be134dae_1_l_1err_a3df68ae, l_be134dae_1_l_2err_26a15d6f, l_crc_dc188f0d_1_l_0_eb6a1b8d,
       l_crc_dc188f0d_1_l_1_ef5de30d, l_crc_dc188f0d_1_l_2_d93bbbb2, l_crc_e0b66718_1_clr2,
       l_crc_e0b66718_1_clr3, l_crc_e0b66718_1_clr4, l_crc_e0b66718_1_en5, l_crc_e0b66718_1_l_1err_a3df68ae,
       l_crc_e0b66718_1_l_2err_26a15d6f, undriven_3, undriven_4, undriven_6, undriven_8;
  wire [6:0] nationalstandardtransitionareacode_1_l_d0f54a78, nationalstandardtransitionareacode_1_l_e0d75744;
  wire [15:0] chinesecharacterdisplay_1_educoder, l_8e5bae90_1_l_d332f524, l_455c5dad_1_l_9904c55d,
       l_crc_dc188f0d_1_l_9904c55d, undriven, undriven_2, undriven_5, undriven_7;
  wire [16:0] l_b33f7de1_1_l_fc3bd895;
  wire [21:0] l_00584185_1_l_ba8a574d, l_crc_4439dc43_1_crc_5864b47a;

  NationalStandardTransitionAreaCode nationalstandardtransitionareacode_1 (
    .L_e0d75744(nationalstandardtransitionareacode_1_l_e0d75744),
    .L_d0f54a78(nationalstandardtransitionareacode_1_l_d0f54a78), .GB2312(undriven_2));
  L_00584185 l_00584185_1 (.L_ba8a574d(l_00584185_1_l_ba8a574d), .L_d11c89cc(undriven));
  ChineseCharacterDisplay chinesecharacterdisplay_1 (.EduCoder(chinesecharacterdisplay_1_educoder));
  L_be134dae l_be134dae_1 (
    .EDU(undriven_3), .L_7d930fa3(undriven_4), .L_1err_a3df68ae(l_be134dae_1_l_1err_a3df68ae),
    .L_2err_26a15d6f(l_be134dae_1_l_2err_26a15d6f), .clr2(l_be134dae_1_clr2), .clr3(l_be134dae_1_clr3),
    .clr4(l_be134dae_1_clr4), .en5(l_be134dae_1_en5));
  L_455c5dad l_455c5dad_1 (
    .L_0_eb6a1b8d(l_455c5dad_1_l_0_eb6a1b8d), .L_1_ef5de30d(l_455c5dad_1_l_1_ef5de30d),
    .L_2_d93bbbb2(l_455c5dad_1_l_2_d93bbbb2), .L_9904c55d(l_455c5dad_1_l_9904c55d),
    .L_ba8a574d(l_00584185_1_l_ba8a574d));
  L_b33f7de1 l_b33f7de1_1 (.L_fc3bd895(l_b33f7de1_1_l_fc3bd895), .\原始数据 (undriven_5));
  L_CRC_e0b66718 l_crc_e0b66718_1 (
    .EDU(undriven_6), .L_7d930fa3(undriven_8), .L_1err_a3df68ae(l_crc_e0b66718_1_l_1err_a3df68ae),
    .L_2err_26a15d6f(l_crc_e0b66718_1_l_2err_26a15d6f), .clr2(l_crc_e0b66718_1_clr2),
    .clr3(l_crc_e0b66718_1_clr3), .clr4(l_crc_e0b66718_1_clr4), .en5(l_crc_e0b66718_1_en5));
  L_CRC_4439dc43 l_crc_4439dc43_1 (.CRC_5864b47a(l_crc_4439dc43_1_crc_5864b47a), .L_d11c89cc(undriven_7));
  L_8e5bae90 l_8e5bae90_1 (
    .L_d332f524(l_8e5bae90_1_l_d332f524), .L_1425883c(l_8e5bae90_1_l_1425883c),
    .L_fc3bd895(l_b33f7de1_1_l_fc3bd895));
  L_CRC_dc188f0d l_crc_dc188f0d_1 (
    .L_0_eb6a1b8d(l_crc_dc188f0d_1_l_0_eb6a1b8d), .L_1_ef5de30d(l_crc_dc188f0d_1_l_1_ef5de30d),
    .L_2_d93bbbb2(l_crc_dc188f0d_1_l_2_d93bbbb2), .L_9904c55d(l_crc_dc188f0d_1_l_9904c55d),
    .CRC_1f12ebce(l_crc_4439dc43_1_crc_5864b47a));

  // Notes on the sheet:
  //   GB2312
  //   国标转区位码电路封装测试
  //   原始数据
  //   GB2312
  //   EDU
  //   汉字显示电路封装测试
  //   1位错
  //   海明编码
  //   海明编解码电路封装测试
  //   加噪
  //   1err
  //   2err
  //   en5
  //   海明流水传输电路封装测试
  //   最好通过引脚悬浮提示看看连接是否正确，如果有问题，请调整封装引脚位置直至连接正确
  //   原始数据
  //   2位错
  //   0位错
  //   clr2
  //   clr3
  //   clr4
  //   原始数据
  //   EDU
  //   请勿在子电路中增删改，甚至移动引脚位置，这些都可能导致子电路外观---封装发生改变，从而使得测试电路无法正确测试
  //   提交EduCoder平台检测之前，请先检查一下对应子电路的封装连接是否正确，主要查看引脚位置是否连接正确，有否错位未连接等情况
  //   原始数据
  //   加噪
  //   1err
  //   2err
  //   en5
  //   CRC流水传输电路封装测试
  //   偶校验编码
  //   偶校验编解码电路封装测试
  //   clr2
  //   clr3
  //   clr4
  //   CRC编码
  //   CRC编解码电路封装测试
  //   检错位
  //   原始数据
  //   2位错
  //   1位错
  //   0位错
  //   原始数据
endmodule
